// Logisim project cpu21-riscv.circ as structural Verilog: 18 circuits, main circuit ◇单周期RISC-V
module \单周期RISC_V  (
  input  IR1,
  input  IR2,
  input  IR3,
  output RegWrite,
  output MemWrite,
  output [31:0] PC,
  output [31:0] IR,
  output [31:0] RDin,
  output [31:0] MDin,
  output [31:0] LedData
);

  wire and_1_out, and_2_out, and_3_out, and_4_out, and_5_out, begu, BGEU, CLK, clock_2_out, comparator_1_eq,
       comparator_2_eq, comparator_2_lt, d_ff_1_q, ecall, equal, Go, halt, IR1_t, IR2_t, IR3_t, IRA, IRB,
       IRC, Jal, Jalr, key, nand_1_out, not_1_out, not_2_out, not_3_out, not_4_out, or_5_out, RST, SB, W1,
       W2, W3, xor_1_out, \单周期硬布线控制器_1_alu_src , \单周期硬布线控制器_1_beq , \单周期硬布线控制器_1_bne ,
       \单周期硬布线控制器_1_memtoreg , \单周期硬布线控制器_1_s_type ;
  wire [1:0] select;
  wire [3:0] \单周期硬布线控制器_1_alu_op ;
  wire [4:0] multiplexer_5_out, multiplexer_6_out;
  wire [11:0] shifter_1_out;
  wire [12:0] CNT_num;
  wire [15:0] \总周期数 ;
  wire [19:0] shifter_2_out;
  wire [31:0] bit_extender_1_out, bit_extender_2_out, imm, immB, immJal, multiplexer_1_out,
       multiplexer_2_out, multiplexer_3_out, multiplexer_4_out, multiplexer_8_out, PC_4, PCB, PCBGEU, PCJal,
       PCJalr, rs1, rs2, SB2, sb_t;
  wire [31:2] alu_1_result;

  Clock #(.highDuration(1), .lowDuration(1)) clock_1 ();  // open: out
  Button _1 (.out(IRA));
  Button _2 (.out(IRB));
  Button _3 (.out(IRC));
  Counter #(.width(16), .max('hffff), .ongoal("wrap"), .trigger("rising"), .behavior("old")) counter_1 (
    .Q(\总周期数 ), .clk(and_1_out));  // open: load, D, count, carry, clr, preset
  and and_1 (and_1_out, CLK, not_1_out);
  not not_1 (not_1_out, halt);
  Button \u_继续运行  (.out(Go));
  LED #(.active("true")) led_1 (.in(W1));
  LED #(.active("true")) led_2 (.in(W2));
  LED #(.active("true")) led_3 (.in(W3));
  Comparator #(.width(32), .mode("twosComplement")) comparator_1 (
    .a(rs1), .b(32'ha), .eq(comparator_1_eq));  // open: gt, lt
  // Probe on multiplexer_1_out
  Multiplexer #(.select(1), .width(32), .disabled("Z"), .enable("false")) multiplexer_1 (
    .in0(multiplexer_2_out), .in1(PCJalr), .out(multiplexer_1_out), .sel(Jalr));
  Multiplexer #(.select(1), .width(32), .disabled("Z"), .enable("false")) multiplexer_2 (
    .in0(multiplexer_3_out), .in1(PCJal), .out(multiplexer_2_out), .sel(Jal));
  and and_2 (and_2_out, begu, BGEU);
  Multiplexer #(.select(1), .width(32), .disabled("Z"), .enable("false")) multiplexer_3 (
    .in0(multiplexer_4_out), .in1(PCBGEU), .out(multiplexer_3_out), .sel(and_2_out));
  Multiplexer #(.select(1), .width(32), .disabled("Z"), .enable("false")) multiplexer_4 (
    .in0(PC_4), .in1(PCB), .out(multiplexer_4_out), .sel(key));
  Hex_Digit_Display hex_digit_display_1 (.value(LedData[31:28]));  // open: dp
  and and_3 (and_3_out, ecall, comparator_1_eq);
  Register #(.width(32), .trigger("rising"), .Select("low")) u_PC (
    .D(multiplexer_1_out), .en(not_2_out), .Q(PC), .clk(CLK), .clr(RST));
  not not_2 (not_2_out, halt);
  Hex_Digit_Display hex_digit_display_2 (.value(LedData[27:24]));  // open: dp
  Hex_Digit_Display hex_digit_display_3 (.value(LedData[23:20]));  // open: dp
  xor xor_1 (xor_1_out, and_3_out, Go);
  // Probe on PC
  Hex_Digit_Display hex_digit_display_4 (.value(LedData[19:16]));  // open: dp
  Hex_Digit_Display hex_digit_display_5 (.value(LedData[15:12]));  // open: dp
  Register #(.width(1), .trigger("falling"), .Select("low")) PC_2 (
    .D(xor_1_out), .en(xor_1_out), .Q(halt), .clk(CLK), .clr(Go));
  Counter #(.width(32), .max('hffffffff), .ongoal("wrap"), .trigger("rising"), .behavior("old")) counter_2 (
    .load(ecall), .D(rs2), .count(1'b0), .Q(LedData), .clk(CLK));  // open: carry, clr, preset
  // RiscV_Probe riscv_probe_1: pin names not known; wires that end beside it: IR
  // Probe on IR
  Hex_Digit_Display hex_digit_display_6 (.value(LedData[7:4]));  // open: dp
  Hex_Digit_Display hex_digit_display_7 (.value(LedData[11:8]));  // open: dp
  // Probe on \总周期数 
  // Probe on \总周期数 
  ROM #(.addrWidth(10), .dataWidth(32), .Select("high")) rom_1 (.addr(PC[11:2]), .data(IR));
  Hex_Digit_Display hex_digit_display_8 (.value(LedData[3:0]));  // open: dp
  \单周期硬布线控制器  \u_单周期硬布线控制器_1  (
    .Funct({IR[30], IR[25], IR[14:12]}), .OP(IR[6:2]), .ALU_OP(\单周期硬布线控制器_1_alu_op ),
    .MemToReg(\单周期硬布线控制器_1_memtoreg ), .MemWrite(MemWrite), .ALU_SRC(\单周期硬布线控制器_1_alu_src ),
    .RegWrite(RegWrite), .ecall(ecall), .S_type(\单周期硬布线控制器_1_s_type ), .Jalr(Jalr), .Beq(\单周期硬布线控制器_1_beq ),
    .JAL(Jal), .Bne(\单周期硬布线控制器_1_bne ), .SB(SB), .BGEU(BGEU));  // open: CSRRSI, CSRRCI
  Multiplexer #(.select(1), .width(5), .disabled("Z"), .enable("false")) multiplexer_5 (
    .in0(IR[19:15]), .in1(5'b10001), .out(multiplexer_5_out), .sel(ecall));
  Multiplexer #(.select(1), .width(5), .disabled("Z"), .enable("false")) multiplexer_6 (
    .in0(IR[24:20]), .in1(5'b01010), .out(multiplexer_6_out), .sel(ecall));
  assign bit_extender_1_out = {{20{IR[31]}}, IR[31:20]};  // Bit_Extender bit_extender_1
  assign bit_extender_2_out = {{20{IR[31]}}, {IR[31:25], IR[11:7]}};  // Bit_Extender bit_extender_2
  or or_1 (IR1_t, IR1, IRA);
  Multiplexer #(.select(1), .width(32), .disabled("Z"), .enable("false")) multiplexer_7 (
    .in0(bit_extender_1_out), .in1(bit_extender_2_out), .out(imm), .sel(\单周期硬布线控制器_1_s_type ));
  Shifter #(.width(12), .shift("ll")) shifter_1 (
    .in({IR[31], IR[7], IR[30:25], IR[11:8]}), .\dist (4'b0001), .out(shifter_1_out));
  Shifter #(.width(20), .shift("ll")) shifter_2 (
    .in({IR[31], IR[19:12], IR[20], IR[30:21]}), .\dist (5'b00001), .out(shifter_2_out));
  assign immJal = {{12{shifter_2_out[19]}}, shifter_2_out};  // Bit_Extender bit_extender_3
  or or_2 (IR2_t, IR2, IRB);
  assign immB = {{20{shifter_1_out[11]}}, shifter_1_out};  // Bit_Extender bit_extender_4
  not not_3 (not_3_out, equal);
  Regifile regifile_1 (
    .Din(RDin), .Clk(CLK), .R1(rs1), .R2(rs2), .WE(RegWrite), .W_num(IR[11:7]), .R1_num(multiplexer_5_out),
    .R2_num(multiplexer_6_out));
  or or_3 (IR3_t, IR3, IRC);
  and and_4 (and_4_out, equal, \单周期硬布线控制器_1_beq );
  and and_5 (and_5_out, not_3_out, \单周期硬布线控制器_1_bne );
  Multiplexer #(.select(1), .width(32), .disabled("Z"), .enable("false")) multiplexer_8 (
    .in0(rs2), .in1(imm), .out(multiplexer_8_out), .sel(\单周期硬布线控制器_1_alu_src ));
  Adder #(.width(32)) adder_1 (.a(PC), .b(32'h4), .out(PC_4));  // open: cin, cout
  Adder #(.width(32)) adder_2 (.a(PC), .b(immB), .out(PCB));  // open: cin, cout
  Adder #(.width(32)) adder_3 (.a(PC), .b(immJal), .out(PCJal));  // open: cin, cout
  Adder #(.width(32)) adder_4 (.a(PC), .b(immB), .out(PCBGEU));  // open: cin, cout
  or or_4 (key, and_4_out, and_5_out);
  ALU alu_1 (
    .X(rs1), .Y(multiplexer_8_out), .AluOP(\单周期硬布线控制器_1_alu_op ), .Equal(equal),
    .Result({alu_1_result, select}), .out_4(begu));  // open: Result_2, out_6
  Multiplexer #(.select(1), .width(32), .disabled("Z"), .enable("false")) multiplexer_9 (
    .in0(rs2), .in1(sb_t), .out(MDin), .sel(SB));
  not not_4 (not_4_out, halt);
  RAM #(.addrWidth(10), .dataWidth(32), .bus("separate"), .Select("high")) ram_1 (
    .addr(alu_1_result[11:2]), .din(MDin), .data(SB2), .str(MemWrite), .sel(not_4_out), .clk(CLK));  // open: ld, clr
  or or_5 (or_5_out, Jal, Jalr);
  Multiplexer #(.select(1), .width(32), .disabled("Z"), .enable("false")) multiplexer_10 (
    .in0(PCJalr), .in1(PC_4), .out(RDin), .sel(or_5_out));
  Multiplexer #(.select(1), .width(32), .disabled("Z"), .enable("false")) multiplexer_11 (
    .in0({alu_1_result, select}), .in1(SB2), .out(PCJalr), .sel(\单周期硬布线控制器_1_memtoreg ));
  // Probe on PCJalr
  Multiplexer #(.select(2), .width(32), .disabled("Z"), .enable("false")) multiplexer_12 (
    .in0({SB2[31:8], rs2[7:0]}), .in1({SB2[31:16], rs2[7:0], SB2[7:0]}),
    .in2({SB2[31:24], rs2[7:0], SB2[15:0]}), .in3({rs2[7:0], SB2[23:0]}), .out(sb_t), .sel(select));
  D_Flip_Flop #(.trigger("high"), .Pre_Clr_Positions("LEGACY"), .NegatePresetClear("false"), .enable("true"), .NewFFLayout("false")) d_ff_1 (.Q(d_ff_1_q));  // open: clk, D, Qn, preset, en, reset
  // Probe on 13'hc
  Comparator #(.width(13), .mode("twosComplement")) comparator_2 (
    .a(CNT_num), .b(13'hc), .eq(comparator_2_eq), .lt(comparator_2_lt));  // open: gt
  Clock #(.highDuration(1), .lowDuration(1)) clock_2 (.out(clock_2_out));
  Counter #(.width(13), .max('h1fff), .ongoal("stay"), .trigger("rising"), .behavior("old")) counter_3 (
    .count(comparator_2_lt), .Q(CNT_num), .clk(clock_2_out));  // open: load, D, carry, clr, preset
  nand nand_1 (nand_1_out, d_ff_1_q, comparator_2_eq);
  assign CLK = nand_1_out ? clock_2_out : 1'bz;  // Controlled_Buffer controlled_buffer_1
  Pull_Resistor #(.pull(1)) pull_resistor_1 (.node(CLK));

  // Other names for the same wires on the sheet: SB1[7:0] = rs2[7:0]

  // Notes on the sheet:
  //   中断源
  //   中断等待指示
  //   总复位信号应将除ROM以外所有存储组件全部清零
  //   数码管输出
  //   指令存储器
  //   指令字
  //   contents of rom_1 (hex, n*v repeats v):
  //   100493 100006f 100493 200913 300993 100006f 100493 200913 300993 100006f 100493 200913 300993
  //   100006f 100493 200913 300993 29c000ef 100413 100493 1f49493 900533 2200893 73 24d493 48463 fedff06f
  //   900533 2200893 73 100493 249493 900533 2200893 73 48463 fedff06f 100493 1f49493 900533 2200893 73
  //   4034d493 900533 2200893 73 4044d493 900533 2200893 73 4044d493 900533 2200893 73 4044d493 900533
  //   2200893 73 4044d493 900533 2200893 73 4044d493 900533 2200893 73 4044d493 900533 2200893 73 4044d493
  //   900533 2200893 73 100413 1f41993 41f9d993 433 c00913 300b13 140413 f47413 800293 100313 499993
  //   89e9b3 1300533 2200893 73 406282b3 fe0294e3 140413 f00f93 1f47433 1c41413 800293 100313 49d993
  //   89e9b3 1300533 2200893 73 406282b3 fe0294e3 1c45413 406b0b33 b0463 f95ff06f 2b3 fff2c293 829293
  //   ff2e293 500533 2200893 73 fff00413 493 84a023 140413 448493 84a023 140413 448493 84a023 140413
  //   448493 84a023 140413 448493 84a023 140413 448493 84a023 140413 448493 84a023 140413 448493 84a023
  //   140413 448493 84a023 140413 448493 84a023 140413 448493 84a023 140413 448493 84a023 140413 448493
  //   84a023 140413 448493 84a023 140413 448493 84a023 140413 448493 84a023 140413 448493 140413 433
  //   3c00493 42983 4aa03 149a2b3 28663 134a023 1442023 ffc48493 fe9412e3 800533 2200893 73 440413 3c00493
  //   fc9416e3 a00893 73 413 140413 800533 2200893 73 240413 800533 2200893 73 340413 800533 2200893 73
  //   440413 800533 2200893 73 540413 800533 2200893 73 640413 800533 2200893 73 740413 800533 2200893 73
  //   840413 800533 2200893 2200893 73 8067
  //   数码管输出应该用寄存器锁存，否则显示数据只能一闪而过
  //   Jal
  //   Jalr
  //   SB
  //   BGEU
  //   I型指令
  //   s型指令
  //   B型指令
  //   Jal
  //   Beq
  //   Bne
  //   MemToReg
  //   MemWrite
  //   AluOP
  //   AluSrcB
  //   RegWrite
  //   S_type
  //   ecall
  //   为方便自动评测，需要输出PC，IR，寄存器堆写如数据RDin
  //   数据存储器
  //   RAM写使能MemWrite、RAM写入数据MDin等信号
  //   控制位
  //   暂停节拍，不能为0
  //   戳工具置1进入计数暂停模式，ctrl+k时钟自动运行到对应节拍暂停
  //   ctrl+k关闭时钟连续运行，将控制位置零，进入单步调试模式调试
  //   用这个时钟源需要去掉电路中的其他时钟源
  //   可计数暂停的时钟源
endmodule

// 单周期硬布线控制器
module \单周期硬布线控制器  (
  input  [4:0] OP,
  input  [4:0] Funct,
  output [3:0] ALU_OP,
  output MemToReg,
  output MemWrite,
  output ALU_SRC,
  output RegWrite,
  output SB,
  output BGEU,
  output ecall,
  output S_type,
  output Beq,
  output Bne,
  output Jalr,
  output JAL,
  output CSRRSI,
  output CSRRCI
);

  \运算控制器自动生成  \u_运算控制器自动生成_1  (
    .OP2(OP[0]), .OP3(OP[1]), .OP4(OP[2]), .OP5(OP[3]), .OP6(OP[4]), .F12(Funct[0]), .F13(Funct[1]),
    .F14(Funct[2]), .F25(Funct[3]), .F30(Funct[4]), .S0(ALU_OP[0]), .S1(ALU_OP[1]), .S2(ALU_OP[2]),
    .S3(ALU_OP[3]));
  \控制信号自动生成  \u_控制信号自动生成_1  (
    .OP2(OP[0]), .OP3(OP[1]), .MemToReg(MemToReg), .OP4(OP[2]), .OP5(OP[3]), .OP6(OP[4]), .F12(Funct[0]),
    .F13(Funct[1]), .F14(Funct[2]), .MemWrite(MemWrite), .F25(Funct[3]), .F30(Funct[4]), .ALU_SRC(ALU_SRC),
    .RegWrite(RegWrite), .SB(SB), .CSRRSI(CSRRSI), .BGEU(BGEU), .CSRRCI(CSRRCI), .ecall(ecall),
    .S_Type(S_type), .BEQ(Beq), .BNE(Bne), .JALR(Jalr), .JAL(JAL));

  // Other names for the same wires on the sheet: OP_CODE[4:0] = OP

  // Notes on the sheet:
  //   运算器控制器，根据指令生成运算器功能选择信号
endmodule

// 运算器控制器
module \运算控制器自动生成  (
  input  OP2,
  input  OP3,
  input  OP4,
  input  OP5,
  input  OP6,
  input  F12,
  input  F13,
  input  F14,
  input  F25,
  input  F30,
  output S0,
  output S1,
  output S2,
  output S3
);

  wire and_1_out, and_2_out, and_3_out, and_4_out, and_5_out, and_6_out, and_7_out, and_8_out, and_9_out,
       and_10_out, and_11_out, and_12_out, and_13_out, and_14_out, and_15_out, and_16_out, and_17_out,
       and_18_out, and_19_out, and_20_out, and_21_out, and_22_out, and_23_out, and_24_out, and_25_out,
       and_26_out, and_27_out, and_28_out, and_29_out, and_30_out, and_31_out, and_32_out, and_33_out,
       and_34_out, and_35_out, not_1_out, not_2_out, not_3_out, not_4_out, not_5_out, not_6_out, not_7_out,
       not_8_out, not_9_out, not_10_out, not_11_out, not_12_out, not_13_out, not_14_out, not_15_out,
       not_16_out, not_17_out, not_18_out, not_19_out, not_20_out, not_21_out, not_22_out, not_23_out,
       not_24_out, not_25_out, not_26_out, not_27_out, not_28_out, not_29_out, not_30_out, not_31_out,
       not_32_out, not_33_out, not_34_out, not_35_out, not_36_out, not_37_out, not_38_out, not_39_out,
       not_40_out, not_41_out, not_42_out, not_43_out, not_44_out, not_45_out, not_46_out, not_47_out,
       not_48_out, not_49_out, not_50_out, not_51_out, not_52_out, not_53_out, not_54_out, not_55_out,
       not_56_out, not_57_out, not_58_out, not_59_out, not_60_out, not_61_out, not_62_out, not_63_out,
       not_64_out, not_65_out, not_66_out, not_67_out, not_68_out, not_69_out, not_70_out, not_71_out,
       not_72_out, not_73_out, not_74_out, not_75_out, not_76_out, not_77_out, not_78_out, not_79_out,
       not_80_out, not_81_out, not_82_out, not_83_out, not_84_out, not_85_out, not_86_out, not_87_out,
       not_88_out, not_89_out, not_90_out, not_91_out, not_92_out, not_93_out, not_94_out, not_95_out,
       not_96_out, not_97_out, not_98_out, not_99_out, not_100_out, not_101_out, not_102_out, not_103_out,
       not_104_out, not_105_out, not_106_out, not_107_out, not_108_out, not_109_out, not_110_out,
       not_111_out, not_112_out, not_113_out, not_114_out, not_115_out, not_116_out, not_117_out,
       not_118_out, not_119_out, not_120_out, not_121_out, not_122_out, not_123_out, not_124_out,
       not_125_out, not_126_out, not_127_out, not_128_out, not_129_out, not_130_out, not_131_out,
       not_132_out, not_133_out, not_134_out, not_135_out, not_136_out, not_137_out, not_138_out,
       not_139_out, not_140_out, not_141_out, not_142_out, not_143_out, not_144_out, not_145_out,
       not_146_out, not_147_out, not_148_out, not_149_out, not_150_out, not_151_out, not_152_out,
       not_153_out, not_154_out, not_155_out, not_156_out, not_157_out, not_158_out, not_159_out,
       not_160_out, not_161_out, not_162_out, not_163_out, not_164_out, not_165_out, not_166_out,
       not_167_out, not_168_out, not_169_out, not_170_out, not_171_out, not_172_out, not_173_out,
       not_174_out, not_175_out, not_176_out, not_177_out, not_178_out, not_179_out, not_180_out,
       not_181_out, not_182_out, not_183_out, not_184_out, not_185_out, not_186_out, not_187_out,
       not_188_out, not_189_out, not_190_out, not_191_out, not_192_out, not_193_out, not_194_out,
       not_195_out, not_196_out, not_197_out, not_198_out, not_199_out, not_200_out, not_201_out,
       not_202_out, not_203_out, not_204_out, not_205_out, not_206_out, not_207_out, not_208_out,
       not_209_out, not_210_out, not_211_out, not_212_out, not_213_out, not_214_out, not_215_out,
       not_216_out, not_217_out;

  not not_1 (not_1_out, F30);
  not not_2 (not_2_out, F25);
  not not_3 (not_3_out, F14);
  not not_4 (not_4_out, F13);
  not not_5 (not_5_out, F12);
  not not_6 (not_6_out, OP6);
  not not_7 (not_7_out, OP3);
  not not_8 (not_8_out, OP2);
  not not_9 (not_9_out, F30);
  not not_10 (not_10_out, F25);
  not not_11 (not_11_out, OP6);
  not not_12 (not_12_out, OP3);
  not not_13 (not_13_out, OP2);
  not not_14 (not_14_out, F30);
  not not_15 (not_15_out, F25);
  not not_16 (not_16_out, F14);
  not not_17 (not_17_out, F12);
  not not_18 (not_18_out, OP6);
  not not_19 (not_19_out, OP3);
  not not_20 (not_20_out, OP2);
  not not_21 (not_21_out, F14);
  not not_22 (not_22_out, F13);
  not not_23 (not_23_out, F12);
  not not_24 (not_24_out, OP6);
  not not_25 (not_25_out, OP5);
  not not_26 (not_26_out, OP3);
  not not_27 (not_27_out, OP2);
  not not_28 (not_28_out, OP6);
  not not_29 (not_29_out, OP5);
  not not_30 (not_30_out, OP3);
  not not_31 (not_31_out, OP2);
  not not_32 (not_32_out, F13);
  not not_33 (not_33_out, F12);
  not not_34 (not_34_out, OP6);
  not not_35 (not_35_out, OP5);
  not not_36 (not_36_out, OP3);
  not not_37 (not_37_out, OP2);
  not not_38 (not_38_out, F14);
  not not_39 (not_39_out, F12);
  not not_40 (not_40_out, OP6);
  not not_41 (not_41_out, OP5);
  not not_42 (not_42_out, OP3);
  not not_43 (not_43_out, OP2);
  not not_44 (not_44_out, F25);
  not not_45 (not_45_out, F13);
  not not_46 (not_46_out, OP6);
  not not_47 (not_47_out, OP5);
  not not_48 (not_48_out, OP3);
  not not_49 (not_49_out, OP2);
  not not_50 (not_50_out, F14);
  not not_51 (not_51_out, F12);
  not not_52 (not_52_out, OP6);
  not not_53 (not_53_out, OP5);
  not not_54 (not_54_out, OP4);
  not not_55 (not_55_out, OP3);
  not not_56 (not_56_out, OP2);
  not not_57 (not_57_out, F14);
  not not_58 (not_58_out, F12);
  not not_59 (not_59_out, OP6);
  not not_60 (not_60_out, OP4);
  not not_61 (not_61_out, OP3);
  not not_62 (not_62_out, OP2);
  not not_63 (not_63_out, F25);
  not not_64 (not_64_out, F13);
  not not_65 (not_65_out, OP6);
  not not_66 (not_66_out, OP3);
  not not_67 (not_67_out, OP2);
  not not_68 (not_68_out, F30);
  not not_69 (not_69_out, F25);
  not not_70 (not_70_out, F13);
  not not_71 (not_71_out, F12);
  not not_72 (not_72_out, OP6);
  not not_73 (not_73_out, OP3);
  not not_74 (not_74_out, OP2);
  not not_75 (not_75_out, F14);
  not not_76 (not_76_out, F13);
  not not_77 (not_77_out, F12);
  not not_78 (not_78_out, OP6);
  not not_79 (not_79_out, OP4);
  not not_80 (not_80_out, OP3);
  not not_81 (not_81_out, OP2);
  not not_82 (not_82_out, F25);
  not not_83 (not_83_out, F14);
  not not_84 (not_84_out, F13);
  not not_85 (not_85_out, F12);
  not not_86 (not_86_out, OP6);
  not not_87 (not_87_out, OP3);
  not not_88 (not_88_out, OP2);
  not not_89 (not_89_out, F30);
  not not_90 (not_90_out, F25);
  not not_91 (not_91_out, OP6);
  not not_92 (not_92_out, OP3);
  not not_93 (not_93_out, OP2);
  not not_94 (not_94_out, F30);
  not not_95 (not_95_out, F25);
  not not_96 (not_96_out, F14);
  not not_97 (not_97_out, F12);
  not not_98 (not_98_out, OP6);
  not not_99 (not_99_out, OP3);
  not not_100 (not_100_out, OP2);
  not not_101 (not_101_out, OP6);
  not not_102 (not_102_out, OP5);
  not not_103 (not_103_out, OP3);
  not not_104 (not_104_out, OP2);
  not not_105 (not_105_out, F14);
  not not_106 (not_106_out, F12);
  not not_107 (not_107_out, OP6);
  not not_108 (not_108_out, OP5);
  not not_109 (not_109_out, OP3);
  not not_110 (not_110_out, OP2);
  not not_111 (not_111_out, F30);
  not not_112 (not_112_out, F25);
  not not_113 (not_113_out, F13);
  not not_114 (not_114_out, OP6);
  not not_115 (not_115_out, OP5);
  not not_116 (not_116_out, OP3);
  not not_117 (not_117_out, OP2);
  not not_118 (not_118_out, F30);
  not not_119 (not_119_out, F25);
  not not_120 (not_120_out, F14);
  not not_121 (not_121_out, F13);
  not not_122 (not_122_out, F12);
  not not_123 (not_123_out, OP6);
  not not_124 (not_124_out, OP3);
  not not_125 (not_125_out, OP2);
  not not_126 (not_126_out, F25);
  not not_127 (not_127_out, F14);
  not not_128 (not_128_out, F13);
  not not_129 (not_129_out, F12);
  not not_130 (not_130_out, OP6);
  not not_131 (not_131_out, OP3);
  not not_132 (not_132_out, OP2);
  not not_133 (not_133_out, F30);
  not not_134 (not_134_out, F25);
  not not_135 (not_135_out, OP6);
  not not_136 (not_136_out, OP3);
  not not_137 (not_137_out, OP2);
  not not_138 (not_138_out, F30);
  not not_139 (not_139_out, F25);
  not not_140 (not_140_out, F14);
  not not_141 (not_141_out, OP6);
  not not_142 (not_142_out, OP3);
  not not_143 (not_143_out, OP2);
  not not_144 (not_144_out, F14);
  not not_145 (not_145_out, F13);
  not not_146 (not_146_out, F12);
  not not_147 (not_147_out, OP6);
  not not_148 (not_148_out, OP5);
  not not_149 (not_149_out, OP3);
  not not_150 (not_150_out, OP2);
  not not_151 (not_151_out, OP6);
  not not_152 (not_152_out, OP5);
  not not_153 (not_153_out, OP3);
  not not_154 (not_154_out, OP2);
  not not_155 (not_155_out, F14);
  not not_156 (not_156_out, F12);
  not not_157 (not_157_out, OP6);
  not not_158 (not_158_out, OP5);
  not not_159 (not_159_out, OP4);
  not not_160 (not_160_out, OP3);
  not not_161 (not_161_out, OP2);
  not not_162 (not_162_out, F14);
  not not_163 (not_163_out, F12);
  not not_164 (not_164_out, OP6);
  not not_165 (not_165_out, OP4);
  not not_166 (not_166_out, OP3);
  not not_167 (not_167_out, OP2);
  not not_168 (not_168_out, F14);
  not not_169 (not_169_out, F13);
  not not_170 (not_170_out, F12);
  not not_171 (not_171_out, OP6);
  not not_172 (not_172_out, OP4);
  not not_173 (not_173_out, OP3);
  not not_174 (not_174_out, OP2);
  not not_175 (not_175_out, F30);
  not not_176 (not_176_out, F25);
  not not_177 (not_177_out, F12);
  not not_178 (not_178_out, OP6);
  not not_179 (not_179_out, OP3);
  not not_180 (not_180_out, OP2);
  not not_181 (not_181_out, F30);
  not not_182 (not_182_out, F25);
  not not_183 (not_183_out, F14);
  not not_184 (not_184_out, F12);
  not not_185 (not_185_out, OP6);
  not not_186 (not_186_out, OP3);
  not not_187 (not_187_out, OP2);
  not not_188 (not_188_out, F30);
  not not_189 (not_189_out, F25);
  not not_190 (not_190_out, F14);
  not not_191 (not_191_out, OP6);
  not not_192 (not_192_out, OP3);
  not not_193 (not_193_out, OP2);
  not not_194 (not_194_out, F12);
  not not_195 (not_195_out, OP6);
  not not_196 (not_196_out, OP5);
  not not_197 (not_197_out, OP3);
  not not_198 (not_198_out, OP2);
  not not_199 (not_199_out, F13);
  not not_200 (not_200_out, F12);
  not not_201 (not_201_out, OP6);
  not not_202 (not_202_out, OP5);
  not not_203 (not_203_out, OP3);
  not not_204 (not_204_out, OP2);
  not not_205 (not_205_out, F14);
  not not_206 (not_206_out, F12);
  not not_207 (not_207_out, OP6);
  not not_208 (not_208_out, OP5);
  not not_209 (not_209_out, OP3);
  not not_210 (not_210_out, OP2);
  not not_211 (not_211_out, F30);
  not not_212 (not_212_out, F25);
  not not_213 (not_213_out, F13);
  not not_214 (not_214_out, F12);
  not not_215 (not_215_out, OP6);
  not not_216 (not_216_out, OP3);
  not not_217 (not_217_out, OP2);
  and and_1 (and_1_out, not_1_out, not_2_out, not_3_out, not_4_out, not_5_out, not_6_out, OP5, OP4, not_7_out, not_8_out);
  and and_2 (and_2_out, not_9_out, not_10_out, F14, F13, F12, not_11_out, OP5, OP4, not_12_out, not_13_out);
  and and_3 (and_3_out, not_14_out, not_15_out, not_16_out, F13, not_17_out, not_18_out, OP5, OP4, not_19_out, not_20_out);
  and and_4 (and_4_out, not_21_out, not_22_out, not_23_out, not_24_out, not_25_out, OP4, not_26_out, not_27_out);
  and and_5 (and_5_out, F14, F13, F12, not_28_out, not_29_out, OP4, not_30_out, not_31_out);
  and and_6 (and_6_out, F14, not_32_out, not_33_out, not_34_out, not_35_out, OP4, not_36_out, not_37_out);
  and and_7 (and_7_out, not_38_out, F13, not_39_out, not_40_out, not_41_out, OP4, not_42_out, not_43_out);
  and and_8 (and_8_out, F30, not_44_out, F14, not_45_out, F12, not_46_out, not_47_out, OP4, not_48_out, not_49_out);
  and and_9 (and_9_out, not_50_out, F13, not_51_out, not_52_out, not_53_out, not_54_out, not_55_out, not_56_out);
  and and_10 (and_10_out, not_57_out, F13, not_58_out, not_59_out, OP5, not_60_out, not_61_out, not_62_out);
  and and_11 (and_11_out, F30, not_63_out, F14, not_64_out, F12, not_65_out, OP5, OP4, not_66_out, not_67_out);
  and and_12 (and_12_out, not_68_out, not_69_out, F14, not_70_out, not_71_out, not_72_out, OP5, OP4, not_73_out, not_74_out);
  and and_13 (and_13_out, not_75_out, not_76_out, not_77_out, not_78_out, OP5, not_79_out, not_80_out, not_81_out);
  and and_14 (and_14_out, F30, not_82_out, not_83_out, not_84_out, not_85_out, not_86_out, OP5, OP4, not_87_out, not_88_out);
  and and_15 (and_15_out, not_89_out, not_90_out, F14, F13, F12, not_91_out, OP5, OP4, not_92_out, not_93_out);
  and and_16 (and_16_out, not_94_out, not_95_out, not_96_out, F13, not_97_out, not_98_out, OP5, OP4, not_99_out, not_100_out);
  and and_17 (and_17_out, F14, F13, F12, not_101_out, not_102_out, OP4, not_103_out, not_104_out);
  and and_18 (and_18_out, not_105_out, F13, not_106_out, not_107_out, not_108_out, OP4, not_109_out, not_110_out);
  and and_19 (and_19_out, not_111_out, not_112_out, F14, not_113_out, F12, not_114_out, not_115_out, OP4, not_116_out, not_117_out);
  and and_20 (and_20_out, not_118_out, not_119_out, not_120_out, not_121_out, not_122_out, not_123_out, OP5, OP4, not_124_out, not_125_out);
  and and_21 (and_21_out, F30, not_126_out, not_127_out, not_128_out, not_129_out, not_130_out, OP5, OP4, not_131_out, not_132_out);
  and and_22 (and_22_out, not_133_out, not_134_out, F14, F13, F12, not_135_out, OP5, OP4, not_136_out, not_137_out);
  and and_23 (and_23_out, not_138_out, not_139_out, not_140_out, F13, F12, not_141_out, OP5, OP4, not_142_out, not_143_out);
  and and_24 (and_24_out, not_144_out, not_145_out, not_146_out, not_147_out, not_148_out, OP4, not_149_out, not_150_out);
  and and_25 (and_25_out, F14, F13, F12, not_151_out, not_152_out, OP4, not_153_out, not_154_out);
  and and_26 (and_26_out, not_155_out, F13, not_156_out, not_157_out, not_158_out, not_159_out, not_160_out, not_161_out);
  and and_27 (and_27_out, not_162_out, F13, not_163_out, not_164_out, OP5, not_165_out, not_166_out, not_167_out);
  and and_28 (and_28_out, not_168_out, not_169_out, not_170_out, not_171_out, OP5, not_172_out, not_173_out, not_174_out);
  and and_29 (and_29_out, not_175_out, not_176_out, F14, F13, not_177_out, not_178_out, OP5, OP4, not_179_out, not_180_out);
  and and_30 (and_30_out, not_181_out, not_182_out, not_183_out, F13, not_184_out, not_185_out, OP5, OP4, not_186_out, not_187_out);
  and and_31 (and_31_out, not_188_out, not_189_out, not_190_out, F13, F12, not_191_out, OP5, OP4, not_192_out, not_193_out);
  and and_32 (and_32_out, F14, F13, not_194_out, not_195_out, not_196_out, OP4, not_197_out, not_198_out);
  and and_33 (and_33_out, F14, not_199_out, not_200_out, not_201_out, not_202_out, OP4, not_203_out, not_204_out);
  and and_34 (and_34_out, not_205_out, F13, not_206_out, not_207_out, not_208_out, OP4, not_209_out, not_210_out);
  and and_35 (and_35_out, not_211_out, not_212_out, F14, not_213_out, not_214_out, not_215_out, OP5, OP4, not_216_out, not_217_out);
  or or_1 (S0, and_1_out, and_2_out, and_3_out, and_4_out, and_5_out, and_6_out, and_7_out, and_8_out, and_9_out, and_10_out, and_11_out, and_12_out, and_13_out);
  or or_2 (S1, and_14_out, and_15_out, and_16_out, and_17_out, and_18_out, and_19_out);
  or or_3 (S2, and_20_out, and_21_out, and_22_out, and_23_out, and_24_out, and_25_out, and_26_out, and_27_out, and_28_out);
  or or_4 (S3, and_29_out, and_30_out, and_31_out, and_32_out, and_33_out, and_34_out, and_35_out);
endmodule

// 控制信号生成
module \控制信号自动生成  (
  input  OP2,
  input  OP3,
  input  OP4,
  input  OP5,
  input  OP6,
  input  F12,
  input  F13,
  input  F14,
  input  F25,
  input  F30,
  output MemToReg,
  output MemWrite,
  output ALU_SRC,
  output RegWrite,
  output SB,
  output CSRRSI,
  output BGEU,
  output CSRRCI,
  output ecall,
  output S_Type,
  output BEQ,
  output BNE,
  output JALR,
  output JAL
);

  wire and_2_out, and_3_out, and_4_out, and_5_out, and_6_out, and_7_out, and_8_out, and_9_out, and_10_out,
       and_11_out, and_12_out, and_13_out, and_14_out, and_15_out, and_16_out, and_17_out, and_18_out,
       and_19_out, and_20_out, and_21_out, and_22_out, and_23_out, and_24_out, and_25_out, and_26_out,
       and_27_out, and_28_out, and_29_out, and_30_out, and_31_out, and_32_out, and_33_out, and_34_out,
       and_40_out, and_41_out, not_1_out, not_2_out, not_3_out, not_4_out, not_5_out, not_6_out, not_7_out,
       not_8_out, not_9_out, not_10_out, not_11_out, not_12_out, not_13_out, not_14_out, not_15_out,
       not_16_out, not_17_out, not_18_out, not_19_out, not_20_out, not_21_out, not_22_out, not_23_out,
       not_24_out, not_25_out, not_26_out, not_27_out, not_28_out, not_29_out, not_30_out, not_31_out,
       not_32_out, not_33_out, not_34_out, not_35_out, not_36_out, not_37_out, not_38_out, not_39_out,
       not_40_out, not_41_out, not_42_out, not_43_out, not_44_out, not_45_out, not_46_out, not_47_out,
       not_48_out, not_49_out, not_50_out, not_51_out, not_52_out, not_53_out, not_54_out, not_55_out,
       not_56_out, not_57_out, not_58_out, not_59_out, not_60_out, not_61_out, not_62_out, not_63_out,
       not_64_out, not_65_out, not_66_out, not_67_out, not_68_out, not_69_out, not_70_out, not_71_out,
       not_72_out, not_73_out, not_74_out, not_75_out, not_76_out, not_77_out, not_78_out, not_79_out,
       not_80_out, not_81_out, not_82_out, not_83_out, not_84_out, not_85_out, not_86_out, not_87_out,
       not_88_out, not_89_out, not_90_out, not_91_out, not_92_out, not_93_out, not_94_out, not_95_out,
       not_96_out, not_97_out, not_98_out, not_99_out, not_100_out, not_101_out, not_102_out, not_103_out,
       not_104_out, not_105_out, not_106_out, not_107_out, not_108_out, not_109_out, not_110_out,
       not_111_out, not_112_out, not_113_out, not_114_out, not_115_out, not_116_out, not_117_out,
       not_118_out, not_119_out, not_120_out, not_121_out, not_122_out, not_123_out, not_124_out,
       not_125_out, not_126_out, not_127_out, not_128_out, not_129_out, not_130_out, not_131_out,
       not_132_out, not_133_out, not_134_out, not_135_out, not_136_out, not_137_out, not_138_out,
       not_139_out, not_140_out, not_141_out, not_142_out, not_143_out, not_144_out, not_145_out,
       not_146_out, not_147_out, not_148_out, not_149_out, not_150_out, not_151_out, not_152_out,
       not_153_out, not_154_out, not_155_out, not_156_out, not_157_out, not_158_out, not_159_out,
       not_160_out, not_161_out, not_162_out, not_163_out, not_164_out, not_165_out, not_166_out,
       not_167_out, not_168_out, not_169_out, not_170_out, not_171_out, not_172_out, not_173_out,
       not_174_out, not_175_out, not_176_out, not_177_out, not_178_out, not_179_out, not_180_out,
       not_181_out, not_182_out, not_183_out, not_184_out, not_185_out, not_186_out, not_187_out,
       not_188_out, not_189_out, not_190_out, not_191_out, not_192_out, not_193_out, not_194_out,
       not_195_out, not_196_out, not_197_out, not_198_out, not_199_out, not_200_out, not_201_out,
       not_202_out, not_203_out, not_204_out, not_205_out, not_206_out, not_207_out, not_208_out,
       not_209_out, not_210_out, not_211_out, not_212_out, not_213_out, not_214_out, not_215_out,
       not_216_out, not_217_out, not_218_out, not_219_out, not_220_out, not_221_out, not_222_out,
       not_223_out, not_224_out, not_225_out, not_226_out, not_227_out, not_228_out, not_229_out,
       not_230_out, not_231_out, not_232_out, not_233_out, not_234_out, not_235_out, not_236_out,
       not_237_out, not_238_out, not_239_out, not_240_out, not_241_out, not_242_out, not_243_out,
       not_244_out, not_245_out, not_246_out, not_247_out, not_248_out, not_249_out, not_250_out,
       not_251_out, not_252_out, not_253_out, not_254_out, not_255_out, not_256_out, not_257_out,
       not_258_out, not_259_out;

  not not_1 (not_1_out, F14);
  not not_2 (not_2_out, F12);
  not not_3 (not_3_out, OP6);
  not not_4 (not_4_out, OP5);
  not not_5 (not_5_out, OP4);
  not not_6 (not_6_out, OP3);
  not not_7 (not_7_out, OP2);
  not not_8 (not_8_out, F14);
  not not_9 (not_9_out, F12);
  not not_10 (not_10_out, OP6);
  not not_11 (not_11_out, OP4);
  not not_12 (not_12_out, OP3);
  not not_13 (not_13_out, OP2);
  not not_14 (not_14_out, F14);
  not not_15 (not_15_out, F13);
  not not_16 (not_16_out, F12);
  not not_17 (not_17_out, OP6);
  not not_18 (not_18_out, OP4);
  not not_19 (not_19_out, OP3);
  not not_20 (not_20_out, OP2);
  not not_21 (not_21_out, F14);
  not not_22 (not_22_out, F13);
  not not_23 (not_23_out, F12);
  not not_24 (not_24_out, OP6);
  not not_25 (not_25_out, OP5);
  not not_26 (not_26_out, OP3);
  not not_27 (not_27_out, OP2);
  not not_28 (not_28_out, OP6);
  not not_29 (not_29_out, OP5);
  not not_30 (not_30_out, OP3);
  not not_31 (not_31_out, OP2);
  not not_32 (not_32_out, F12);
  not not_33 (not_33_out, OP6);
  not not_34 (not_34_out, OP5);
  not not_35 (not_35_out, OP3);
  not not_36 (not_36_out, OP2);
  not not_37 (not_37_out, F13);
  not not_38 (not_38_out, F12);
  not not_39 (not_39_out, OP6);
  not not_40 (not_40_out, OP5);
  not not_41 (not_41_out, OP3);
  not not_42 (not_42_out, OP2);
  not not_43 (not_43_out, F14);
  not not_44 (not_44_out, F12);
  not not_45 (not_45_out, OP6);
  not not_46 (not_46_out, OP5);
  not not_47 (not_47_out, OP3);
  not not_48 (not_48_out, OP2);
  not not_49 (not_49_out, F30);
  not not_50 (not_50_out, F25);
  not not_51 (not_51_out, F14);
  not not_52 (not_52_out, F13);
  not not_53 (not_53_out, OP6);
  not not_54 (not_54_out, OP5);
  not not_55 (not_55_out, OP3);
  not not_56 (not_56_out, OP2);
  not not_57 (not_57_out, F30);
  not not_58 (not_58_out, F25);
  not not_59 (not_59_out, F13);
  not not_60 (not_60_out, OP6);
  not not_61 (not_61_out, OP5);
  not not_62 (not_62_out, OP3);
  not not_63 (not_63_out, OP2);
  not not_64 (not_64_out, F25);
  not not_65 (not_65_out, F13);
  not not_66 (not_66_out, OP6);
  not not_67 (not_67_out, OP5);
  not not_68 (not_68_out, OP3);
  not not_69 (not_69_out, OP2);
  not not_70 (not_70_out, F14);
  not not_71 (not_71_out, F12);
  not not_72 (not_72_out, OP6);
  not not_73 (not_73_out, OP5);
  not not_74 (not_74_out, OP4);
  not not_75 (not_75_out, OP3);
  not not_76 (not_76_out, OP2);
  not not_77 (not_77_out, F14);
  not not_78 (not_78_out, F12);
  not not_79 (not_79_out, OP6);
  not not_80 (not_80_out, OP4);
  not not_81 (not_81_out, OP3);
  not not_82 (not_82_out, OP2);
  not not_83 (not_83_out, F14);
  not not_84 (not_84_out, F13);
  not not_85 (not_85_out, F12);
  not not_86 (not_86_out, OP4);
  not not_87 (not_87_out, OP3);
  not not_88 (not_88_out, F14);
  not not_89 (not_89_out, F13);
  not not_90 (not_90_out, F12);
  not not_91 (not_91_out, OP6);
  not not_92 (not_92_out, OP4);
  not not_93 (not_93_out, OP3);
  not not_94 (not_94_out, OP2);
  not not_95 (not_95_out, F30);
  not not_96 (not_96_out, F25);
  not not_97 (not_97_out, F14);
  not not_98 (not_98_out, F13);
  not not_99 (not_99_out, F12);
  not not_100 (not_100_out, OP6);
  not not_101 (not_101_out, OP3);
  not not_102 (not_102_out, OP2);
  not not_103 (not_103_out, F25);
  not not_104 (not_104_out, F14);
  not not_105 (not_105_out, F13);
  not not_106 (not_106_out, F12);
  not not_107 (not_107_out, OP6);
  not not_108 (not_108_out, OP3);
  not not_109 (not_109_out, OP2);
  not not_110 (not_110_out, F30);
  not not_111 (not_111_out, F25);
  not not_112 (not_112_out, OP6);
  not not_113 (not_113_out, OP3);
  not not_114 (not_114_out, OP2);
  not not_115 (not_115_out, F30);
  not not_116 (not_116_out, F25);
  not not_117 (not_117_out, F12);
  not not_118 (not_118_out, OP6);
  not not_119 (not_119_out, OP3);
  not not_120 (not_120_out, OP2);
  not not_121 (not_121_out, F30);
  not not_122 (not_122_out, F25);
  not not_123 (not_123_out, F14);
  not not_124 (not_124_out, F12);
  not not_125 (not_125_out, OP6);
  not not_126 (not_126_out, OP3);
  not not_127 (not_127_out, OP2);
  not not_128 (not_128_out, F30);
  not not_129 (not_129_out, F25);
  not not_130 (not_130_out, F14);
  not not_131 (not_131_out, OP6);
  not not_132 (not_132_out, OP3);
  not not_133 (not_133_out, OP2);
  not not_134 (not_134_out, F14);
  not not_135 (not_135_out, F13);
  not not_136 (not_136_out, F12);
  not not_137 (not_137_out, OP6);
  not not_138 (not_138_out, OP5);
  not not_139 (not_139_out, OP3);
  not not_140 (not_140_out, OP2);
  not not_141 (not_141_out, OP6);
  not not_142 (not_142_out, OP5);
  not not_143 (not_143_out, OP3);
  not not_144 (not_144_out, OP2);
  not not_145 (not_145_out, F12);
  not not_146 (not_146_out, OP6);
  not not_147 (not_147_out, OP5);
  not not_148 (not_148_out, OP3);
  not not_149 (not_149_out, OP2);
  not not_150 (not_150_out, F13);
  not not_151 (not_151_out, F12);
  not not_152 (not_152_out, OP6);
  not not_153 (not_153_out, OP5);
  not not_154 (not_154_out, OP3);
  not not_155 (not_155_out, OP2);
  not not_156 (not_156_out, F14);
  not not_157 (not_157_out, F12);
  not not_158 (not_158_out, OP6);
  not not_159 (not_159_out, OP5);
  not not_160 (not_160_out, OP3);
  not not_161 (not_161_out, OP2);
  not not_162 (not_162_out, F30);
  not not_163 (not_163_out, F25);
  not not_164 (not_164_out, F14);
  not not_165 (not_165_out, F13);
  not not_166 (not_166_out, OP6);
  not not_167 (not_167_out, OP5);
  not not_168 (not_168_out, OP3);
  not not_169 (not_169_out, OP2);
  not not_170 (not_170_out, F30);
  not not_171 (not_171_out, F25);
  not not_172 (not_172_out, F13);
  not not_173 (not_173_out, OP6);
  not not_174 (not_174_out, OP5);
  not not_175 (not_175_out, OP3);
  not not_176 (not_176_out, OP2);
  not not_177 (not_177_out, F25);
  not not_178 (not_178_out, F13);
  not not_179 (not_179_out, OP6);
  not not_180 (not_180_out, OP5);
  not not_181 (not_181_out, OP3);
  not not_182 (not_182_out, OP2);
  not not_183 (not_183_out, F14);
  not not_184 (not_184_out, F12);
  not not_185 (not_185_out, OP6);
  not not_186 (not_186_out, OP5);
  not not_187 (not_187_out, OP4);
  not not_188 (not_188_out, OP3);
  not not_189 (not_189_out, OP2);
  not not_190 (not_190_out, OP4);
  not not_191 (not_191_out, F14);
  not not_192 (not_192_out, F13);
  not not_193 (not_193_out, F12);
  not not_194 (not_194_out, OP4);
  not not_195 (not_195_out, OP3);
  not not_196 (not_196_out, F25);
  not not_197 (not_197_out, F13);
  not not_198 (not_198_out, OP6);
  not not_199 (not_199_out, OP3);
  not not_200 (not_200_out, OP2);
  not not_201 (not_201_out, F30);
  not not_202 (not_202_out, F25);
  not not_203 (not_203_out, F13);
  not not_204 (not_204_out, F12);
  not not_205 (not_205_out, OP6);
  not not_206 (not_206_out, OP3);
  not not_207 (not_207_out, OP2);
  not not_208 (not_208_out, F14);
  not not_209 (not_209_out, F13);
  not not_210 (not_210_out, F12);
  not not_211 (not_211_out, OP6);
  not not_212 (not_212_out, OP4);
  not not_213 (not_213_out, OP3);
  not not_214 (not_214_out, OP2);
  not not_215 (not_215_out, F12);
  not not_216 (not_216_out, OP3);
  not not_217 (not_217_out, OP2);
  not not_218 (not_218_out, OP4);
  not not_219 (not_219_out, OP3);
  not not_220 (not_220_out, OP2);
  not not_221 (not_221_out, OP3);
  not not_222 (not_222_out, OP2);
  not not_223 (not_223_out, F30);
  not not_224 (not_224_out, F25);
  not not_225 (not_225_out, F14);
  not not_226 (not_226_out, F13);
  not not_227 (not_227_out, F12);
  not not_228 (not_228_out, OP3);
  not not_229 (not_229_out, OP2);
  not not_230 (not_230_out, F14);
  not not_231 (not_231_out, F12);
  not not_232 (not_232_out, OP6);
  not not_233 (not_233_out, OP4);
  not not_234 (not_234_out, OP3);
  not not_235 (not_235_out, OP2);
  not not_236 (not_236_out, F14);
  not not_237 (not_237_out, F13);
  not not_238 (not_238_out, F12);
  not not_239 (not_239_out, OP6);
  not not_240 (not_240_out, OP4);
  not not_241 (not_241_out, OP3);
  not not_242 (not_242_out, OP2);
  not not_243 (not_243_out, F14);
  not not_244 (not_244_out, F13);
  not not_245 (not_245_out, F12);
  not not_246 (not_246_out, OP4);
  not not_247 (not_247_out, OP3);
  not not_248 (not_248_out, OP2);
  not not_249 (not_249_out, F14);
  not not_250 (not_250_out, F13);
  not not_251 (not_251_out, OP4);
  not not_252 (not_252_out, OP3);
  not not_253 (not_253_out, OP2);
  not not_254 (not_254_out, F14);
  not not_255 (not_255_out, F13);
  not not_256 (not_256_out, F12);
  not not_257 (not_257_out, OP4);
  not not_258 (not_258_out, OP3);
  not not_259 (not_259_out, OP4);
  and and_1 (MemToReg, not_1_out, F13, not_2_out, not_3_out, not_4_out, not_5_out, not_6_out, not_7_out);
  and and_2 (and_2_out, not_8_out, F13, not_9_out, not_10_out, OP5, not_11_out, not_12_out, not_13_out);
  and and_3 (and_3_out, not_14_out, not_15_out, not_16_out, not_17_out, OP5, not_18_out, not_19_out, not_20_out);
  and and_4 (and_4_out, not_21_out, not_22_out, not_23_out, not_24_out, not_25_out, OP4, not_26_out, not_27_out);
  and and_5 (and_5_out, F14, F13, F12, not_28_out, not_29_out, OP4, not_30_out, not_31_out);
  and and_6 (and_6_out, F14, F13, not_32_out, not_33_out, not_34_out, OP4, not_35_out, not_36_out);
  and and_7 (and_7_out, F14, not_37_out, not_38_out, not_39_out, not_40_out, OP4, not_41_out, not_42_out);
  and and_8 (and_8_out, not_43_out, F13, not_44_out, not_45_out, not_46_out, OP4, not_47_out, not_48_out);
  and and_9 (and_9_out, not_49_out, not_50_out, not_51_out, not_52_out, F12, not_53_out, not_54_out, OP4, not_55_out, not_56_out);
  and and_10 (and_10_out, not_57_out, not_58_out, F14, not_59_out, F12, not_60_out, not_61_out, OP4, not_62_out, not_63_out);
  and and_11 (and_11_out, F30, not_64_out, F14, not_65_out, F12, not_66_out, not_67_out, OP4, not_68_out, not_69_out);
  and and_12 (and_12_out, not_70_out, F13, not_71_out, not_72_out, not_73_out, not_74_out, not_75_out, not_76_out);
  and and_13 (and_13_out, not_77_out, F13, not_78_out, not_79_out, OP5, not_80_out, not_81_out, not_82_out);
  and and_14 (and_14_out, not_83_out, not_84_out, not_85_out, OP6, OP5, not_86_out, not_87_out, OP2);
  and and_15 (and_15_out, not_88_out, not_89_out, not_90_out, not_91_out, OP5, not_92_out, not_93_out, not_94_out);
  and and_16 (and_16_out, not_95_out, not_96_out, not_97_out, not_98_out, not_99_out, not_100_out, OP5, OP4, not_101_out, not_102_out);
  and and_17 (and_17_out, F30, not_103_out, not_104_out, not_105_out, not_106_out, not_107_out, OP5, OP4, not_108_out, not_109_out);
  and and_18 (and_18_out, not_110_out, not_111_out, F14, F13, F12, not_112_out, OP5, OP4, not_113_out, not_114_out);
  and and_19 (and_19_out, not_115_out, not_116_out, F14, F13, not_117_out, not_118_out, OP5, OP4, not_119_out, not_120_out);
  and and_20 (and_20_out, not_121_out, not_122_out, not_123_out, F13, not_124_out, not_125_out, OP5, OP4, not_126_out, not_127_out);
  and and_21 (and_21_out, not_128_out, not_129_out, not_130_out, F13, F12, not_131_out, OP5, OP4, not_132_out, not_133_out);
  and and_22 (and_22_out, not_134_out, not_135_out, not_136_out, not_137_out, not_138_out, OP4, not_139_out, not_140_out);
  and and_23 (and_23_out, F14, F13, F12, not_141_out, not_142_out, OP4, not_143_out, not_144_out);
  and and_24 (and_24_out, F14, F13, not_145_out, not_146_out, not_147_out, OP4, not_148_out, not_149_out);
  and and_25 (and_25_out, F14, not_150_out, not_151_out, not_152_out, not_153_out, OP4, not_154_out, not_155_out);
  and and_26 (and_26_out, not_156_out, F13, not_157_out, not_158_out, not_159_out, OP4, not_160_out, not_161_out);
  and and_27 (and_27_out, not_162_out, not_163_out, not_164_out, not_165_out, F12, not_166_out, not_167_out, OP4, not_168_out, not_169_out);
  and and_28 (and_28_out, not_170_out, not_171_out, F14, not_172_out, F12, not_173_out, not_174_out, OP4, not_175_out, not_176_out);
  and and_29 (and_29_out, F30, not_177_out, F14, not_178_out, F12, not_179_out, not_180_out, OP4, not_181_out, not_182_out);
  and and_30 (and_30_out, not_183_out, F13, not_184_out, not_185_out, not_186_out, not_187_out, not_188_out, not_189_out);
  and and_31 (and_31_out, OP6, OP5, not_190_out, OP3, OP2);
  and and_32 (and_32_out, not_191_out, not_192_out, not_193_out, OP6, OP5, not_194_out, not_195_out, OP2);
  and and_33 (and_33_out, F30, not_196_out, F14, not_197_out, F12, not_198_out, OP5, OP4, not_199_out, not_200_out);
  and and_34 (and_34_out, not_201_out, not_202_out, F14, not_203_out, not_204_out, not_205_out, OP5, OP4, not_206_out, not_207_out);
  and and_35 (SB, not_208_out, not_209_out, not_210_out, not_211_out, OP5, not_212_out, not_213_out, not_214_out);
  and and_36 (CSRRSI, F14, F13, not_215_out, OP6, OP5, OP4, not_216_out, not_217_out);
  and and_37 (BGEU, F14, F13, F12, OP6, OP5, not_218_out, not_219_out, not_220_out);
  and and_38 (CSRRCI, F14, F13, F12, OP6, OP5, OP4, not_221_out, not_222_out);
  and and_39 (ecall, not_223_out, not_224_out, not_225_out, not_226_out, not_227_out, OP6, OP5, OP4, not_228_out, not_229_out);
  and and_40 (and_40_out, not_230_out, F13, not_231_out, not_232_out, OP5, not_233_out, not_234_out, not_235_out);
  and and_41 (and_41_out, not_236_out, not_237_out, not_238_out, not_239_out, OP5, not_240_out, not_241_out, not_242_out);
  and and_42 (BEQ, not_243_out, not_244_out, not_245_out, OP6, OP5, not_246_out, not_247_out, not_248_out);
  and and_43 (BNE, not_249_out, not_250_out, F12, OP6, OP5, not_251_out, not_252_out, not_253_out);
  and and_44 (JALR, not_254_out, not_255_out, not_256_out, OP6, OP5, not_257_out, not_258_out, OP2);
  and and_45 (JAL, OP6, OP5, not_259_out, OP3, OP2);
  or or_1 (MemWrite, and_2_out, and_3_out);
  or or_2 (S_Type, and_40_out, and_41_out);
  or or_3 (ALU_SRC, and_4_out, and_5_out, and_6_out, and_7_out, and_8_out, and_9_out, and_10_out, and_11_out, and_12_out, and_13_out, and_14_out, and_15_out);
  or or_4 (RegWrite, and_16_out, and_17_out, and_18_out, and_19_out, and_20_out, and_21_out, and_22_out, and_23_out, and_24_out, and_25_out, and_26_out, and_27_out, and_28_out, and_29_out, and_30_out, and_31_out, and_32_out, and_33_out, and_34_out);
endmodule

// ALU
module ALU (
  input  [31:0] X,
  input  [31:0] Y,
  input  [3:0] AluOP,
  output out_4,
  output Equal,
  output out_6,
  output [31:0] Result,
  output [31:0] Result_2
);

  wire [0:0] comparator_1_lt, comparator_2_lt;
  wire [31:0] adder_1_out, AND_out, divider_1_out, divider_1_rem, multiplier_1_cout, multiplier_1_out,
       NOR_out, OR_out, shifter_1_out, shifter_2_out, shifter_3_out, subtractor_1_out, XOR_out;

  assign AND_out = X & Y;  // AND_Gate AND, 32 bits wide
  assign OR_out = X | Y;  // OR_Gate OR, 32 bits wide
  Shifter #(.width(32), .shift("ll")) shifter_1 (.in(X), .\dist (Y[4:0]), .out(shifter_1_out));
  Shifter #(.width(32), .shift("ar")) shifter_2 (.in(X), .\dist (Y[4:0]), .out(shifter_2_out));
  Shifter #(.width(32), .shift("lr")) shifter_3 (.in(X), .\dist (Y[4:0]), .out(shifter_3_out));
  Multiplier #(.width(32)) multiplier_1 (.a(X), .b(Y), .out(multiplier_1_out), .cout(multiplier_1_cout));  // open: cin
  Divider #(.width(32)) divider_1 (.a(X), .b(Y), .out(divider_1_out), .rem(divider_1_rem));  // open: upper
  Adder #(.width(32)) adder_1 (.a(X), .b(Y), .out(adder_1_out));  // open: cin, cout
  Subtractor #(.width(32)) subtractor_1 (.a(X), .b(Y), .out(subtractor_1_out));  // open: bin, bout
  assign XOR_out = X ^ Y;  // XOR_Gate XOR, 32 bits wide
  assign NOR_out = ~(X | Y);  // NOR_Gate NOR, 32 bits wide
  Comparator #(.width(32), .mode("twosComplement")) comparator_1 (
    .a(X), .b(Y), .eq(Equal), .lt(comparator_1_lt[0]));  // open: gt
  Comparator #(.width(32), .mode("unsigned")) comparator_2 (.a(X), .b(Y), .lt(comparator_2_lt[0]));  // open: gt, eq
  Multiplexer #(.select(4), .width(32), .disabled("Z"), .enable("false")) multiplexer_1 (
    .in0(shifter_1_out), .in1(shifter_2_out), .in2(shifter_3_out), .in3(multiplier_1_out),
    .in4(divider_1_out), .in5(adder_1_out), .in6(subtractor_1_out), .in7(AND_out), .in8(OR_out),
    .in9(XOR_out), .in10(NOR_out), .in11({{31{1'b0}}, comparator_1_lt[0]}),
    .in12({{31{1'b0}}, comparator_2_lt[0]}), .in13({32{1'b0}}), .in14({32{1'b0}}), .in15({32{1'b0}}),
    .out(Result), .sel(AluOP));
  Multiplexer #(.select(4), .width(32), .disabled("Z"), .enable("false")) multiplexer_2 (
    .in0({32{1'b0}}), .in1({32{1'b0}}), .in2({32{1'b0}}), .in3(multiplier_1_cout), .in4(divider_1_rem),
    .in5({32{1'b0}}), .in6({32{1'b0}}), .in7({32{1'b0}}), .in8({32{1'b0}}), .in9({32{1'b0}}),
    .in10({32{1'b0}}), .in11({32{1'b0}}), .in12({32{1'b0}}), .in13({32{1'b0}}), .in14({32{1'b0}}),
    .in15({32{1'b0}}), .out(Result_2), .sel(AluOP));
  Multiplexer #(.select(4), .width(1), .disabled("Z"), .enable("false")) multiplexer_3 (
    .in0(1'b0), .in1(1'b0), .in2(1'b0), .in3(1'b0), .in4(1'b0), .in5(1'b0), .in6(1'b0), .in7(1'b0),
    .in8(1'b0), .in9(1'b0), .in10(1'b0), .in11(comparator_1_lt[0]), .in12(comparator_2_lt[0]), .in13(1'b0),
    .in14(1'b0), .in15(1'b0), .out(out_6), .sel(AluOP));
  not not_1 (out_4, out_6);

  // Other names for the same wires on the sheet: Result2[31:0] = Result_2; S[3:0] = AluOP; tunnel = out_6;
  //   tunnel_t = out_4

  // Notes on the sheet:
  //   不要改变此引脚区域内容，也不要改变ALU封装形式
  //   输入引脚
  //   输出引脚
endmodule

module Regifile (
  input  [31:0] Din,
  input  Clk,
  input  WE,
  input  [4:0] R1_num,
  input  [4:0] W_num,
  input  [4:0] R2_num,
  output [31:0] R1,
  output [31:0] R2
);

  // RegisterFile registerfile_1: pin names not known; wires that end beside it: Din, Clk, WE, W_num, R1_num, R2_num, R1, R2
endmodule

module \理想流水线  (
  output RegWrite,
  output MemWrite,
  output [31:0] IF_PC,
  output [31:0] ID_PC,
  output [31:0] EX_PC,
  output [31:0] M_PC,
  output [31:0] WB_PC,
  output [31:0] RDin,
  output [31:0] MDin,
  output [31:0] LedData
);

  wire AluSrcB, and_1_out, and_2_out, and_3_out, and_4_out, and_5_out, begu, Beq, BGEU, Bne, CLK,
       clock_1_out, clock_2_out, comparator_1_eq, comparator_2_eq, comparator_2_lt, d_ff_1_q, ecall, equal,
       EX_ecall, Go, halt, ID_Beq, ID_BGEU, ID_Bne, ID_ecall, ID_Jal, ID_Jalr, ID_MemToReg, ID_MemWrite,
       ID_RegWrite, ID_SB, IR1, IR2, IR3, Jal, Jalr, key, MBM_ecall, nand_1_out, not_1_out, not_2_out,
       not_3_out, not_4_out, or_1_out, riscv_probe_2_p1, RST, SB, W1, W2, W3, \单周期硬布线控制器_1_s_type ,
       \理想ex_mem_1_jal_2 , \理想ex_mem_1_jalr_2 , \理想ex_mem_1_memtoreg_2 , \理想ex_mem_1_regwrite_2 ,
       \理想ex_mem_1_sb_2 , \理想id_ex_1_alusrcb_2 , \理想id_ex_1_jal_2 , \理想id_ex_1_jalr_2 ,
       \理想id_ex_1_memtoreg_2 , \理想id_ex_1_memwrite_2 , \理想id_ex_1_regwrite_2 , \理想id_ex_1_sb_2 ,
       \理想mem_wb_1_memtoreg_2 ;
  wire [1:0] select;
  wire [3:0] AluOP, \理想id_ex_1_aluop_2 ;
  wire [4:0] multiplexer_5_out, multiplexer_6_out, rd, \理想ex_mem_1_rd_2 , \理想id_ex_1_rd_2 ;
  wire [7:0] SB1, \理想ex_mem_1_sb1_2 ;
  wire [9:0] \理想ex_mem_1_alu_2 ;
  wire [11:0] shifter_1_out;
  wire [12:0] CNT_num;
  wire [15:0] \LoadUse次数 , \总周期数 , \插入气泡数 , \无条件分支数 , \条件分支成功数 ;
  wire [19:0] shifter_2_out;
  wire [31:0] bit_extender_1_out, bit_extender_2_out, bit_extender_3_out, bit_extender_4_out, EX_IR, ID_IR,
       IF_IR, immB, immJal, MEM_IR, multiplexer_1_out, multiplexer_2_out, multiplexer_3_out,
       multiplexer_4_out, multiplexer_7_out, multiplexer_8_out, multiplexer_9_out, PC_4, PCB, PCBGEU, PCJal,
       PCJalr, ram_1_data, rs1, rs2, SB2, sb_t, WB_IR, \理想ex_mem_1_select_4 , \理想id_ex_1_imm_2 ,
       \理想id_ex_1_rs1_2 , \理想id_ex_1_rs2_2 , \理想mem_wb_1_alu_2 ;
  wire [31:2] alu_1_result;

  Button \u_总复位  (.out(RST));
  Button _1 (.out(IR1));
  Button _2 (.out(IR2));
  Button _3 (.out(IR3));
  // Probe on \总周期数 
  // Probe on \总周期数 
  Counter #(.width(16), .max('hffff), .ongoal("wrap"), .trigger("rising"), .behavior("old")) counter_1 (
    .Q(\总周期数 ), .clk(and_1_out));  // open: load, D, count, carry, clr, preset
  and and_1 (and_1_out, CLK, not_1_out);
  not not_1 (not_1_out, halt);
  Button \u_继续运行  (.out(Go));
  LED #(.active("true")) led_1 (.in(W1));
  LED #(.active("true")) led_2 (.in(W2));
  LED #(.active("true")) led_3 (.in(W3));
  Comparator #(.width(32), .mode("twosComplement")) comparator_1 (
    .a(rs1), .b(32'ha), .eq(comparator_1_eq));  // open: gt, lt
  Multiplexer #(.select(1), .width(32), .disabled("Z"), .enable("false")) multiplexer_1 (
    .in0(multiplexer_2_out), .in1(PCJalr), .out(multiplexer_1_out), .sel(Jalr));
  Multiplexer #(.select(1), .width(32), .disabled("Z"), .enable("false")) multiplexer_2 (
    .in0(multiplexer_3_out), .in1(PCJal), .out(multiplexer_2_out), .sel(Jal));
  and and_2 (and_2_out, begu, BGEU);
  Multiplexer #(.select(1), .width(32), .disabled("Z"), .enable("false")) multiplexer_3 (
    .in0(multiplexer_4_out), .in1(PCBGEU), .out(multiplexer_3_out), .sel(and_2_out));
  Multiplexer #(.select(1), .width(32), .disabled("Z"), .enable("false")) multiplexer_4 (
    .in0(PC_4), .in1(PCB), .out(multiplexer_4_out), .sel(key));
  Hex_Digit_Display hex_digit_display_1 (.value(LedData[31:28]));  // open: dp
  // Probe on IF_PC[19:0]
  // RiscV_Probe riscv_probe_1: pin names not known; wires that end beside it: IF_IR
  and and_3 (and_3_out, ecall, comparator_1_eq);
  Register #(.width(32), .trigger("rising"), .Select("low")) PC (
    .D(multiplexer_1_out), .en(not_2_out), .Q(IF_PC), .clk(CLK), .clr(RST));
  not not_2 (not_2_out, halt);
  Hex_Digit_Display hex_digit_display_2 (.value(LedData[23:20]));  // open: dp
  Hex_Digit_Display hex_digit_display_3 (.value(LedData[27:24]));  // open: dp
  // Probe on ID_PC[19:0]
  // RiscV_Probe riscv_probe_2: pin names not known; wires that end beside it: riscv_probe_2_p1, ID_IR
  xor xor_1 (riscv_probe_2_p1, and_3_out, Go);
  // Probe on IF_PC
  Hex_Digit_Display hex_digit_display_4 (.value(LedData[15:12]));  // open: dp
  Hex_Digit_Display hex_digit_display_5 (.value(LedData[19:16]));  // open: dp
  Register #(.width(1), .trigger("falling"), .Select("low")) PC_2 (
    .D(riscv_probe_2_p1), .en(riscv_probe_2_p1), .Q(halt), .clk(CLK), .clr(Go));
  Counter #(.width(32), .max('hffffffff), .ongoal("wrap"), .trigger("rising"), .behavior("old")) counter_2 (
    .load(ecall), .D(rs2), .count(1'b0), .Q(LedData), .clk(CLK));  // open: carry, clr, preset
  // Probe on IF_IR
  Hex_Digit_Display hex_digit_display_6 (.value(LedData[7:4]));  // open: dp
  Hex_Digit_Display hex_digit_display_7 (.value(LedData[11:8]));  // open: dp
  Clock #(.highDuration(1), .lowDuration(1)) clock_1 (.out(clock_1_out));
  // Probe on EX_PC[19:0]
  // RiscV_Probe riscv_probe_3: pin names not known; wires that end beside it: clock_1_out, EX_IR, CLK
  ROM #(.addrWidth(10), .dataWidth(32), .Select("high")) rom_1 (.addr(IF_PC[11:2]), .data(IF_IR));
  Hex_Digit_Display hex_digit_display_8 (.value(LedData[3:0]));  // open: dp
  \理想IF_ID  \u_理想if_id_1  (
    .IF_PC(IF_PC), .IF_IR(IF_IR), .ID_PC(ID_PC), .ID_IR(ID_IR), .CLK(CLK));  // open: 同步清零_高电平有效, 使能端_低电平有效_stall_高电平有效
  // Probe on \总周期数 
  // Probe on M_PC[19:0]
  // RiscV_Probe riscv_probe_4: pin names not known; wires that end beside it: MEM_IR
  // Probe on ID_IR
  // Probe on \总周期数 
  // Probe on \无条件分支数 
  // Probe on \条件分支成功数 
  // Probe on \插入气泡数 
  // Probe on \LoadUse次数 
  // Probe on IF_PC[11:0]
  // Probe on WB_PC[19:0]
  // RiscV_Probe riscv_probe_5: pin names not known; wires that end beside it: WB_IR
  \单周期硬布线控制器  \u_单周期硬布线控制器_1  (
    .Funct({ID_IR[30], ID_IR[25], ID_IR[14:12]}), .OP(ID_IR[6:2]), .ALU_OP(AluOP), .MemToReg(ID_MemToReg),
    .MemWrite(ID_MemWrite), .ALU_SRC(AluSrcB), .RegWrite(ID_RegWrite), .ecall(ID_ecall),
    .S_type(\单周期硬布线控制器_1_s_type ), .Jalr(ID_Jalr), .Beq(ID_Beq), .JAL(ID_Jal), .Bne(ID_Bne), .SB(ID_SB),
    .BGEU(ID_BGEU));  // open: CSRRSI, CSRRCI
  Multiplexer #(.select(1), .width(5), .disabled("Z"), .enable("false")) multiplexer_5 (
    .in0(ID_IR[19:15]), .in1(5'b10001), .out(multiplexer_5_out), .sel(ecall));
  Multiplexer #(.select(1), .width(5), .disabled("Z"), .enable("false")) multiplexer_6 (
    .in0(ID_IR[24:20]), .in1(5'b01010), .out(multiplexer_6_out), .sel(ecall));
  assign bit_extender_1_out = {{20{ID_IR[31]}}, ID_IR[31:20]};  // Bit_Extender bit_extender_1
  assign bit_extender_2_out = {{20{ID_IR[31]}}, {ID_IR[31:25], ID_IR[11:7]}};  // Bit_Extender bit_extender_2
  Shifter #(.width(12), .shift("ll")) shifter_1 (
    .in({ID_IR[31], ID_IR[7], ID_IR[30:25], ID_IR[11:8]}), .\dist (4'b0001), .out(shifter_1_out));
  Shifter #(.width(20), .shift("ll")) shifter_2 (
    .in({ID_IR[31], ID_IR[19:12], ID_IR[20], ID_IR[30:21]}), .\dist (5'b00001), .out(shifter_2_out));
  // Probe on EX_PC[11:0]
  // Probe on ID_PC[11:0]
  // Probe on multiplexer_5_out
  // Probe on multiplexer_6_out
  Multiplexer #(.select(1), .width(32), .disabled("Z"), .enable("false")) multiplexer_7 (
    .in0(bit_extender_1_out), .in1(bit_extender_2_out), .out(multiplexer_7_out), .sel(\单周期硬布线控制器_1_s_type ));
  assign bit_extender_3_out = {{20{shifter_1_out[11]}}, shifter_1_out};  // Bit_Extender bit_extender_3
  assign bit_extender_4_out = {{12{shifter_2_out[19]}}, shifter_2_out};  // Bit_Extender bit_extender_4
  // Probe on M_PC[11:0]
  D_Flip_Flop #(.trigger("high"), .Pre_Clr_Positions("LEGACY"), .NegatePresetClear("false"), .enable("true"), .NewFFLayout("false")) d_ff_1 (.Q(d_ff_1_q));  // open: clk, D, Qn, preset, en, reset
  // Probe on 13'hc
  // Probe on WB_PC[11:0]
  Comparator #(.width(13), .mode("twosComplement")) comparator_2 (
    .a(CNT_num), .b(13'hc), .eq(comparator_2_eq), .lt(comparator_2_lt));  // open: gt
  Clock #(.highDuration(1), .lowDuration(1)) clock_2 (.out(clock_2_out));
  Regifile regifile_1 (
    .Din(RDin), .Clk(CLK), .R1(rs1), .R2(rs2), .WE(RegWrite), .W_num(rd), .R1_num(multiplexer_5_out),
    .R2_num(multiplexer_6_out));
  nand nand_1 (nand_1_out, d_ff_1_q, comparator_2_eq);
  Counter #(.width(13), .max('h1fff), .ongoal("stay"), .trigger("rising"), .behavior("old")) counter_3 (
    .count(comparator_2_lt), .Q(CNT_num), .clk(clock_2_out));  // open: load, D, carry, clr, preset
  assign CLK = nand_1_out ? clock_2_out : 1'bz;  // Controlled_Buffer controlled_buffer_1
  \理想ID_EX  \u_理想id_ex_1  (
    .ID_IR(ID_IR), .EX_IR(EX_IR), .ID_PC(ID_PC), .EX_PC(EX_PC), .jal(ID_Jal), .Jal_2(\理想id_ex_1_jal_2 ),
    .jalr(ID_Jalr), .jalr_2(\理想id_ex_1_jalr_2 ), .SB(ID_SB), .SB_2(\理想id_ex_1_sb_2 ), .BGEU(ID_BGEU),
    .BGEU_2(BGEU), .Beq(ID_Beq), .Beq_2(Beq), .Bne(ID_Bne), .Bne_2(Bne), .MemToReg(ID_MemToReg),
    .MemToReg_2(\理想id_ex_1_memtoreg_2 ), .MemWrite(ID_MemWrite), .MemWrite_2(\理想id_ex_1_memwrite_2 ),
    .AluSrcB(AluSrcB), .AluSrcB_2(\理想id_ex_1_alusrcb_2 ), .rs1(rs1), .rs1_2(\理想id_ex_1_rs1_2 ), .rs2(rs2),
    .rs2_2(\理想id_ex_1_rs2_2 ), .immB(bit_extender_3_out), .immB_2(immB), .immJal(bit_extender_4_out),
    .immJal_2(immJal), .CLK(CLK), .ecall(ID_ecall), .ecall_2(EX_ecall), .RegWrite_2(\理想id_ex_1_regwrite_2 ),
    .RegWrite(ID_RegWrite), .AluOP(AluOP), .AluOP_2(\理想id_ex_1_aluop_2 ), .imm_2(\理想id_ex_1_imm_2 ),
    .imm(multiplexer_7_out), .rd_2(\理想id_ex_1_rd_2 ), .rd(ID_IR[11:7]));  // open: 同步清零_气泡_高电平有效, 使能端_低电平有效_stall_高电平有效, FwdRs1, FwdRs1_2, FwdRs2, FwdRs2_2
  Pull_Resistor #(.pull(1)) pull_resistor_1 (.node(CLK));
  Multiplexer #(.select(1), .width(32), .disabled("Z"), .enable("false")) multiplexer_8 (
    .in0(\理想id_ex_1_rs2_2 ), .in1(\理想id_ex_1_imm_2 ), .out(multiplexer_8_out), .sel(\理想id_ex_1_alusrcb_2 ));
  Adder #(.width(32)) adder_1 (.a(IF_PC), .b(32'h4), .out(PC_4));  // open: cin, cout
  Adder #(.width(32)) adder_2 (.a(IF_PC), .b(immB), .out(PCB));  // open: cin, cout
  Adder #(.width(32)) adder_3 (.a(IF_PC), .b(immJal), .out(PCJal));  // open: cin, cout
  Adder #(.width(32)) adder_4 (.a(IF_PC), .b(immB), .out(PCBGEU));  // open: cin, cout
  ALU alu_1 (
    .X(\理想id_ex_1_rs1_2 ), .Y(multiplexer_8_out), .AluOP(\理想id_ex_1_aluop_2 ), .Equal(equal),
    .Result({alu_1_result, select}), .out_4(begu));  // open: Result_2, out_6
  Multiplexer #(.select(1), .width(32), .disabled("Z"), .enable("false")) multiplexer_9 (
    .in0(\理想id_ex_1_rs2_2 ), .in1(sb_t), .out(multiplexer_9_out), .sel(SB));
  \理想EX_MEM  \u_理想ex_mem_1  (
    .EX_IR(EX_IR), .EX_PC(EX_PC), .jal(\理想id_ex_1_jal_2 ), .jalr(\理想id_ex_1_jalr_2 ), .SB(\理想id_ex_1_sb_2 ),
    .MemToReg(\理想id_ex_1_memtoreg_2 ), .MemWrite(\理想id_ex_1_memwrite_2 ), .ALU(alu_1_result[11:2]),
    .MDin(multiplexer_9_out), .MEM_IR(MEM_IR), .MEM_PC(M_PC), .Jal_2(\理想ex_mem_1_jal_2 ),
    .jalr_2(\理想ex_mem_1_jalr_2 ), .SB_2(\理想ex_mem_1_sb_2 ), .MemToReg_2(\理想ex_mem_1_memtoreg_2 ),
    .MemWrite_2(MemWrite), .ALU_2(\理想ex_mem_1_alu_2 ), .MDin_2(MDin), .CLK(CLK),
    .select_4(\理想ex_mem_1_select_4 ), .select_2({alu_1_result, select}), .SB1(\理想id_ex_1_rs2_2 [7:0]),
    .SB1_2(\理想ex_mem_1_sb1_2 ), .RegWrite(\理想id_ex_1_regwrite_2 ), .RegWrite_2(\理想ex_mem_1_regwrite_2 ),
    .rd(\理想id_ex_1_rd_2 ), .rd_2(\理想ex_mem_1_rd_2 ), .ecall(EX_ecall), .ecall_2(MBM_ecall));  // open: select, rs1, rs2, select_3, rs1_2, rs2_2, 同步清零_气泡_高电平有效, 使能端_低电平有效_stall_高电平有效
  not not_3 (not_3_out, halt);
  RAM #(.addrWidth(10), .dataWidth(32), .bus("separate"), .Select("high")) ram_1 (
    .addr(\理想ex_mem_1_alu_2 ), .din(MDin), .data(ram_1_data), .str(MemWrite), .sel(not_3_out), .clk(CLK));  // open: ld, clr
  Multiplexer #(.select(2), .width(32), .disabled("Z"), .enable("false")) multiplexer_10 (
    .in0({SB2[31:8], SB1}), .in1({SB2[31:16], SB1, SB2[7:0]}), .in2({SB2[31:24], SB1, SB2[15:0]}),
    .in3({SB1, SB2[23:0]}), .out(sb_t), .sel(select));
  \理想MEM_WB  \u_理想mem_wb_1  (
    .EX_IR(MEM_IR), .EX_PC(M_PC), .jal(\理想ex_mem_1_jal_2 ), .jalr(\理想ex_mem_1_jalr_2 ),
    .SB(\理想ex_mem_1_sb_2 ), .MemToReg(\理想ex_mem_1_memtoreg_2 ), .ALU(\理想ex_mem_1_select_4 ),
    .MDout(ram_1_data), .MEM_IR(WB_IR), .MEM_PC(WB_PC), .Jal_2(Jal), .jalr_2(Jalr), .SB_2(SB),
    .MemToReg_2(\理想mem_wb_1_memtoreg_2 ), .ALU_2(\理想mem_wb_1_alu_2 ), .MDout_2(SB2), .CLK(CLK),
    .SB1(\理想ex_mem_1_sb1_2 ), .SB1_2(SB1), .RegWrite_2(RegWrite), .RegWrite(\理想ex_mem_1_regwrite_2 ),
    .rd(\理想ex_mem_1_rd_2 ), .rd_2(rd), .ecall(MBM_ecall), .ecall_2(ecall));  // open: select, rs1, rs2, select_2, rs1_2, rs2_2, 同步清零_气泡_高电平有效, 使能端_低电平有效_stall_高电平有效
  Multiplexer #(.select(1), .width(32), .disabled("Z"), .enable("false")) multiplexer_11 (
    .in0(\理想mem_wb_1_alu_2 ), .in1(SB2), .out(PCJalr), .sel(\理想mem_wb_1_memtoreg_2 ));
  or or_1 (or_1_out, Jal, Jalr);
  Multiplexer #(.select(1), .width(32), .disabled("Z"), .enable("false")) multiplexer_12 (
    .in0(PCJalr), .in1(PC_4), .out(RDin), .sel(or_1_out));
  not not_4 (not_4_out, equal);
  and and_4 (and_4_out, equal, Beq);
  and and_5 (and_5_out, not_4_out, Bne);
  or or_2 (key, and_4_out, and_5_out);

  // Other names for the same wires on the sheet: ID_rd[4:0] = ID_IR[11:7]; MEM_PC[31:0] = M_PC; PC[31:0] = IF_PC

  // Notes on the sheet:
  //   中断源
  //   中断等待指示
  //   时空图监测，可删除
  //   数码管输出
  //   指令存储器
  //   contents of rom_1 (hex, n*v repeats v):
  //   413 493 913 993 46413 14e493 296913 39e993 842023 942223 1242423 1342623 a00893 493 913 993 73
  //   指令字
  //   Jal
  //   Jalr
  //   SB
  //   BGEU
  //   ecall
  //   I型指令
  //   s型指令
  //   B型指令
  //   Jal
  //   Beq
  //   Bne
  //   MemToReg
  //   MemWrite
  //   AluOP
  //   AluSrcB
  //   RegWrite
  //   S_type
  //   控制位
  //   流水调试日志用
  //   暂停节拍，不能为0
  //   戳工具置1进入计数暂停模式，ctrl+k时钟自动运行到对应节拍暂停
  //   ctrl+k关闭时钟连续运行，将控制位置零，进入单步调试模式调试
  //   用这个时钟源需要去掉电路中的其他时钟源
  //   可计数暂停的时钟源
  //   为方便自动评测，需要输出流水线各段保存的PC值，注意是PC不是PC+4，另外ID段寄存器写入信息，Mem段内存写入信息也要输出
  //   数据存储器
endmodule

module \气泡流水线  (
  output RegWrite,
  output MemWrite,
  output [31:0] IF_PC,
  output [31:0] ID_PC,
  output [31:0] EX_PC,
  output [31:0] M_PC,
  output [31:0] WB_PC,
  output [31:0] RDin,
  output [31:0] MDin,
  output [31:0] LedData
);

  wire AluSrcB, and_1_out, and_2_out, and_3_out, and_4_out, and_5_out, and_6_out, and_7_out, and_8_out,
       and_9_out, and_10_out, and_11_out, and_12_out, and_13_out, and_14_out, and_15_out, and_16_out,
       and_17_out, and_18_out, and_19_out, and_20_out, and_21_out, begu, Beq, BGEU, Bne, CLK, clock_1_out,
       clock_2_out, comparator_1_eq, comparator_2_eq, comparator_3_eq, comparator_4_eq, comparator_5_eq,
       comparator_6_eq, comparator_7_eq, comparator_8_eq, comparator_8_lt, d_ff_1_q, DataHazzard, ecall,
       equal, EX_ecall, EX_RegWrite, Go, halt, ID_Beq, ID_BGEU, ID_Bne, ID_ecall, ID_Jal, ID_Jalr,
       ID_MemToReg, ID_MemWrite, ID_RegWrite, ID_SB, IR1, IR2, IR3, Jal, Jalr, Jamp, key, MBM_ecall,
       MEM_RegWrite, nand_1_out, not_1_out, not_2_out, not_3_out, not_4_out, or_2_out, or_5_out,
       riscv_probe_2_p1, RS1_Used, RS2_Used, RST, SB, W1, W2, W3, WB_Jal, WB_Jalr, \单周期硬布线控制器_1_s_type ,
       \理想ex_mem_1_jal_2 , \理想ex_mem_1_jalr_2 , \理想ex_mem_1_memtoreg_2 , \理想ex_mem_1_sb_2 ,
       \理想id_ex_1_alusrcb_2 , \理想id_ex_1_memtoreg_2 , \理想id_ex_1_memwrite_2 , \理想id_ex_1_sb_2 ,
       \理想mem_wb_1_memtoreg_2 ;
  wire [1:0] select;
  wire [3:0] AluOP, \理想id_ex_1_aluop_2 ;
  wire [4:0] EX_RD_num, Funct, MEM_RD_num, R1_num, R2_num, rd;
  wire [7:0] SB1, \理想ex_mem_1_sb1_2 ;
  wire [9:0] \理想ex_mem_1_alu_2 ;
  wire [11:0] shifter_1_out;
  wire [12:0] CNT_num;
  wire [15:0] \LoadUse次数 , \总周期数 , \插入气泡数 , \无条件分支数 , \条件分支成功数 ;
  wire [19:0] shifter_2_out;
  wire [31:0] adder_6_out, bit_extender_1_out, bit_extender_2_out, bit_extender_3_out, bit_extender_4_out,
       EX_IR, EX_rs1, ID_IR, IF_IR, immB, immJal, MEM_IR, multiplexer_1_out, multiplexer_2_out,
       multiplexer_3_out, multiplexer_4_out, multiplexer_7_out, multiplexer_8_out, multiplexer_9_out,
       multiplexer_11_out, PC_4, PCB, PCBGEU, PCJal, PCJalr, ram_1_data, rs1, rs2, SB2, sb_t, WB_IR,
       \理想ex_mem_1_select_4 , \理想id_ex_1_imm_2 , \理想id_ex_1_rs2_2 , \理想mem_wb_1_alu_2 ;
  wire [31:2] alu_1_result;

  Button \u_总复位  (.out(RST));
  Button _1 (.out(IR1));
  Button _2 (.out(IR2));
  Button _3 (.out(IR3));
  // Probe on \总周期数 
  // Probe on \总周期数 
  Counter #(.width(16), .max('hffff), .ongoal("wrap"), .trigger("rising"), .behavior("old")) counter_1 (
    .Q(\总周期数 ), .clk(and_1_out));  // open: load, D, count, carry, clr, preset
  and and_1 (and_1_out, CLK, not_1_out);
  not not_1 (not_1_out, halt);
  // Probe on multiplexer_1_out
  Button \u_继续运行  (.out(Go));
  LED #(.active("true")) led_1 (.in(W1));
  LED #(.active("true")) led_2 (.in(W2));
  LED #(.active("true")) led_3 (.in(W3));
  Comparator #(.width(32), .mode("twosComplement")) comparator_1 (
    .a(rs1), .b(32'ha), .eq(comparator_1_eq));  // open: gt, lt
  Multiplexer #(.select(1), .width(32), .disabled("Z"), .enable("false")) multiplexer_1 (
    .in0(multiplexer_2_out), .in1(PCJalr), .out(multiplexer_1_out), .sel(Jalr));
  Multiplexer #(.select(1), .width(32), .disabled("Z"), .enable("false")) multiplexer_2 (
    .in0(multiplexer_3_out), .in1(PCJal), .out(multiplexer_2_out), .sel(Jal));
  and and_2 (and_2_out, begu, BGEU);
  Multiplexer #(.select(1), .width(32), .disabled("Z"), .enable("false")) multiplexer_3 (
    .in0(multiplexer_4_out), .in1(PCBGEU), .out(multiplexer_3_out), .sel(and_2_out));
  Multiplexer #(.select(1), .width(32), .disabled("Z"), .enable("false")) multiplexer_4 (
    .in0(PC_4), .in1(PCB), .out(multiplexer_4_out), .sel(key));
  Hex_Digit_Display hex_digit_display_1 (.value(LedData[31:28]));  // open: dp
  // Probe on IF_PC[19:0]
  // RiscV_Probe riscv_probe_1: pin names not known; wires that end beside it: IF_IR
  and and_3 (and_3_out, ID_ecall, comparator_1_eq);
  Register #(.width(32), .trigger("rising"), .Select("low")) PC (
    .D(multiplexer_1_out), .en(and_4_out), .Q(IF_PC), .clk(CLK), .clr(RST));
  and and_4 (and_4_out, ~halt, ~and_5_out);  // AND_Gate
  Hex_Digit_Display hex_digit_display_2 (.value(LedData[27:24]));  // open: dp
  Hex_Digit_Display hex_digit_display_3 (.value(LedData[23:20]));  // open: dp
  // Probe on ID_PC[19:0]
  // RiscV_Probe riscv_probe_2: pin names not known; wires that end beside it: riscv_probe_2_p1, {ID_IR[31], Funct[4], ID_IR[29:26], Funct[3], ID_IR[24:15], Funct[2:0], ID_IR[11:0]}
  xor xor_1 (riscv_probe_2_p1, and_3_out, Go);
  // Probe on IF_PC
  and and_5 (and_5_out, DataHazzard, ~Jamp);  // AND_Gate
  Comparator #(.width(5), .mode("twosComplement")) comparator_2 (
    .a(R1_num), .b(EX_RD_num), .eq(comparator_2_eq));  // open: gt, lt
  Comparator #(.width(5), .mode("twosComplement")) comparator_3 (
    .a(R1_num), .b({5{1'b0}}), .eq(comparator_3_eq));  // open: gt, lt
  Comparator #(.width(5), .mode("twosComplement")) comparator_4 (
    .a(R1_num), .b(MEM_RD_num), .eq(comparator_4_eq));  // open: gt, lt
  Comparator #(.width(5), .mode("twosComplement")) comparator_5 (
    .a(EX_RD_num), .b(R2_num), .eq(comparator_5_eq));  // open: gt, lt
  Comparator #(.width(5), .mode("twosComplement")) comparator_6 (
    .a(R2_num), .b({5{1'b0}}), .eq(comparator_6_eq));  // open: gt, lt
  Comparator #(.width(5), .mode("twosComplement")) comparator_7 (
    .a(R2_num), .b(MEM_RD_num), .eq(comparator_7_eq));  // open: gt, lt
  Hex_Digit_Display hex_digit_display_4 (.value(LedData[19:16]));  // open: dp
  Hex_Digit_Display hex_digit_display_5 (.value(LedData[15:12]));  // open: dp
  Register #(.width(1), .trigger("falling"), .Select("low")) PC_2 (
    .D(riscv_probe_2_p1), .en(riscv_probe_2_p1), .Q(halt), .clk(CLK), .clr(Go));
  Counter #(.width(32), .max('hffffffff), .ongoal("wrap"), .trigger("rising"), .behavior("old")) counter_2 (
    .load(ID_ecall), .D(rs2), .count(1'b0), .Q(LedData), .clk(CLK));  // open: carry, clr, preset
  // Probe on IF_IR
  Hex_Digit_Display hex_digit_display_6 (.value(LedData[11:8]));  // open: dp
  Hex_Digit_Display hex_digit_display_7 (.value(LedData[7:4]));  // open: dp
  Clock #(.highDuration(1), .lowDuration(1)) clock_1 (.out(clock_1_out));
  // Probe on EX_PC[19:0]
  // RiscV_Probe riscv_probe_3: pin names not known; wires that end beside it: clock_1_out, EX_IR, CLK
  ROM #(.addrWidth(10), .dataWidth(32), .Select("high")) rom_1 (.addr(IF_PC[11:2]), .data(IF_IR));
  and and_6 (and_6_out, comparator_2_eq, RS1_Used);
  not not_2 (not_2_out, comparator_3_eq);
  and and_7 (and_7_out, comparator_4_eq, RS1_Used);
  and and_8 (and_8_out, comparator_5_eq, RS2_Used);
  not not_3 (not_3_out, comparator_6_eq);
  and and_9 (and_9_out, comparator_7_eq, RS2_Used);
  Hex_Digit_Display hex_digit_display_8 (.value(LedData[3:0]));  // open: dp
  \理想IF_ID  \u_理想if_id_1  (
    .IF_PC(IF_PC), .IF_IR(IF_IR), .ID_PC(ID_PC),
    .ID_IR({ID_IR[31], Funct[4], ID_IR[29:26], Funct[3], ID_IR[24:15], Funct[2:0], ID_IR[11:0]}),
    .\同步清零_高电平有效 (Jamp), .CLK(CLK), .\使能端_低电平有效_stall_高电平有效 (and_10_out));
  and and_10 (and_10_out, DataHazzard, ~Jamp);  // AND_Gate
  // Probe on \总周期数 
  // Probe on M_PC[19:0]
  // RiscV_Probe riscv_probe_4: pin names not known; wires that end beside it: MEM_IR
  // Probe on {ID_IR[31], Funct[4], ID_IR[29:26], Funct[3], ID_IR[24:15], Funct[2:0], ID_IR[11:0]}
  and and_11 (and_11_out, and_6_out, not_2_out);
  and and_12 (and_12_out, and_7_out, not_2_out);
  and and_13 (and_13_out, and_8_out, not_3_out);
  and and_14 (and_14_out, and_9_out, not_3_out);
  // Probe on \总周期数 
  // Probe on \无条件分支数 
  // Probe on \条件分支成功数 
  // Probe on \插入气泡数 
  // Probe on \LoadUse次数 
  // Probe on IF_PC[11:0]
  // Probe on WB_PC[19:0]
  // RiscV_Probe riscv_probe_5: pin names not known; wires that end beside it: WB_IR
  \单周期硬布线控制器  \u_单周期硬布线控制器_1  (
    .Funct(Funct), .OP(ID_IR[6:2]), .ALU_OP(AluOP), .MemToReg(ID_MemToReg), .MemWrite(ID_MemWrite),
    .ALU_SRC(AluSrcB), .RegWrite(ID_RegWrite), .ecall(ID_ecall), .S_type(\单周期硬布线控制器_1_s_type ),
    .Jalr(ID_Jalr), .Beq(ID_Beq), .JAL(ID_Jal), .Bne(ID_Bne), .SB(ID_SB), .BGEU(ID_BGEU));  // open: CSRRSI, CSRRCI
  Multiplexer #(.select(1), .width(5), .disabled("Z"), .enable("false")) multiplexer_5 (
    .in0(ID_IR[19:15]), .in1(5'b10001), .out(R1_num), .sel(ID_ecall));
  Multiplexer #(.select(1), .width(5), .disabled("Z"), .enable("false")) multiplexer_6 (
    .in0(ID_IR[24:20]), .in1(5'b01010), .out(R2_num), .sel(ID_ecall));
  assign bit_extender_1_out = {{20{ID_IR[31]}}, {ID_IR[31], Funct[4], ID_IR[29:26], Funct[3], ID_IR[24:20]}};  // Bit_Extender bit_extender_1
  assign bit_extender_2_out = {{20{ID_IR[31]}}, {ID_IR[31], Funct[4], ID_IR[29:26], Funct[3], ID_IR[11:7]}};  // Bit_Extender bit_extender_2
  Shifter #(.width(12), .shift("ll")) shifter_1 (
    .in({ID_IR[31], ID_IR[7], Funct[4], ID_IR[29:26], Funct[3], ID_IR[11:8]}), .\dist (4'b0001),
    .out(shifter_1_out));
  Shifter #(.width(20), .shift("ll")) shifter_2 (
    .in({ID_IR[31], ID_IR[19:15], Funct[2:0], ID_IR[20], Funct[4], ID_IR[29:26], Funct[3], ID_IR[24:21]}),
    .\dist (5'b00001), .out(shifter_2_out));
  and and_15 (and_15_out, and_11_out, EX_RegWrite);
  and and_16 (and_16_out, and_12_out, MEM_RegWrite);
  and and_17 (and_17_out, and_13_out, EX_RegWrite);
  and and_18 (and_18_out, and_14_out, MEM_RegWrite);
  // Probe on EX_PC[11:0]
  // Probe on ID_PC[11:0]
  Multiplexer #(.select(1), .width(32), .disabled("Z"), .enable("false")) multiplexer_7 (
    .in0(bit_extender_1_out), .in1(bit_extender_2_out), .out(multiplexer_7_out), .sel(\单周期硬布线控制器_1_s_type ));
  assign bit_extender_3_out = {{20{shifter_1_out[11]}}, shifter_1_out};  // Bit_Extender bit_extender_3
  assign bit_extender_4_out = {{12{shifter_2_out[19]}}, shifter_2_out};  // Bit_Extender bit_extender_4
  // Probe on M_PC[11:0]
  D_Flip_Flop #(.trigger("high"), .Pre_Clr_Positions("LEGACY"), .NegatePresetClear("false"), .enable("true"), .NewFFLayout("false")) d_ff_1 (.Q(d_ff_1_q));  // open: clk, D, Qn, preset, en, reset
  // Probe on 13'h56
  or or_1 (DataHazzard, and_15_out, and_16_out, and_17_out, and_18_out);
  // Probe on WB_PC[11:0]
  Comparator #(.width(13), .mode("twosComplement")) comparator_8 (
    .a(CNT_num), .b(13'h56), .eq(comparator_8_eq), .lt(comparator_8_lt));  // open: gt
  Clock #(.highDuration(1), .lowDuration(1)) clock_2 (.out(clock_2_out));
  or or_2 (or_2_out, Jamp, DataHazzard);
  Regifile regifile_1 (
    .Din(RDin), .Clk(CLK), .R1(rs1), .R2(rs2), .WE(RegWrite), .W_num(rd), .R1_num(R1_num), .R2_num(R2_num));
  nand nand_1 (nand_1_out, d_ff_1_q, comparator_8_eq);
  Counter #(.width(13), .max('h1fff), .ongoal("stay"), .trigger("rising"), .behavior("old")) counter_3 (
    .count(comparator_8_lt), .Q(CNT_num), .clk(clock_2_out));  // open: load, D, carry, clr, preset
  rs_used rs_used_1 (
    .OP2(ID_IR[2]), .OP3(ID_IR[3]), .OP4(ID_IR[4]), .OP5(ID_IR[5]), .OP6(ID_IR[6]), .F12(Funct[0]),
    .F13(Funct[1]), .F14(Funct[2]), .F25(Funct[3]), .F30(Funct[4]), .rs1_used(RS1_Used), .rs2_used(RS2_Used));
  assign CLK = nand_1_out ? clock_2_out : 1'bz;  // Controlled_Buffer controlled_buffer_1
  \理想ID_EX  \u_理想id_ex_1  (
    .ID_IR({ID_IR[31], Funct[4], ID_IR[29:26], Funct[3], ID_IR[24:15], Funct[2:0], ID_IR[11:0]}),
    .EX_IR(EX_IR), .ID_PC(ID_PC), .EX_PC(EX_PC), .jal(ID_Jal), .Jal_2(Jal), .jalr(ID_Jalr), .jalr_2(Jalr),
    .SB(ID_SB), .SB_2(\理想id_ex_1_sb_2 ), .BGEU(ID_BGEU), .BGEU_2(BGEU), .Beq(ID_Beq), .Beq_2(Beq),
    .Bne(ID_Bne), .Bne_2(Bne), .MemToReg(ID_MemToReg), .MemToReg_2(\理想id_ex_1_memtoreg_2 ),
    .MemWrite(ID_MemWrite), .MemWrite_2(\理想id_ex_1_memwrite_2 ), .AluSrcB(AluSrcB),
    .AluSrcB_2(\理想id_ex_1_alusrcb_2 ), .rs1(rs1), .rs1_2(EX_rs1), .rs2(rs2), .rs2_2(\理想id_ex_1_rs2_2 ),
    .immB(bit_extender_3_out), .immB_2(immB), .immJal(bit_extender_4_out), .immJal_2(immJal),
    .\同步清零_气泡_高电平有效 (or_2_out), .CLK(CLK), .\使能端_低电平有效_stall_高电平有效 (halt), .ecall(ID_ecall),
    .ecall_2(EX_ecall), .RegWrite_2(EX_RegWrite), .RegWrite(ID_RegWrite), .AluOP(AluOP),
    .AluOP_2(\理想id_ex_1_aluop_2 ), .imm_2(\理想id_ex_1_imm_2 ), .imm(multiplexer_7_out), .rd_2(EX_RD_num),
    .rd(ID_IR[11:7]));  // open: FwdRs1, FwdRs1_2, FwdRs2, FwdRs2_2
  Pull_Resistor #(.pull(1)) pull_resistor_1 (.node(CLK));
  Multiplexer #(.select(1), .width(32), .disabled("Z"), .enable("false")) multiplexer_8 (
    .in0(\理想id_ex_1_rs2_2 ), .in1(\理想id_ex_1_imm_2 ), .out(multiplexer_8_out), .sel(\理想id_ex_1_alusrcb_2 ));
  Adder #(.width(32)) adder_1 (.a(EX_rs1), .b(\理想id_ex_1_imm_2 ), .out(PCJalr));  // open: cin, cout
  Adder #(.width(32)) adder_2 (.a(IF_PC), .b(32'h4), .out(PC_4));  // open: cin, cout
  Adder #(.width(32)) adder_3 (.a(EX_PC), .b(immB), .out(PCB));  // open: cin, cout
  Adder #(.width(32)) adder_4 (.a(EX_PC), .b(immJal), .out(PCJal));  // open: cin, cout
  Adder #(.width(32)) adder_5 (.a(EX_PC), .b(immB), .out(PCBGEU));  // open: cin, cout
  ALU alu_1 (
    .X(EX_rs1), .Y(multiplexer_8_out), .AluOP(\理想id_ex_1_aluop_2 ), .Equal(equal),
    .Result({alu_1_result, select}), .out_4(begu));  // open: Result_2, out_6
  Multiplexer #(.select(1), .width(32), .disabled("Z"), .enable("false")) multiplexer_9 (
    .in0(\理想id_ex_1_rs2_2 ), .in1(sb_t), .out(multiplexer_9_out), .sel(SB));
  \理想EX_MEM  \u_理想ex_mem_1  (
    .EX_IR(EX_IR), .EX_PC(EX_PC), .jal(Jal), .jalr(Jalr), .SB(\理想id_ex_1_sb_2 ),
    .MemToReg(\理想id_ex_1_memtoreg_2 ), .MemWrite(\理想id_ex_1_memwrite_2 ), .ALU(alu_1_result[11:2]),
    .MDin(multiplexer_9_out), .MEM_IR(MEM_IR), .MEM_PC(M_PC), .Jal_2(\理想ex_mem_1_jal_2 ),
    .jalr_2(\理想ex_mem_1_jalr_2 ), .SB_2(\理想ex_mem_1_sb_2 ), .MemToReg_2(\理想ex_mem_1_memtoreg_2 ),
    .MemWrite_2(MemWrite), .ALU_2(\理想ex_mem_1_alu_2 ), .MDin_2(MDin), .CLK(CLK),
    .\使能端_低电平有效_stall_高电平有效 (halt), .select_4(\理想ex_mem_1_select_4 ), .select_2({alu_1_result, select}),
    .SB1(\理想id_ex_1_rs2_2 [7:0]), .SB1_2(\理想ex_mem_1_sb1_2 ), .RegWrite(EX_RegWrite),
    .RegWrite_2(MEM_RegWrite), .rd(EX_RD_num), .rd_2(MEM_RD_num), .ecall(EX_ecall), .ecall_2(MBM_ecall));  // open: select, rs1, rs2, select_3, rs1_2, rs2_2, 同步清零_气泡_高电平有效
  not not_4 (not_4_out, equal);
  and and_19 (and_19_out, BGEU, begu);
  and and_20 (and_20_out, equal, Beq);
  and and_21 (and_21_out, not_4_out, Bne);
  or or_3 (key, and_20_out, and_21_out);
  or or_4 (Jamp, key, and_19_out, Jalr, Jal);
  RAM #(.addrWidth(10), .dataWidth(32), .bus("separate"), .Select("high")) ram_1 (
    .addr(\理想ex_mem_1_alu_2 ), .din(MDin), .data(ram_1_data), .str(MemWrite), .clk(CLK));  // open: sel, ld, clr
  Multiplexer #(.select(2), .width(32), .disabled("Z"), .enable("false")) multiplexer_10 (
    .in0({SB2[31:8], SB1}), .in1({SB2[31:16], SB1, SB2[7:0]}), .in2({SB2[31:24], SB1, SB2[15:0]}),
    .in3({SB1, SB2[23:0]}), .out(sb_t), .sel(select));
  \理想MEM_WB  \u_理想mem_wb_1  (
    .EX_IR(MEM_IR), .EX_PC(M_PC), .jal(\理想ex_mem_1_jal_2 ), .jalr(\理想ex_mem_1_jalr_2 ),
    .SB(\理想ex_mem_1_sb_2 ), .MemToReg(\理想ex_mem_1_memtoreg_2 ), .ALU(\理想ex_mem_1_select_4 ),
    .MDout(ram_1_data), .MEM_IR(WB_IR), .MEM_PC(WB_PC), .Jal_2(WB_Jal), .jalr_2(WB_Jalr), .SB_2(SB),
    .MemToReg_2(\理想mem_wb_1_memtoreg_2 ), .ALU_2(\理想mem_wb_1_alu_2 ), .MDout_2(SB2), .CLK(CLK),
    .\使能端_低电平有效_stall_高电平有效 (halt), .SB1(\理想ex_mem_1_sb1_2 ), .SB1_2(SB1), .RegWrite_2(RegWrite),
    .RegWrite(MEM_RegWrite), .rd(MEM_RD_num), .rd_2(rd), .ecall(MBM_ecall), .ecall_2(ecall));  // open: select, rs1, rs2, select_2, rs1_2, rs2_2, 同步清零_气泡_高电平有效
  Multiplexer #(.select(1), .width(32), .disabled("Z"), .enable("false")) multiplexer_11 (
    .in0(\理想mem_wb_1_alu_2 ), .in1(SB2), .out(multiplexer_11_out), .sel(\理想mem_wb_1_memtoreg_2 ));
  or or_5 (or_5_out, WB_Jal, WB_Jalr);
  Multiplexer #(.select(1), .width(32), .disabled("Z"), .enable("false")) multiplexer_12 (
    .in0(multiplexer_11_out), .in1(adder_6_out), .out(RDin), .sel(or_5_out));
  Adder #(.width(32)) adder_6 (.a(WB_PC), .b(32'h4), .out(adder_6_out));  // open: cin, cout

  // Other names for the same wires on the sheet: ID_rd[4:0] = ID_IR[11:7]; ID_IR (some bits) = Funct;
  //   OP[4:0] = ID_IR[6:2]; MEM_PC[31:0] = M_PC; PC[31:0] = IF_PC

  // Notes on the sheet:
  //   中断源
  //   时空图监测，可删除
  //   中断等待指示
  //   数码管输出
  //   指令存储器
  //   contents of rom_1 (hex, n*v repeats v):
  //   100493 100006f 100493 200913 300993 100006f 100493 200913 300993 100006f 100493 200913 300993
  //   100006f 100493 200913 300993 29c000ef 100413 100493 1f49493 900533 2200893 73 24d493 48463 fedff06f
  //   900533 2200893 73 100493 249493 900533 2200893 73 48463 fedff06f 100493 1f49493 900533 2200893 73
  //   4034d493 900533 2200893 73 4044d493 900533 2200893 73 4044d493 900533 2200893 73 4044d493 900533
  //   2200893 73 4044d493 900533 2200893 73 4044d493 900533 2200893 73 4044d493 900533 2200893 73 4044d493
  //   900533 2200893 73 100413 1f41993 41f9d993 433 c00913 300b13 140413 f47413 800293 100313 499993
  //   89e9b3 1300533 2200893 73 406282b3 fe0294e3 140413 f00f93 1f47433 1c41413 800293 100313 49d993
  //   89e9b3 1300533 2200893 73 406282b3 fe0294e3 1c45413 406b0b33 b0463 f95ff06f 2b3 fff2c293 829293
  //   ff2e293 500533 2200893 73 fff00413 493 84a023 140413 448493 84a023 140413 448493 84a023 140413
  //   448493 84a023 140413 448493 84a023 140413 448493 84a023 140413 448493 84a023 140413 448493 84a023
  //   140413 448493 84a023 140413 448493 84a023 140413 448493 84a023 140413 448493 84a023 140413 448493
  //   84a023 140413 448493 84a023 140413 448493 84a023 140413 448493 84a023 140413 448493 140413 433
  //   3c00493 42983 4aa03 149a2b3 28663 134a023 1442023 ffc48493 fe9412e3 800533 2200893 73 440413 3c00493
  //   fc9416e3 a00893 73 413 140413 800533 2200893 73 240413 800533 2200893 73 340413 800533 2200893 73
  //   440413 800533 2200893 73 540413 800533 2200893 73 640413 800533 2200893 73 740413 800533 2200893 73
  //   840413 800533 2200893 2200893 73 8067
  //   指令字
  //   Jal
  //   Jalr
  //   SB
  //   BGEU
  //   ecall
  //   I型指令
  //   s型指令
  //   B型指令
  //   Jal
  //   Beq
  //   Bne
  //   MemToReg
  //   MemWrite
  //   AluOP
  //   AluSrcB
  //   RegWrite
  //   S_type
  //   控制位
  //   流水调试日志用
  //   暂停节拍，不能为0
  //   戳工具置1进入计数暂停模式，ctrl+k时钟自动运行到对应节拍暂停
  //   ctrl+k关闭时钟连续运行，将控制位置零，进入单步调试模式调试
  //   可计数暂停的时钟源
  //   为方便自动评测，需要输出流水线各段保存的PC值，注意是PC不是PC+4，另外ID段寄存器写入信息，Mem段内存写入信息也要输出
  //   数据存储器
endmodule
module \重定向流水线  (
  output RegWrite,
  output MemWrite,
  output [31:0] IF_PC,
  output [31:0] ID_PC,
  output [31:0] EX_PC,
  output [31:0] M_PC,
  output [31:0] WB_PC,
  output [31:0] RDin,
  output [31:0] MDin,
  output [31:0] LedData
);

  wire AluSrcB, and_1_out, and_2_out, and_3_out, and_4_out, and_5_out, and_6_out, and_7_out, and_8_out,
       and_9_out, and_10_out, and_11_out, and_12_out, and_13_out, and_14_out, and_15_out, and_16_out,
       and_17_out, and_18_out, and_19_out, and_24_out, and_25_out, and_26_out, and_27_out, and_28_out,
       and_29_out, and_30_out, begu, Beq, BGEU, Bne, CLK, clock_1_out, clock_2_out, comparator_1_eq,
       comparator_2_eq, comparator_3_eq, comparator_4_eq, comparator_5_eq, comparator_6_eq, comparator_6_lt,
       comparator_7_eq, comparator_8_eq, comparator_9_eq, comparator_10_eq, comparator_11_eq,
       comparator_12_eq, comparator_13_eq, comparator_14_eq, d_ff_1_q, ecall, equal, EX_ecall, EX_MemToReg,
       EX_RegWrite, Go, halt, ID_Beq, ID_BGEU, ID_Bne, ID_ecall, ID_Jal, ID_Jalr, ID_MemToReg, ID_MemWrite,
       ID_RegWrite, ID_SB, IR1, IR2, IR3, Jal, Jalr, Jamp, key, LoadUse, MBM_ecall, MEM_RegWrite, nand_1_out,
       not_1_out, not_2_out, not_3_out, not_4_out, not_5_out, not_6_out, not_7_out, not_8_out, not_9_out,
       not_10_out, not_11_out, not_12_out, or_1_out, or_2_out, or_4_out, or_5_out, or_7_out,
       riscv_probe_2_p1, RS1_Used, RS2_Used, RST, SB, W1, W2, W3, WB_Jal, WB_Jalr, \单周期硬布线控制器_1_s_type ,
       \理想ex_mem_1_jal_2 , \理想ex_mem_1_jalr_2 , \理想ex_mem_1_memtoreg_2 , \理想id_ex_1_alusrcb_2 ,
       \理想id_ex_1_memwrite_2 , \理想id_ex_1_sb_2 , \理想mem_wb_1_memtoreg_2 ;
  wire [1:0] EX_FwdRs1, EX_FwdRs2, EX_select, FwdRs1, FwdRs2, select;
  wire [3:0] AluOP, \理想id_ex_1_aluop_2 ;
  wire [4:0] EX_RD_num, Funct, MEM_RD_num, R1_num, R2_num, rd;
  wire [7:0] SB1;
  wire [9:0] \理想ex_mem_1_alu_2 ;
  wire [11:0] shifter_1_out;
  wire [12:0] CNT_num;
  wire [15:0] adder_6_out, \LoadUse次数 , \总周期数 , \插入气泡数 , \插入气泡数1 , \无条件分支数 , \条件分支成功数 ;
  wire [19:0] shifter_2_out;
  wire [31:0] adder_8_out, ALU1Result, ALU2Result, bit_extender_1_out, bit_extender_2_out,
       bit_extender_3_out, bit_extender_4_out, EX_IR, EX_rs1, EX_rs2, ID_IR, IF_IR, immB, immJal, MEM_IR,
       multiplexer_1_out, multiplexer_2_out, multiplexer_3_out, multiplexer_4_out, multiplexer_7_out,
       multiplexer_10_out, multiplexer_13_out, PC_4, PCB, PCBGEU, PCJal, PCJalr, rs1, rs2, SB2, sb_t, WB_IR,
       WB_rs1, WB_rs2, \理想ex_mem_1_mdin_2 , \理想ex_mem_1_rs1_2 , \理想ex_mem_1_rs2_2 , \理想id_ex_1_imm_2 ,
       \理想id_ex_1_rs1_2 , \理想id_ex_1_rs2_2 , \理想mem_wb_1_mdout_2 ;
  wire [31:2] alu_1_result;

  Button \u_总复位  (.out(RST));
  Button _1 (.out(IR1));
  Button _2 (.out(IR2));
  Button _3 (.out(IR3));
  // Probe on \总周期数 
  // Probe on \总周期数 
  Counter #(.width(16), .max('hffff), .ongoal("wrap"), .trigger("rising"), .behavior("old")) counter_1 (
    .Q(\总周期数 ), .clk(and_1_out));  // open: load, D, count, carry, clr, preset
  and and_1 (and_1_out, CLK, not_1_out);
  not not_1 (not_1_out, halt);
  // Probe on multiplexer_1_out
  Button \u_继续运行  (.out(Go));
  LED #(.active("true")) led_1 (.in(W1));
  LED #(.active("true")) led_2 (.in(W2));
  LED #(.active("true")) led_3 (.in(W3));
  Comparator #(.width(32), .mode("twosComplement")) comparator_1 (
    .a(WB_rs1), .b(32'ha), .eq(comparator_1_eq));  // open: gt, lt
  Multiplexer #(.select(1), .width(32), .disabled("Z"), .enable("false")) multiplexer_1 (
    .in0(multiplexer_2_out), .in1(PCJalr), .out(multiplexer_1_out), .sel(Jalr));
  Multiplexer #(.select(1), .width(32), .disabled("Z"), .enable("false")) multiplexer_2 (
    .in0(multiplexer_3_out), .in1(PCJal), .out(multiplexer_2_out), .sel(Jal));
  and and_2 (and_2_out, begu, BGEU);
  Multiplexer #(.select(1), .width(32), .disabled("Z"), .enable("false")) multiplexer_3 (
    .in0(multiplexer_4_out), .in1(PCBGEU), .out(multiplexer_3_out), .sel(and_2_out));
  Multiplexer #(.select(1), .width(32), .disabled("Z"), .enable("false")) multiplexer_4 (
    .in0(PC_4), .in1(PCB), .out(multiplexer_4_out), .sel(key));
  Hex_Digit_Display hex_digit_display_1 (.value(LedData[31:28]));  // open: dp
  // Probe on IF_PC[19:0]
  // RiscV_Probe riscv_probe_1: pin names not known; wires that end beside it: IF_IR
  and and_3 (and_3_out, ecall, comparator_1_eq);
  or or_1 (or_1_out, Jalr, Jal);
  Register #(.width(32), .trigger("rising"), .Select("low")) PC (
    .D(multiplexer_1_out), .en(and_4_out), .Q(IF_PC), .clk(CLK), .clr(RST));
  and and_4 (and_4_out, ~halt, ~LoadUse);  // AND_Gate
  Comparator #(.width(5), .mode("twosComplement")) comparator_2 (
    .a({5{1'b0}}), .b(R1_num), .eq(comparator_2_eq));  // open: gt, lt
  Comparator #(.width(5), .mode("twosComplement")) comparator_3 (
    .a(R1_num), .b(EX_RD_num), .eq(comparator_3_eq));  // open: gt, lt
  Comparator #(.width(5), .mode("twosComplement")) comparator_4 (
    .a(EX_RD_num), .b(R2_num), .eq(comparator_4_eq));  // open: gt, lt
  Comparator #(.width(5), .mode("twosComplement")) comparator_5 (
    .a(R2_num), .b({5{1'b0}}), .eq(comparator_5_eq));  // open: gt, lt
  Hex_Digit_Display hex_digit_display_2 (.value(LedData[27:24]));  // open: dp
  Hex_Digit_Display hex_digit_display_3 (.value(LedData[23:20]));  // open: dp
  // Probe on ID_PC[19:0]
  // RiscV_Probe riscv_probe_2: pin names not known; wires that end beside it: riscv_probe_2_p1, {ID_IR[31], Funct[4], ID_IR[29:26], Funct[3], ID_IR[24:15], Funct[2:0], ID_IR[11:0]}
  xor xor_1 (riscv_probe_2_p1, and_3_out, Go);
  Counter #(.width(16), .max('hffff), .ongoal("wrap"), .trigger("rising"), .behavior("old")) counter_2 (
    .count(or_1_out), .Q(\无条件分支数 ), .clk(and_5_out));  // open: load, D, carry, clr, preset
  and and_5 (and_5_out, CLK, not_2_out);
  not not_2 (not_2_out, halt);
  // Probe on IF_PC
  not not_3 (not_3_out, comparator_2_eq);
  and and_6 (and_6_out, not_3_out, comparator_3_eq);
  and and_7 (and_7_out, comparator_4_eq, not_4_out);
  not not_4 (not_4_out, comparator_5_eq);
  Hex_Digit_Display hex_digit_display_4 (.value(LedData[15:12]));  // open: dp
  Hex_Digit_Display hex_digit_display_5 (.value(LedData[19:16]));  // open: dp
  Register #(.width(1), .trigger("falling"), .Select("low")) PC_2 (
    .D(riscv_probe_2_p1), .en(riscv_probe_2_p1), .Q(halt), .clk(CLK), .clr(Go));
  Counter #(.width(32), .max('hffffffff), .ongoal("wrap"), .trigger("rising"), .behavior("old")) counter_3 (
    .load(ecall), .D(WB_rs2), .count(1'b0), .Q(LedData), .clk(CLK));  // open: carry, clr, preset
  Hex_Digit_Display hex_digit_display_6 (.value(LedData[11:8]));  // open: dp
  Hex_Digit_Display hex_digit_display_7 (.value(LedData[7:4]));  // open: dp
  Clock #(.highDuration(1), .lowDuration(1)) clock_1 (.out(clock_1_out));
  // Probe on EX_PC[19:0]
  // RiscV_Probe riscv_probe_3: pin names not known; wires that end beside it: clock_1_out, EX_IR, CLK
  ROM #(.addrWidth(10), .dataWidth(32), .Select("high")) rom_1 (.addr(IF_PC[11:2]), .data(IF_IR));
  and and_8 (and_8_out, and_6_out, RS1_Used);
  and and_9 (and_9_out, and_7_out, RS2_Used);
  Hex_Digit_Display hex_digit_display_8 (.value(LedData[3:0]));  // open: dp
  \理想IF_ID  \u_理想if_id_1  (
    .IF_PC(IF_PC), .IF_IR(IF_IR), .ID_PC(ID_PC),
    .ID_IR({ID_IR[31], Funct[4], ID_IR[29:26], Funct[3], ID_IR[24:15], Funct[2:0], ID_IR[11:0]}),
    .\同步清零_高电平有效 (Jamp), .CLK(CLK), .\使能端_低电平有效_stall_高电平有效 (or_2_out));
  or or_2 (or_2_out, halt, LoadUse);
  and and_10 (and_10_out, and_8_out, EX_MemToReg);
  and and_11 (and_11_out, and_9_out, EX_MemToReg);
  // Probe on \总周期数 
  // Probe on M_PC[19:0]
  // RiscV_Probe riscv_probe_4: pin names not known; wires that end beside it: MEM_IR
  // Probe on {ID_IR[31], Funct[4], ID_IR[29:26], Funct[3], ID_IR[24:15], Funct[2:0], ID_IR[11:0]}
  or or_3 (LoadUse, and_10_out, and_11_out);
  // Probe on \总周期数 
  // Probe on \无条件分支数 
  // Probe on \条件分支成功数 
  // Probe on \插入气泡数 
  // Probe on \LoadUse次数 
  // Probe on \总周期数 
  // Probe on IF_PC[11:0]
  // Probe on WB_PC[19:0]
  // RiscV_Probe riscv_probe_5: pin names not known; wires that end beside it: WB_IR
  rs_used rs_used_1 (
    .OP2(ID_IR[2]), .OP3(ID_IR[3]), .OP4(ID_IR[4]), .OP5(ID_IR[5]), .OP6(ID_IR[6]), .F12(Funct[0]),
    .F13(Funct[1]), .F14(Funct[2]), .F25(Funct[3]), .F30(Funct[4]), .rs1_used(RS1_Used), .rs2_used(RS2_Used));
  \单周期硬布线控制器  \u_单周期硬布线控制器_1  (
    .Funct(Funct), .OP(ID_IR[6:2]), .ALU_OP(AluOP), .MemToReg(ID_MemToReg), .MemWrite(ID_MemWrite),
    .ALU_SRC(AluSrcB), .RegWrite(ID_RegWrite), .ecall(ID_ecall), .S_type(\单周期硬布线控制器_1_s_type ),
    .Jalr(ID_Jalr), .Beq(ID_Beq), .JAL(ID_Jal), .Bne(ID_Bne), .SB(ID_SB), .BGEU(ID_BGEU));  // open: CSRRSI, CSRRCI
  Multiplexer #(.select(1), .width(5), .disabled("Z"), .enable("false")) multiplexer_5 (
    .in0(ID_IR[19:15]), .in1(5'b10001), .out(R1_num), .sel(ID_ecall));
  Multiplexer #(.select(1), .width(5), .disabled("Z"), .enable("false")) multiplexer_6 (
    .in0(ID_IR[24:20]), .in1(5'b01010), .out(R2_num), .sel(ID_ecall));
  assign bit_extender_1_out = {{20{ID_IR[31]}}, {ID_IR[31], Funct[4], ID_IR[29:26], Funct[3], ID_IR[24:20]}};  // Bit_Extender bit_extender_1
  assign bit_extender_2_out = {{20{ID_IR[31]}}, {ID_IR[31], Funct[4], ID_IR[29:26], Funct[3], ID_IR[11:7]}};  // Bit_Extender bit_extender_2
  Shifter #(.width(12), .shift("ll")) shifter_1 (
    .in({ID_IR[31], ID_IR[7], Funct[4], ID_IR[29:26], Funct[3], ID_IR[11:8]}), .\dist (4'b0001),
    .out(shifter_1_out));
  Shifter #(.width(20), .shift("ll")) shifter_2 (
    .in({ID_IR[31], ID_IR[19:15], Funct[2:0], ID_IR[20], Funct[4], ID_IR[29:26], Funct[3], ID_IR[24:21]}),
    .\dist (5'b00001), .out(shifter_2_out));
  // Probe on \总周期数 
  // Probe on ID_PC[11:0]
  // Probe on EX_PC[11:0]
  Multiplexer #(.select(1), .width(32), .disabled("Z"), .enable("false")) multiplexer_7 (
    .in0(bit_extender_1_out), .in1(bit_extender_2_out), .out(multiplexer_7_out), .sel(\单周期硬布线控制器_1_s_type ));
  assign bit_extender_3_out = {{20{shifter_1_out[11]}}, shifter_1_out};  // Bit_Extender bit_extender_3
  assign bit_extender_4_out = {{12{shifter_2_out[19]}}, shifter_2_out};  // Bit_Extender bit_extender_4
  // Probe on M_PC[11:0]
  D_Flip_Flop #(.trigger("high"), .Pre_Clr_Positions("LEGACY"), .NegatePresetClear("false"), .enable("true"), .NewFFLayout("false")) d_ff_1 (.Q(d_ff_1_q));  // open: clk, D, Qn, preset, en, reset
  // Probe on 13'h8f2
  // Probe on WB_PC[11:0]
  Comparator #(.width(13), .mode("twosComplement")) comparator_6 (
    .a(CNT_num), .b(13'h8f2), .eq(comparator_6_eq), .lt(comparator_6_lt));  // open: gt
  Clock #(.highDuration(1), .lowDuration(1)) clock_2 (.out(clock_2_out));
  or or_4 (or_4_out, Jamp, LoadUse);
  Regifile regifile_1 (
    .Din(RDin), .Clk(CLK), .R1(rs1), .R2(rs2), .WE(RegWrite), .W_num(rd), .R1_num(R1_num), .R2_num(R2_num));
  not not_5 (not_5_out, comparator_7_eq);
  Comparator #(.width(5), .mode("twosComplement")) comparator_7 (
    .a({5{1'b0}}), .b(R1_num), .eq(comparator_7_eq));  // open: gt, lt
  Comparator #(.width(5), .mode("twosComplement")) comparator_8 (
    .a(R1_num), .b(EX_RD_num), .eq(comparator_8_eq));  // open: gt, lt
  Comparator #(.width(5), .mode("twosComplement")) comparator_9 (
    .a({5{1'b0}}), .b(R1_num), .eq(comparator_9_eq));  // open: gt, lt
  not not_6 (not_6_out, comparator_9_eq);
  Comparator #(.width(5), .mode("twosComplement")) comparator_10 (
    .a(R1_num), .b(MEM_RD_num), .eq(comparator_10_eq));  // open: gt, lt
  not not_7 (not_7_out, comparator_11_eq);
  Comparator #(.width(5), .mode("twosComplement")) comparator_11 (
    .a({5{1'b0}}), .b(R2_num), .eq(comparator_11_eq));  // open: gt, lt
  Comparator #(.width(5), .mode("twosComplement")) comparator_12 (
    .a(R2_num), .b(EX_RD_num), .eq(comparator_12_eq));  // open: gt, lt
  not not_8 (not_8_out, comparator_13_eq);
  Comparator #(.width(5), .mode("twosComplement")) comparator_13 (
    .a({5{1'b0}}), .b(R2_num), .eq(comparator_13_eq));  // open: gt, lt
  Comparator #(.width(5), .mode("twosComplement")) comparator_14 (
    .a(R2_num), .b(MEM_RD_num), .eq(comparator_14_eq));  // open: gt, lt
  nand nand_1 (nand_1_out, d_ff_1_q, comparator_6_eq);
  Counter #(.width(13), .max('h1fff), .ongoal("stay"), .trigger("rising"), .behavior("old")) counter_4 (
    .count(comparator_6_lt), .Q(CNT_num), .clk(clock_2_out));  // open: load, D, carry, clr, preset
  // Probe on rs2
  and and_12 (and_12_out, not_5_out, comparator_8_eq);
  and and_13 (and_13_out, not_6_out, comparator_10_eq);
  and and_14 (and_14_out, not_7_out, comparator_12_eq);
  and and_15 (and_15_out, not_8_out, comparator_14_eq);
  assign CLK = nand_1_out ? clock_2_out : 1'bz;  // Controlled_Buffer controlled_buffer_1
  \理想ID_EX  \u_理想id_ex_1  (
    .ID_IR({ID_IR[31], Funct[4], ID_IR[29:26], Funct[3], ID_IR[24:15], Funct[2:0], ID_IR[11:0]}),
    .EX_IR(EX_IR), .ID_PC(ID_PC), .EX_PC(EX_PC), .jal(ID_Jal), .Jal_2(Jal), .jalr(ID_Jalr), .jalr_2(Jalr),
    .SB(ID_SB), .SB_2(\理想id_ex_1_sb_2 ), .BGEU(ID_BGEU), .BGEU_2(BGEU), .Beq(ID_Beq), .Beq_2(Beq),
    .Bne(ID_Bne), .Bne_2(Bne), .MemToReg(ID_MemToReg), .MemToReg_2(EX_MemToReg), .MemWrite(ID_MemWrite),
    .MemWrite_2(\理想id_ex_1_memwrite_2 ), .AluSrcB(AluSrcB), .AluSrcB_2(\理想id_ex_1_alusrcb_2 ), .rs1(rs1),
    .rs1_2(\理想id_ex_1_rs1_2 ), .rs2(rs2), .rs2_2(\理想id_ex_1_rs2_2 ), .immB(bit_extender_3_out),
    .immB_2(immB), .immJal(bit_extender_4_out), .immJal_2(immJal), .\同步清零_气泡_高电平有效 (or_4_out), .CLK(CLK),
    .\使能端_低电平有效_stall_高电平有效 (halt), .ecall(ID_ecall), .ecall_2(EX_ecall), .RegWrite_2(EX_RegWrite),
    .RegWrite(ID_RegWrite), .AluOP(AluOP), .AluOP_2(\理想id_ex_1_aluop_2 ), .imm_2(\理想id_ex_1_imm_2 ),
    .imm(multiplexer_7_out), .rd_2(EX_RD_num), .rd(ID_IR[11:7]), .FwdRs1(FwdRs1), .FwdRs1_2(EX_FwdRs1),
    .FwdRs2(FwdRs2), .FwdRs2_2(EX_FwdRs2));
  and and_16 (and_16_out, and_12_out, EX_RegWrite);
  and and_17 (and_17_out, and_13_out, MEM_RegWrite);
  and and_18 (and_18_out, and_14_out, EX_RegWrite);
  and and_19 (and_19_out, and_15_out, MEM_RegWrite);
  Pull_Resistor #(.pull(1)) pull_resistor_1 (.node(CLK));
  and and_20 (FwdRs1[0], and_16_out, RS1_Used);
  and and_21 (FwdRs1[1], and_17_out, RS1_Used);
  and and_22 (FwdRs2[0], and_18_out, RS2_Used);
  and and_23 (FwdRs2[1], and_19_out, RS2_Used);
  and and_24 (and_24_out, BGEU, begu);
  and and_25 (and_25_out, BGEU, begu);
  Multiplexer #(.select(2), .width(32), .disabled("Z"), .enable("false")) multiplexer_8 (
    .in0(\理想id_ex_1_rs2_2 ), .in1(ALU1Result), .in2(RDin), .in3(ALU1Result), .out(EX_rs2), .sel(EX_FwdRs2));
  Adder #(.width(32)) adder_1 (.a(EX_rs1), .b(\理想id_ex_1_imm_2 ), .out(PCJalr));  // open: cin, cout
  Adder #(.width(32)) adder_2 (.a(IF_PC), .b(32'h4), .out(PC_4));  // open: cin, cout
  Adder #(.width(32)) adder_3 (.a(EX_PC), .b(immB), .out(PCB));  // open: cin, cout
  Adder #(.width(32)) adder_4 (.a(EX_PC), .b(immJal), .out(PCJal));  // open: cin, cout
  Adder #(.width(32)) adder_5 (.a(EX_PC), .b(immB), .out(PCBGEU));  // open: cin, cout
  or or_5 (or_5_out, and_24_out, key);
  and and_26 (and_26_out, CLK, not_9_out);
  or or_6 (Jamp, key, and_25_out, Jalr, Jal);
  Counter #(.width(16), .max('hffff), .ongoal("wrap"), .trigger("rising"), .behavior("old")) counter_5 (
    .count(or_5_out), .Q(\条件分支成功数 ), .clk(and_26_out));  // open: load, D, carry, clr, preset
  not not_9 (not_9_out, halt);
  Multiplexer #(.select(2), .width(32), .disabled("Z"), .enable("false")) multiplexer_9 (
    .in0(\理想id_ex_1_rs1_2 ), .in1(ALU1Result), .in2(RDin), .in3(ALU1Result), .out(EX_rs1), .sel(EX_FwdRs1));
  Multiplexer #(.select(1), .width(32), .disabled("Z"), .enable("false")) multiplexer_10 (
    .in0(EX_rs2), .in1(\理想id_ex_1_imm_2 ), .out(multiplexer_10_out), .sel(\理想id_ex_1_alusrcb_2 ));
  ALU alu_1 (
    .X(EX_rs1), .Y(multiplexer_10_out), .AluOP(\理想id_ex_1_aluop_2 ), .Equal(equal),
    .Result({alu_1_result, EX_select}), .out_4(begu));  // open: Result_2, out_6
  Counter #(.width(16), .max('hffff), .ongoal("wrap"), .trigger("rising"), .behavior("old")) counter_6 (
    .count(LoadUse), .Q(\LoadUse次数 ), .clk(and_27_out));  // open: load, D, carry, clr, preset
  and and_27 (and_27_out, CLK, not_10_out);
  not not_10 (not_10_out, halt);
  \理想EX_MEM  \u_理想ex_mem_1  (
    .EX_IR(EX_IR), .EX_PC(EX_PC), .jal(Jal), .jalr(Jalr), .SB(\理想id_ex_1_sb_2 ), .select(EX_select),
    .rs1(EX_rs1), .rs2(EX_rs2), .MemToReg(EX_MemToReg), .MemWrite(\理想id_ex_1_memwrite_2 ),
    .ALU(alu_1_result[11:2]), .MDin(EX_rs2), .MEM_IR(MEM_IR), .MEM_PC(M_PC), .Jal_2(\理想ex_mem_1_jal_2 ),
    .jalr_2(\理想ex_mem_1_jalr_2 ), .SB_2(SB), .select_3(select), .rs1_2(\理想ex_mem_1_rs1_2 ),
    .rs2_2(\理想ex_mem_1_rs2_2 ), .MemToReg_2(\理想ex_mem_1_memtoreg_2 ), .MemWrite_2(MemWrite),
    .ALU_2(\理想ex_mem_1_alu_2 ), .MDin_2(\理想ex_mem_1_mdin_2 ), .CLK(CLK), .\使能端_低电平有效_stall_高电平有效 (halt),
    .select_4(ALU1Result), .select_2({alu_1_result, EX_select}), .SB1(EX_rs2[7:0]), .SB1_2(SB1),
    .RegWrite(EX_RegWrite), .RegWrite_2(MEM_RegWrite), .rd(EX_RD_num), .rd_2(MEM_RD_num), .ecall(EX_ecall),
    .ecall_2(MBM_ecall));  // open: 同步清零_气泡_高电平有效
  Multiplexer #(.select(1), .width(32), .disabled("Z"), .enable("false")) multiplexer_11 (
    .in0(\理想ex_mem_1_mdin_2 ), .in1(sb_t), .out(MDin), .sel(SB));
  Counter #(.width(16), .max('hffff), .ongoal("wrap"), .trigger("rising"), .behavior("old")) counter_7 (
    .count(Jamp), .Q(\插入气泡数1 ), .clk(and_28_out));  // open: load, D, carry, clr, preset
  and and_28 (and_28_out, CLK, not_11_out);
  not not_11 (not_11_out, halt);
  RAM #(.addrWidth(10), .dataWidth(32), .bus("separate"), .Select("high")) ram_1 (
    .addr(\理想ex_mem_1_alu_2 ), .din(MDin), .data(SB2), .str(MemWrite), .clk(CLK));  // open: sel, ld, clr
  Adder #(.width(16)) adder_6 (.a(\插入气泡数1 ), .b(\插入气泡数1 ), .out(adder_6_out));  // open: cin, cout
  Multiplexer #(.select(2), .width(32), .disabled("Z"), .enable("false")) multiplexer_12 (
    .in0({SB2[31:8], SB1}), .in1({SB2[31:16], SB1, SB2[7:0]}), .in2({SB2[31:24], SB1, SB2[15:0]}),
    .in3({SB1, SB2[23:0]}), .out(sb_t), .sel(select));
  Adder #(.width(16)) adder_7 (.a(adder_6_out), .b(\LoadUse次数 ), .out(\插入气泡数 ));  // open: cin, cout
  \理想MEM_WB  \u_理想mem_wb_1  (
    .EX_IR(MEM_IR), .EX_PC(M_PC), .jal(\理想ex_mem_1_jal_2 ), .jalr(\理想ex_mem_1_jalr_2 ),
    .rs1(\理想ex_mem_1_rs1_2 ), .rs2(\理想ex_mem_1_rs2_2 ), .MemToReg(\理想ex_mem_1_memtoreg_2 ), .ALU(ALU1Result),
    .MDout(SB2), .MEM_IR(WB_IR), .MEM_PC(WB_PC), .Jal_2(WB_Jal), .jalr_2(WB_Jalr), .rs1_2(WB_rs1),
    .rs2_2(WB_rs2), .MemToReg_2(\理想mem_wb_1_memtoreg_2 ), .ALU_2(ALU2Result), .MDout_2(\理想mem_wb_1_mdout_2 ),
    .CLK(CLK), .\使能端_低电平有效_stall_高电平有效 (halt), .RegWrite_2(RegWrite), .RegWrite(MEM_RegWrite),
    .rd(MEM_RD_num), .rd_2(rd), .ecall(MBM_ecall), .ecall_2(ecall));  // open: SB, select, SB_2, select_2, 同步清零_气泡_高电平有效, SB1, SB1_2
  Multiplexer #(.select(1), .width(32), .disabled("Z"), .enable("false")) multiplexer_13 (
    .in0(ALU2Result), .in1(\理想mem_wb_1_mdout_2 ), .out(multiplexer_13_out), .sel(\理想mem_wb_1_memtoreg_2 ));
  or or_7 (or_7_out, WB_Jal, WB_Jalr);
  Multiplexer #(.select(1), .width(32), .disabled("Z"), .enable("false")) multiplexer_14 (
    .in0(multiplexer_13_out), .in1(adder_8_out), .out(RDin), .sel(or_7_out));
  Adder #(.width(32)) adder_8 (.a(WB_PC), .b(32'h4), .out(adder_8_out));  // open: cin, cout
  not not_12 (not_12_out, equal);
  and and_29 (and_29_out, equal, Beq);
  and and_30 (and_30_out, not_12_out, Bne);
  or or_8 (key, and_29_out, and_30_out);

  // Other names for the same wires on the sheet: ID_rd[4:0] = ID_IR[11:7]; ID_IR (some bits) = Funct;
  //   OP[4:0] = ID_IR[6:2]; MEM_PC[31:0] = M_PC; PC[31:0] = IF_PC

  // Notes on the sheet:
  //   中断源
  //   时空图监测，可删除
  //   中断等待指示
  //   数码管输出
  //   指令存储器
  //   contents of rom_1 (hex, n*v repeats v):
  //   100493 100006f 100493 200913 300993 100006f 100493 200913 300993 100006f 100493 200913 300993
  //   100006f 100493 200913 300993 3b4000ef 100413 100493 1f49493 900533 2200893 73 24d493 48463 fedff06f
  //   900533 2200893 73 100493 249493 900533 2200893 73 48463 fedff06f 100493 1f49493 900533 2200893 73
  //   4034d493 900533 2200893 73 4044d493 900533 2200893 73 4044d493 900533 2200893 73 4044d493 900533
  //   2200893 73 4044d493 900533 2200893 73 4044d493 900533 2200893 73 4044d493 900533 2200893 73 4044d493
  //   900533 2200893 73 100413 1f41993 41f9d993 433 c00913 300b13 140413 f47413 800293 100313 499993
  //   89e9b3 1300533 2200893 73 406282b3 fe0294e3 140413 f00f93 1f47433 1c41413 800293 100313 49d993
  //   89e9b3 1300533 2200893 73 406282b3 fe0294e3 1c45413 406b0b33 b0463 f95ff06f 2b3 fff2c293 829293
  //   ff2e293 500533 2200893 73 fff00413 493 84a023 140413 448493 84a023 140413 448493 84a023 140413
  //   448493 84a023 140413 448493 84a023 140413 448493 84a023 140413 448493 84a023 140413 448493 84a023
  //   140413 448493 84a023 140413 448493 84a023 140413 448493 84a023 140413 448493 84a023 140413 448493
  //   84a023 140413 448493 84a023 140413 448493 84a023 140413 448493 84a023 140413 448493 140413 433
  //   3c00493 42983 4aa03 149a2b3 28663 134a023 1442023 ffc48493 fe9412e3 800533 2200893 73 440413 3c00493
  //   fc9416e3 a00893 73 100293 300313 800493 849493 7648493 1449493 900533 2200893 73 800e13 4054d4b3
  //   4064d4b3 900533 2200893 73 fffe0e13 fe0e14e3 a00893 73 fff00293 7700493 849493 7748493 900533
  //   2200893 73 1000e13 54c4b3 900533 2200893 73 fffe0e13 fe0e16e3 a00893 73 313 2000e13 493 100913
  //   930023 900533 2200893 73 12484b3 130313 fffe0e13 fe0e12e3 800e13 313 32483 900533 2200893 73 430313
  //   fffe0e13 fe0e14e3 a00893 73 f00493 100913 409909b3 900533 2200893 73 fff48493 ff29f6e3 a00893 73
  //   a00893 73 413 140413 800533 2200893 73 240413 800533 2200893 73 340413 800533 2200893 73 440413
  //   800533 2200893 73 540413 800533 2200893 73 640413 800533 2200893 73 740413 800533 2200893 73 840413
  //   800533 2200893 2200893 73 8067
  //   指令字
  //   Jal
  //   Jalr
  //   SB
  //   BGEU
  //   ecall
  //   I型指令
  //   s型指令
  //   B型指令
  //   Jal
  //   Beq
  //   Bne
  //   MemToReg
  //   MemWrite
  //   AluOP
  //   AluSrcB
  //   RegWrite
  //   S_type
  //   控制位
  //   流水调试日志用
  //   暂停节拍，不能为0
  //   戳工具置1进入计数暂停模式，ctrl+k时钟自动运行到对应节拍暂停
  //   ctrl+k关闭时钟连续运行，将控制位置零，进入单步调试模式调试
  //   可计数暂停的时钟源
  //   为方便自动评测，需要输出流水线各段保存的PC值，注意是PC不是PC+4，另外ID段寄存器写入信息，Mem段内存写入信息也要输出
  //   数据存储器
endmodule

module \中断按键参考电路  (
  input  \同步清零信号 ,
  output \与中断屏蔽位与 
);

  wire \_1号中断_out , and_1_out, clock_1_out, d_ff_1_q, or_1_out, or_2_out;

  Clock #(.highDuration(1), .lowDuration(1)) clock_1 (.out(clock_1_out));
  Button \_1号中断  (.out(\_1号中断_out ));
  or or_1 (or_1_out, \与中断屏蔽位与 , d_ff_1_q);
  LED #(.active("true")) \_1号中断等待指示灯  (.in(or_1_out));
  D_Flip_Flop #(.trigger("rising"), .Pre_Clr_Positions("LEGACY"), .NegatePresetClear("false"), .enable("true"), .NewFFLayout("false")) d_ff_1 (
    .clk(\_1号中断_out ), .D(1'b1), .Q(d_ff_1_q), .reset(\与中断屏蔽位与 ));  // open: Qn, preset, en
  or or_2 (or_2_out, d_ff_1_q, \与中断屏蔽位与 );
  and and_1 (and_1_out, or_2_out, ~\同步清零信号 );  // AND_Gate
  D_Flip_Flop #(.trigger("rising"), .Pre_Clr_Positions("LEGACY"), .NegatePresetClear("false"), .enable("true"), .NewFFLayout("false")) IR1 (
    .clk(clock_1_out), .D(and_1_out), .Q(\与中断屏蔽位与 ));  // open: Qn, preset, en, reset

  // Notes on the sheet:
  //   中断信号采样参考电路
  //   Reset 
endmodule

module \单周期_单级中断  (
  input  IR1,
  input  IR2,
  input  IR3,
  output RegWrite,
  output MemWrite,
  output [31:0] PC,
  output [31:0] IR,
  output [31:0] RDin,
  output [31:0] MDin,
  output [31:0] LedData
);

  wire and_1_out, and_2_out, and_3_out, and_6_out, and_7_out, and_8_out, and_9_out, and_10_out, and_11_out,
       begu, BGEU, Cl1, Cl2, Cl3, CLK, comparator_1_eq, comparator_2_eq, comparator_3_eq, comparator_4_eq,
       comparator_5_eq, d_ff_1_q, d_ff_2_q, d_ff_3_q, ecall, ecall_num, equal, Go, halt, IE, INT, INTto,
       IR1_2_q, IR1_3_q, IR1_q, IR1_t, IR2_t, IR3_t, IRA, IRB, IRC, Jal, Jalr, key, not_1_out, not_2_out,
       not_3_out, not_4_out, not_5_out, not_6_out, not_7_out, or_1_out, or_7_out, or_8_out, or_9_out,
       or_12_out, RST, SB, URET, W1, W2, W3, xor_1_out, \单周期硬布线控制器_1_alu_src , \单周期硬布线控制器_1_beq ,
       \单周期硬布线控制器_1_bne , \单周期硬布线控制器_1_memtoreg , \单周期硬布线控制器_1_s_type ;
  wire [1:0] priority_encoder_1_out, select, \锁存当前中断号_q ;
  wire [3:0] \单周期硬布线控制器_1_alu_op ;
  wire [4:0] multiplexer_7_out, multiplexer_8_out;
  wire [11:0] shifter_1_out;
  wire [15:0] \总周期数 ;
  wire [19:0] shifter_2_out;
  wire [31:0] bit_extender_1_out, bit_extender_2_out, imm, immB, immJal, INT_PC, multiplexer_2_out,
       multiplexer_3_out, multiplexer_4_out, multiplexer_5_out, multiplexer_6_out, multiplexer_10_out, PC_4,
       PCB, PCBGEU, PCJal, PCJalr, Ret_addr, Ret_PC, rs1, rs2, SB2, sb_t;
  wire [31:2] alu_1_result;

  Clock #(.highDuration(1), .lowDuration(1)) clock_1 (.out(CLK));
  Button _1 ();  // open: out
  Button _2 ();  // open: out
  Button _3 ();  // open: out
  Counter #(.width(16), .max('hffff), .ongoal("wrap"), .trigger("rising"), .behavior("old")) counter_1 (
    .Q(\总周期数 ), .clk(and_1_out));  // open: load, D, count, carry, clr, preset
  and and_1 (and_1_out, CLK, not_1_out);
  not not_1 (not_1_out, halt);
  Button \u_继续运行  (.out(Go));
  LED #(.active("true")) led_1 (.in(W1));
  LED #(.active("true")) led_2 (.in(W2));
  LED #(.active("true")) led_3 (.in(W3));
  Multiplexer #(.select(1), .width(32), .disabled("Z"), .enable("false")) multiplexer_1 (
    .in0(multiplexer_2_out), .in1(PCJalr), .out(Ret_addr), .sel(Jalr));
  Multiplexer #(.select(1), .width(32), .disabled("Z"), .enable("false")) multiplexer_2 (
    .in0(multiplexer_3_out), .in1(PCJal), .out(multiplexer_2_out), .sel(Jal));
  and and_2 (and_2_out, begu, BGEU);
  Multiplexer #(.select(1), .width(32), .disabled("Z"), .enable("false")) multiplexer_3 (
    .in0(multiplexer_4_out), .in1(PCBGEU), .out(multiplexer_3_out), .sel(and_2_out));
  Multiplexer #(.select(1), .width(32), .disabled("Z"), .enable("false")) multiplexer_4 (
    .in0(PC_4), .in1(PCB), .out(multiplexer_4_out), .sel(key));
  Hex_Digit_Display hex_digit_display_1 (.value(LedData[31:28]));  // open: dp
  Comparator #(.width(32), .mode("twosComplement")) comparator_1 (
    .a(rs1), .b(32'ha), .eq(comparator_1_eq));  // open: gt, lt
  Multiplexer #(.select(1), .width(32), .disabled("Z"), .enable("false")) multiplexer_5 (
    .in0(Ret_addr), .in1(INT_PC), .out(multiplexer_5_out), .sel(INT));
  Comparator #(.width(16), .mode("twosComplement")) comparator_2 (
    .a(16'h23b), .b(\总周期数 ), .eq(comparator_2_eq));  // open: gt, lt
  Comparator #(.width(16), .mode("twosComplement")) comparator_3 (
    .a(\总周期数 ), .b(16'h1), .eq(comparator_3_eq));  // open: gt, lt
  Comparator #(.width(16), .mode("twosComplement")) comparator_4 (
    .a(\总周期数 ), .b(16'h4), .eq(comparator_4_eq));  // open: gt, lt
  Comparator #(.width(16), .mode("twosComplement")) comparator_5 (
    .a(\总周期数 ), .b(16'h7), .eq(comparator_5_eq));  // open: gt, lt
  Hex_Digit_Display hex_digit_display_2 (.value(LedData[27:24]));  // open: dp
  Hex_Digit_Display hex_digit_display_3 (.value(LedData[23:20]));  // open: dp
  and and_3 (and_3_out, ecall, comparator_1_eq);
  Multiplexer #(.select(1), .width(32), .disabled("Z"), .enable("false")) multiplexer_6 (
    .in0(multiplexer_5_out), .in1(Ret_PC), .out(multiplexer_6_out), .sel(URET));
  not not_2 (not_2_out, halt);
  or or_1 (or_1_out, comparator_2_eq, comparator_3_eq);
  assign IRA = or_1_out ? ~CLK : 1'bz;  // Controlled_Inverter controlled_inverter_1
  assign IRB = comparator_4_eq ? ~CLK : 1'bz;  // Controlled_Inverter controlled_inverter_2
  assign IRC = comparator_5_eq ? ~CLK : 1'bz;  // Controlled_Inverter controlled_inverter_3
  Hex_Digit_Display hex_digit_display_4 (.value(LedData[15:12]));  // open: dp
  Hex_Digit_Display hex_digit_display_5 (.value(LedData[19:16]));  // open: dp
  xor xor_1 (xor_1_out, and_3_out, Go);
  Register #(.width(32), .trigger("rising"), .Select("low")) u_PC (
    .D(multiplexer_6_out), .en(not_2_out), .Q(PC), .clk(CLK), .clr(RST));
  Pull_Resistor #(.pull(0)) pull_resistor_1 (.node(IRA));
  Pull_Resistor #(.pull(0)) pull_resistor_2 (.node(IRB));
  Pull_Resistor #(.pull(0)) pull_resistor_3 (.node(IRC));
  Hex_Digit_Display hex_digit_display_6 (.value(LedData[7:4]));  // open: dp
  Hex_Digit_Display hex_digit_display_7 (.value(LedData[11:8]));  // open: dp
  // Probe on \总周期数 
  // Probe on \总周期数 
  Register #(.width(1), .trigger("falling"), .Select("low")) PC_2 (
    .D(xor_1_out), .en(xor_1_out), .Q(halt), .clk(CLK), .clr(Go));
  Counter #(.width(32), .max('hffffffff), .ongoal("wrap"), .trigger("rising"), .behavior("old")) counter_2 (
    .load(ecall), .D(rs2), .count(1'b0), .Q(LedData), .clk(CLK));  // open: carry, clr, preset
  // RiscV_Probe riscv_probe_1: pin names not known; wires that end beside it: IR
  Hex_Digit_Display hex_digit_display_8 (.value(LedData[3:0]));  // open: dp
  ROM #(.addrWidth(10), .dataWidth(32), .Select("high")) rom_1 (.addr(PC[11:2]), .data(IR));
  // Probe on IR
  or or_2 (W1, IR1_2_q, d_ff_2_q);
  D_Flip_Flop #(.trigger("rising"), .Pre_Clr_Positions("LEGACY"), .NegatePresetClear("false"), .enable("true"), .NewFFLayout("false")) d_ff_1 (
    .clk(IR2_t), .D(1'b1), .Q(d_ff_1_q), .reset(IR1_q));  // open: Qn, preset, en
  or or_3 (W2, IR1_q, d_ff_1_q);
  or or_4 (W3, IR1_3_q, d_ff_3_q);
  or or_5 (IR1_t, IR1, IRA);
  \单周期硬布线控制器  \u_单周期硬布线控制器_1  (
    .Funct({IR[30], IR[25], IR[14:12]}), .OP(IR[6:2]), .ALU_OP(\单周期硬布线控制器_1_alu_op ),
    .MemToReg(\单周期硬布线控制器_1_memtoreg ), .MemWrite(MemWrite), .ALU_SRC(\单周期硬布线控制器_1_alu_src ),
    .RegWrite(RegWrite), .ecall(ecall_num), .S_type(\单周期硬布线控制器_1_s_type ), .Jalr(Jalr),
    .Beq(\单周期硬布线控制器_1_beq ), .JAL(Jal), .Bne(\单周期硬布线控制器_1_bne ), .SB(SB), .BGEU(BGEU));  // open: CSRRSI, CSRRCI
  Multiplexer #(.select(1), .width(5), .disabled("Z"), .enable("false")) multiplexer_7 (
    .in0(IR[19:15]), .in1(5'b10001), .out(multiplexer_7_out), .sel(ecall));
  Multiplexer #(.select(1), .width(5), .disabled("Z"), .enable("false")) multiplexer_8 (
    .in0(IR[24:20]), .in1(5'b01010), .out(multiplexer_8_out), .sel(ecall));
  assign bit_extender_1_out = {{20{IR[31]}}, IR[31:20]};  // Bit_Extender bit_extender_1
  assign bit_extender_2_out = {{20{IR[31]}}, {IR[31:25], IR[11:7]}};  // Bit_Extender bit_extender_2
  Shifter #(.width(12), .shift("ll")) shifter_1 (
    .in({IR[31], IR[7], IR[30:25], IR[11:8]}), .\dist (4'b0001), .out(shifter_1_out));
  and and_4 (URET, ecall_num, IR[21]);
  not not_3 (not_3_out, IR[21]);
  Shifter #(.width(20), .shift("ll")) shifter_2 (
    .in({IR[31], IR[19:12], IR[20], IR[30:21]}), .\dist (5'b00001), .out(shifter_2_out));
  D_Flip_Flop #(.trigger("rising"), .Pre_Clr_Positions("LEGACY"), .NegatePresetClear("false"), .enable("true"), .NewFFLayout("false")) d_ff_2 (
    .clk(IR1_t), .D(1'b1), .Q(d_ff_2_q), .reset(IR1_2_q));  // open: Qn, preset, en
  D_Flip_Flop #(.trigger("rising"), .Pre_Clr_Positions("LEGACY"), .NegatePresetClear("false"), .enable("true"), .NewFFLayout("false")) d_ff_3 (
    .clk(IR3_t), .D(1'b1), .Q(d_ff_3_q), .reset(IR1_3_q));  // open: Qn, preset, en
  or or_6 (IR2_t, IR2, IRB);
  Multiplexer #(.select(1), .width(32), .disabled("Z"), .enable("false")) multiplexer_9 (
    .in0(bit_extender_1_out), .in1(bit_extender_2_out), .out(imm), .sel(\单周期硬布线控制器_1_s_type ));
  assign immB = {{20{shifter_1_out[11]}}, shifter_1_out};  // Bit_Extender bit_extender_3
  and and_5 (ecall, ecall_num, not_3_out);
  assign immJal = {{12{shifter_2_out[19]}}, shifter_2_out};  // Bit_Extender bit_extender_4
  or or_7 (or_7_out, d_ff_2_q, IR1_2_q);
  or or_8 (or_8_out, d_ff_1_q, IR1_q);
  and and_6 (and_6_out, or_8_out, ~Cl2);  // AND_Gate
  or or_9 (or_9_out, d_ff_3_q, IR1_3_q);
  and and_7 (and_7_out, or_7_out, ~Cl1);  // AND_Gate
  D_Flip_Flop #(.trigger("rising"), .Pre_Clr_Positions("LEGACY"), .NegatePresetClear("false"), .enable("true"), .NewFFLayout("false")) u_IR1 (
    .clk(CLK), .D(and_6_out), .Q(IR1_q));  // open: Qn, preset, en, reset
  and and_8 (and_8_out, or_9_out, ~Cl3);  // AND_Gate
  or or_10 (IR3_t, IR3, IRC);
  not not_4 (not_4_out, equal);
  Regifile regifile_1 (
    .Din(RDin), .Clk(CLK), .R1(rs1), .R2(rs2), .WE(RegWrite), .W_num(IR[11:7]), .R1_num(multiplexer_7_out),
    .R2_num(multiplexer_8_out));
  D_Flip_Flop #(.trigger("rising"), .Pre_Clr_Positions("LEGACY"), .NegatePresetClear("false"), .enable("true"), .NewFFLayout("false")) IR1_2 (
    .clk(CLK), .D(and_7_out), .Q(IR1_2_q));  // open: Qn, preset, en, reset
  D_Flip_Flop #(.trigger("rising"), .Pre_Clr_Positions("LEGACY"), .NegatePresetClear("false"), .enable("true"), .NewFFLayout("false")) IR1_3 (
    .clk(CLK), .D(and_8_out), .Q(IR1_3_q));  // open: Qn, preset, en, reset
  and and_9 (and_9_out, equal, \单周期硬布线控制器_1_beq );
  and and_10 (and_10_out, not_4_out, \单周期硬布线控制器_1_bne );
  Multiplexer #(.select(1), .width(32), .disabled("Z"), .enable("false")) multiplexer_10 (
    .in0(rs2), .in1(imm), .out(multiplexer_10_out), .sel(\单周期硬布线控制器_1_alu_src ));
  Adder #(.width(32)) adder_1 (.a(PC), .b(32'h4), .out(PC_4));  // open: cin, cout
  Adder #(.width(32)) adder_2 (.a(PC), .b(immB), .out(PCB));  // open: cin, cout
  Adder #(.width(32)) adder_3 (.a(PC), .b(immJal), .out(PCJal));  // open: cin, cout
  Adder #(.width(32)) adder_4 (.a(PC), .b(immB), .out(PCBGEU));  // open: cin, cout
  or or_11 (key, and_9_out, and_10_out);
  ALU alu_1 (
    .X(rs1), .Y(multiplexer_10_out), .AluOP(\单周期硬布线控制器_1_alu_op ), .Equal(equal),
    .Result({alu_1_result, select}), .out_4(begu));  // open: Result_2, out_6
  Multiplexer #(.select(1), .width(32), .disabled("Z"), .enable("false")) multiplexer_11 (
    .in0(rs2), .in1(sb_t), .out(MDin), .sel(SB));
  Priority_Encoder #(.select(2), .disabled("Z")) priority_encoder_1 (
    .in0(IR1_2_q), .in1(IR1_q), .in2(IR1_3_q), .out(priority_encoder_1_out), .gs(INTto));  // open: in3, en_out, en_in
  and and_11 (and_11_out, INTto, not_5_out);
  not not_5 (not_5_out, URET);
  and and_12 (INT, INTto, not_6_out);
  not not_6 (not_6_out, IE);
  Multiplexer #(.select(2), .width(32), .disabled("Z"), .enable("false")) multiplexer_12 (
    .in0(32'h30ac), .in1(32'h3150), .in2(32'h31f4), .out(INT_PC), .sel(priority_encoder_1_out));  // open: in3
  D_Flip_Flop #(.trigger("rising"), .Pre_Clr_Positions("ABOVE_BELOW"), .NegatePresetClear("false"), .enable("false"), .NewFFLayout("true")) d_ff_4 (
    .clk(CLK), .D(and_11_out), .Q(IE));  // open: Qn, preset, reset
  not not_7 (not_7_out, halt);
  // Probe on priority_encoder_1_out
  RAM #(.addrWidth(10), .dataWidth(32), .bus("separate"), .Select("high")) ram_1 (
    .addr(alu_1_result[11:2]), .din(MDin), .data(SB2), .str(MemWrite), .sel(not_7_out), .clk(CLK));  // open: ld, clr
  or or_12 (or_12_out, Jal, Jalr);
  Multiplexer #(.select(1), .width(32), .disabled("Z"), .enable("false")) multiplexer_13 (
    .in0(PCJalr), .in1(PC_4), .out(RDin), .sel(or_12_out));
  Register #(.width(2), .trigger("rising"), .Select("low")) \u_锁存当前中断号  (
    .D(priority_encoder_1_out), .en(INT), .Q(\锁存当前中断号_q ), .clk(CLK));  // open: clr
  Register #(.width(32), .trigger("rising"), .Select("low")) PC_3 (
    .D(Ret_addr), .en(INT), .Q(Ret_PC), .clk(CLK));  // open: clr
  Multiplexer #(.select(1), .width(32), .disabled("Z"), .enable("false")) multiplexer_14 (
    .in0({alu_1_result, select}), .in1(SB2), .out(PCJalr), .sel(\单周期硬布线控制器_1_memtoreg ));
  Multiplexer #(.select(2), .width(32), .disabled("Z"), .enable("false")) multiplexer_15 (
    .in0({SB2[31:8], rs2[7:0]}), .in1({SB2[31:16], rs2[7:0], SB2[7:0]}),
    .in2({SB2[31:24], rs2[7:0], SB2[15:0]}), .in3({rs2[7:0], SB2[23:0]}), .out(sb_t), .sel(select));
  Demultiplexer #(.select(2), .width(1), .tristate("false"), .disabled("Z"), .enable("false")) demultiplexer_1 (
    .out0(Cl1), .out1(Cl2), .out2(Cl3), .in(URET), .sel(\锁存当前中断号_q ));  // open: out3

  // Other names for the same wires on the sheet: SB1[7:0] = rs2[7:0]

  // Notes on the sheet:
  //   中断源
  //   中断等待指示
  //   总复位信号应将除ROM以外所有存储组件全部清零
  //   单级中断测试信号模拟器
  //   数码管输出
  //   数码管输出应该用寄存器锁存，否则显示数据只能一闪而过
  //   指令存储器
  //   指令字
  //   contents of rom_1 (hex, n*v repeats v):
  //   7d000113 100413 1f41993 41f9d993 433 c00913 800b13 140413 f47413 800293 100313 499993 89e9b3 1300533
  //   2200893 73 406282b3 fe0294e3 140413 f00f93 1f47433 1c41413 800293 100313 49d993 89e9b3 1300533
  //   2200893 73 406282b3 fe0294e3 1c45413 406b0b33 b0463 f95ff06f 2b3 fff2c293 1029293 fff2e293 500533
  //   2200893 73 f5dff06f 1112023 410113 a12023 410113 812023 410113 1312023 410113 1412023 410113 1512023
  //   410113 1612023 410113 100b13 300a13 100a93 1600433 441413 14469b3 1300533 2200893 73 fe0416e3
  //   415a0a33 fe0a10e3 ffc10113 12b03 ffc10113 12a83 ffc10113 12a03 ffc10113 12983 ffc10113 12403
  //   ffc10113 12503 ffc10113 12883 200073 1112023 410113 a12023 410113 812023 410113 1312023 410113
  //   1412023 410113 1512023 410113 1612023 410113 200b13 300a13 100a93 1600433 441413 14469b3 1300533
  //   2200893 73 fe0416e3 415a0a33 fe0a10e3 ffc10113 12b03 ffc10113 12a83 ffc10113 12a03 ffc10113 12983
  //   ffc10113 12403 ffc10113 12503 ffc10113 12883 200073 1112023 410113 a12023 410113 812023 410113
  //   1312023 410113 1412023 410113 1512023 410113 1612023 410113 300b13 300a13 100a93 1600433 441413
  //   14469b3 1300533 2200893 73 fe0416e3 415a0a33 fe0a10e3 ffc10113 12b03 ffc10113 12a83 ffc10113 12a03
  //   ffc10113 12983 ffc10113 12403 ffc10113 12503 ffc10113 12883 200073
  //   Jal
  //   Jalr
  //   SB
  //   BGEU
  //   I型指令
  //   s型指令
  //   B型指令
  //   Jal
  //   Beq
  //   Bne
  //   MemToReg
  //   MemWrite
  //   AluOP
  //   AluSrcB
  //   RegWrite
  //   S_type
  //   ecall
  //   Reset 
  //   Reset 
  //   Reset 
  //   为方便自动评测，需要输出PC，IR，寄存器堆写如数据RDin
  //   RAM写使能MemWrite、RAM写入数据MDin等信号
  //   数据存储器
endmodule

module \单周期_多级中断  (
  input  IR1,
  input  IR2,
  input  IR3,
  output RegWrite,
  output MemWrite,
  output [31:0] PC,
  output [31:0] IR,
  output [31:0] RDin,
  output [31:0] MDin,
  output [31:0] LedData
);

  wire and_1_out, and_2_out, and_3_out, and_4_out, and_5_out, and_6_out, and_10_out, and_11_out, and_12_out,
       and_13_out, and_14_out, and_15_out, and_16_out, and_17_out, begu, BGEU, Cl1, Cl2, Cl3, CLK,
       comparator_1_eq, comparator_2_lt, comparator_3_eq, comparator_4_eq, comparator_5_eq, comparator_6_eq,
       comparator_7_eq, CSRRCI, CSRRSI, d_ff_1_q, d_ff_2_q, d_ff_3_q, decoder_1_out1, decoder_1_out2,
       decoder_1_out3, decoder_2_out1, decoder_2_out2, decoder_2_out3, ecall, ecall_num, equal, Go, halt, IE,
       in, INT, INTto, IR1_2_q, IR1_3_q, IR1_q, IR1_t, IR2_t, IR3_t, IRA, IRB, IRC, Jal, Jalr, key,
       not_1_out, not_2_out, not_3_out, not_4_out, not_5_out, not_6_out, or_4_out, or_5_out, or_6_out,
       or_9_out, or_10_out, or_11_out, or_14_out, or_15_out, or_16_out, or_17_out, RST, SB, URET, W1, W2, W3,
       xor_1_out, \单周期硬布线控制器_1_alu_src , \单周期硬布线控制器_1_beq , \单周期硬布线控制器_1_bne , \单周期硬布线控制器_1_memtoreg ,
       \单周期硬布线控制器_1_s_type ;
  wire [1:0] adder_5_out, CUR_IR_NUM, IR_NUM, IR_reg1_q, IR_reg2_q, IR_reg3_q, multiplexer_13_out, P, Q_NUM,
       select;
  wire [3:0] \单周期硬布线控制器_1_alu_op ;
  wire [4:0] multiplexer_7_out, multiplexer_8_out;
  wire [11:0] shifter_1_out;
  wire [15:0] \总周期数 ;
  wire [19:0] shifter_2_out;
  wire [31:0] bit_extender_1_out, bit_extender_2_out, counter_3_q, EPC1_q, EPC2_q, EPC3_q, imm, immB, immJal,
       INT_PC, multiplexer_2_out, multiplexer_3_out, multiplexer_4_out, multiplexer_5_out, multiplexer_6_out,
       multiplexer_11_out, PC_4, PCB, PCBGEU, PCJal, PCJalr, Ret_addr, Ret_PC, rs1, rs2, SB2, sb_t;
  wire [31:2] alu_1_result;

  Clock #(.highDuration(1), .lowDuration(1)) clock_1 (.out(CLK));
  Button _1 (.out(IRA));
  Button _2 (.out(IRB));
  Button _3 (.out(IRC));
  Button \u_继续运行  (.out(Go));
  LED #(.active("true")) led_1 (.in(W1));
  LED #(.active("true")) led_2 (.in(W2));
  LED #(.active("true")) led_3 (.in(W3));
  Counter #(.width(16), .max('hffff), .ongoal("wrap"), .trigger("rising"), .behavior("old")) counter_1 (
    .Q(\总周期数 ), .clk(and_1_out));  // open: load, D, count, carry, clr, preset
  and and_1 (and_1_out, CLK, not_1_out);
  not not_1 (not_1_out, halt);
  Multiplexer #(.select(1), .width(32), .disabled("Z"), .enable("false")) multiplexer_1 (
    .in0(multiplexer_2_out), .in1(PCJalr), .out(Ret_addr), .sel(Jalr));
  Multiplexer #(.select(1), .width(32), .disabled("Z"), .enable("false")) multiplexer_2 (
    .in0(multiplexer_3_out), .in1(PCJal), .out(multiplexer_2_out), .sel(Jal));
  and and_2 (and_2_out, begu, BGEU);
  Multiplexer #(.select(1), .width(32), .disabled("Z"), .enable("false")) multiplexer_3 (
    .in0(multiplexer_4_out), .in1(PCBGEU), .out(multiplexer_3_out), .sel(and_2_out));
  Multiplexer #(.select(1), .width(32), .disabled("Z"), .enable("false")) multiplexer_4 (
    .in0(PC_4), .in1(PCB), .out(multiplexer_4_out), .sel(key));
  Hex_Digit_Display hex_digit_display_1 (.value(LedData[31:28]));  // open: dp
  Comparator #(.width(32), .mode("twosComplement")) comparator_1 (
    .a(rs1), .b(32'ha), .eq(comparator_1_eq));  // open: gt, lt
  Multiplexer #(.select(1), .width(32), .disabled("Z"), .enable("false")) multiplexer_5 (
    .in0(Ret_addr), .in1(INT_PC), .out(multiplexer_5_out), .sel(INT));
  // Probe on INT_PC
  or or_1 (W1, IR1_2_q, d_ff_2_q);
  D_Flip_Flop #(.trigger("rising"), .Pre_Clr_Positions("LEGACY"), .NegatePresetClear("false"), .enable("true"), .NewFFLayout("false")) d_ff_1 (
    .clk(IR2_t), .D(1'b1), .Q(d_ff_1_q), .reset(IR1_q));  // open: Qn, preset, en
  or or_2 (W2, IR1_q, d_ff_1_q);
  or or_3 (W3, IR1_3_q, d_ff_3_q);
  Hex_Digit_Display hex_digit_display_2 (.value(LedData[27:24]));  // open: dp
  Hex_Digit_Display hex_digit_display_3 (.value(LedData[23:20]));  // open: dp
  and and_3 (and_3_out, ecall, comparator_1_eq);
  Multiplexer #(.select(1), .width(32), .disabled("Z"), .enable("false")) multiplexer_6 (
    .in0(multiplexer_5_out), .in1(Ret_PC), .out(multiplexer_6_out), .sel(URET));
  not not_2 (not_2_out, halt);
  // Probe on Ret_PC
  D_Flip_Flop #(.trigger("rising"), .Pre_Clr_Positions("LEGACY"), .NegatePresetClear("false"), .enable("true"), .NewFFLayout("false")) d_ff_2 (
    .clk(IR1_t), .D(1'b1), .Q(d_ff_2_q), .reset(IR1_2_q));  // open: Qn, preset, en
  or or_4 (or_4_out, d_ff_1_q, IR1_q);
  D_Flip_Flop #(.trigger("rising"), .Pre_Clr_Positions("LEGACY"), .NegatePresetClear("false"), .enable("true"), .NewFFLayout("false")) d_ff_3 (
    .clk(IR3_t), .D(1'b1), .Q(d_ff_3_q), .reset(IR1_3_q));  // open: Qn, preset, en
  Hex_Digit_Display hex_digit_display_4 (.value(LedData[19:16]));  // open: dp
  Hex_Digit_Display hex_digit_display_5 (.value(LedData[15:12]));  // open: dp
  xor xor_1 (xor_1_out, and_3_out, Go);
  // Probe on PC
  Register #(.width(32), .trigger("rising"), .Select("low")) u_PC (
    .D(multiplexer_6_out), .en(not_2_out), .Q(PC), .clk(CLK), .clr(RST));
  or or_5 (or_5_out, d_ff_2_q, IR1_2_q);
  and and_4 (and_4_out, or_4_out, ~Cl2);  // AND_Gate
  or or_6 (or_6_out, d_ff_3_q, IR1_3_q);
  Hex_Digit_Display hex_digit_display_6 (.value(LedData[11:8]));  // open: dp
  Hex_Digit_Display hex_digit_display_7 (.value(LedData[7:4]));  // open: dp
  // Probe on \总周期数 
  // Probe on \总周期数 
  Register #(.width(1), .trigger("falling"), .Select("low")) PC_2 (
    .D(xor_1_out), .en(xor_1_out), .Q(halt), .clk(CLK), .clr(Go));
  Counter #(.width(32), .max('hffffffff), .ongoal("wrap"), .trigger("rising"), .behavior("old")) counter_2 (
    .load(ecall), .D(rs2), .count(1'b0), .Q(LedData), .clk(CLK));  // open: carry, clr, preset
  // RiscV_Probe riscv_probe_1: pin names not known; wires that end beside it: IR
  and and_5 (and_5_out, or_5_out, ~Cl1);  // AND_Gate
  D_Flip_Flop #(.trigger("rising"), .Pre_Clr_Positions("LEGACY"), .NegatePresetClear("false"), .enable("true"), .NewFFLayout("false")) u_IR1 (
    .clk(CLK), .D(and_4_out), .Q(IR1_q));  // open: Qn, preset, en, reset
  and and_6 (and_6_out, or_6_out, ~Cl3);  // AND_Gate
  Hex_Digit_Display hex_digit_display_8 (.value(LedData[3:0]));  // open: dp
  ROM #(.addrWidth(10), .dataWidth(32), .Select("high")) rom_1 (.addr(PC[11:2]), .data(IR));
  // Probe on IR
  D_Flip_Flop #(.trigger("rising"), .Pre_Clr_Positions("LEGACY"), .NegatePresetClear("false"), .enable("true"), .NewFFLayout("false")) IR1_2 (
    .clk(CLK), .D(and_5_out), .Q(IR1_2_q));  // open: Qn, preset, en, reset
  D_Flip_Flop #(.trigger("rising"), .Pre_Clr_Positions("LEGACY"), .NegatePresetClear("false"), .enable("true"), .NewFFLayout("false")) IR1_3 (
    .clk(CLK), .D(and_6_out), .Q(IR1_3_q));  // open: Qn, preset, en, reset
  or or_7 (IR1_t, IR1, IRA);
  \单周期硬布线控制器  \u_单周期硬布线控制器_1  (
    .Funct({IR[30], IR[25], IR[14:12]}), .OP(IR[6:2]), .ALU_OP(\单周期硬布线控制器_1_alu_op ),
    .MemToReg(\单周期硬布线控制器_1_memtoreg ), .MemWrite(MemWrite), .ALU_SRC(\单周期硬布线控制器_1_alu_src ),
    .RegWrite(RegWrite), .ecall(ecall_num), .S_type(\单周期硬布线控制器_1_s_type ), .Jalr(Jalr),
    .Beq(\单周期硬布线控制器_1_beq ), .JAL(Jal), .Bne(\单周期硬布线控制器_1_bne ), .SB(SB), .BGEU(BGEU), .CSRRSI(CSRRSI),
    .CSRRCI(CSRRCI));
  Multiplexer #(.select(1), .width(5), .disabled("Z"), .enable("false")) multiplexer_7 (
    .in0(IR[19:15]), .in1(5'b10001), .out(multiplexer_7_out), .sel(ecall));
  Multiplexer #(.select(1), .width(5), .disabled("Z"), .enable("false")) multiplexer_8 (
    .in0(IR[24:20]), .in1(5'b01010), .out(multiplexer_8_out), .sel(ecall));
  assign bit_extender_1_out = {{20{IR[31]}}, IR[31:20]};  // Bit_Extender bit_extender_1
  assign bit_extender_2_out = {{20{IR[31]}}, {IR[31:25], IR[11:7]}};  // Bit_Extender bit_extender_2
  Shifter #(.width(12), .shift("ll")) shifter_1 (
    .in({IR[31], IR[7], IR[30:25], IR[11:8]}), .\dist (4'b0001), .out(shifter_1_out));
  and and_7 (URET, ecall_num, IR[21]);
  not not_3 (not_3_out, IR[21]);
  Shifter #(.width(20), .shift("ll")) shifter_2 (
    .in({IR[31], IR[19:12], IR[20], IR[30:21]}), .\dist (5'b00001), .out(shifter_2_out));
  Priority_Encoder #(.select(2), .disabled("Z")) priority_encoder_1 (
    .in0(1'b1), .in1(IR1_2_q), .in2(IR1_q), .in3(IR1_3_q), .out(IR_NUM), .gs(INTto));  // open: en_out, en_in
  and and_8 (INT, INTto, in, IE);
  or or_8 (IR2_t, IR2, IRB);
  Multiplexer #(.select(1), .width(32), .disabled("Z"), .enable("false")) multiplexer_9 (
    .in0(bit_extender_1_out), .in1(bit_extender_2_out), .out(imm), .sel(\单周期硬布线控制器_1_s_type ));
  assign immB = {{20{shifter_1_out[11]}}, shifter_1_out};  // Bit_Extender bit_extender_3
  and and_9 (ecall, ecall_num, not_3_out);
  assign immJal = {{12{shifter_2_out[19]}}, shifter_2_out};  // Bit_Extender bit_extender_4
  // Probe on IR_NUM
  Multiplexer #(.select(2), .width(32), .disabled("Z"), .enable("false")) multiplexer_10 (
    .in0(Ret_addr), .in1(32'h30ac), .in2(32'h3158), .in3(32'h3204), .out(INT_PC), .sel(IR_NUM));
  or or_9 (or_9_out, INT, CSRRCI);
  Counter #(.width(32), .max('hffffffff), .ongoal("wrap"), .trigger("rising"), .behavior("old")) counter_3 (
    .Q(counter_3_q), .clk(CLK));  // open: load, D, count, carry, clr, preset
  not not_4 (not_4_out, or_9_out);
  or or_10 (or_10_out, or_11_out, comparator_2_lt, INT, URET);
  Comparator #(.width(32), .mode("unsigned")) comparator_2 (
    .a(counter_3_q), .b(32'h2), .lt(comparator_2_lt));  // open: gt, eq
  or or_11 (or_11_out, CSRRCI, CSRRSI);
  or or_12 (IR3_t, IR3, IRC);
  not not_5 (not_5_out, equal);
  Regifile regifile_1 (
    .Din(RDin), .Clk(CLK), .R1(rs1), .R2(rs2), .WE(RegWrite), .W_num(IR[11:7]), .R1_num(multiplexer_7_out),
    .R2_num(multiplexer_8_out));
  Demultiplexer #(.select(2), .width(1), .tristate("false"), .disabled("Z"), .enable("false")) demultiplexer_1 (
    .out1(Cl1), .out2(Cl2), .out3(Cl3), .in(URET), .sel(IR_NUM));  // open: out0
  Register #(.width(1), .trigger("rising"), .Select("low")) u_IE (
    .D(not_4_out), .en(or_10_out), .Q(IE), .clk(CLK));  // open: clr
  and and_10 (and_10_out, equal, \单周期硬布线控制器_1_beq );
  and and_11 (and_11_out, not_5_out, \单周期硬布线控制器_1_bne );
  Multiplexer #(.select(1), .width(32), .disabled("Z"), .enable("false")) multiplexer_11 (
    .in0(rs2), .in1(imm), .out(multiplexer_11_out), .sel(\单周期硬布线控制器_1_alu_src ));
  Adder #(.width(32)) adder_1 (.a(PC), .b(32'h4), .out(PC_4));  // open: cin, cout
  Adder #(.width(32)) adder_2 (.a(PC), .b(immB), .out(PCB));  // open: cin, cout
  Adder #(.width(32)) adder_3 (.a(PC), .b(immJal), .out(PCJal));  // open: cin, cout
  Adder #(.width(32)) adder_4 (.a(PC), .b(immB), .out(PCBGEU));  // open: cin, cout
  or or_13 (key, and_10_out, and_11_out);
  ALU alu_1 (
    .X(rs1), .Y(multiplexer_11_out), .AluOP(\单周期硬布线控制器_1_alu_op ), .Equal(equal),
    .Result({alu_1_result, select}), .out_4(begu));  // open: Result_2, out_6
  Multiplexer #(.select(1), .width(32), .disabled("Z"), .enable("false")) multiplexer_12 (
    .in0(rs2), .in1(sb_t), .out(MDin), .sel(SB));
  // Probe on RDin
  Decoder #(.select(2), .tristate("false"), .disabled("Z"), .enable("false")) decoder_1 (
    .out1(decoder_1_out1), .out2(decoder_1_out2), .out3(decoder_1_out3), .sel(IR_NUM));  // open: out0
  Multiplexer #(.select(1), .width(2), .disabled("Z"), .enable("false")) multiplexer_13 (
    .in0(2'b11), .in1(2'b01), .out(multiplexer_13_out), .sel(INT));
  and and_12 (and_12_out, decoder_1_out1, INT);
  and and_13 (and_13_out, decoder_1_out2, INT);
  and and_14 (and_14_out, decoder_1_out3, INT);
  not not_6 (not_6_out, halt);
  Adder #(.width(2)) adder_5 (.a(P), .b(multiplexer_13_out), .out(adder_5_out));  // open: cin, cout
  or or_14 (or_14_out, INT, URET);
  Decoder #(.select(2), .tristate("false"), .disabled("Z"), .enable("false")) decoder_2 (
    .out1(decoder_2_out1), .out2(decoder_2_out2), .out3(decoder_2_out3), .sel(Q_NUM));  // open: out0
  RAM #(.addrWidth(10), .dataWidth(32), .bus("separate"), .Select("high")) ram_1 (
    .addr(alu_1_result[11:2]), .din(MDin), .data(SB2), .str(MemWrite), .sel(not_6_out), .clk(CLK));  // open: ld, clr
  or or_15 (or_15_out, Jal, Jalr);
  Multiplexer #(.select(1), .width(32), .disabled("Z"), .enable("false")) multiplexer_14 (
    .in0(PCJalr), .in1(PC_4), .out(RDin), .sel(or_15_out));
  Register #(.width(2), .trigger("rising"), .Select("low")) stack (
    .D(adder_5_out), .en(or_14_out), .Q(P), .clk(CLK));  // open: clr
  and and_15 (and_15_out, INT, decoder_2_out1);
  and and_16 (and_16_out, INT, decoder_2_out2);
  and and_17 (and_17_out, INT, decoder_2_out3);
  Register #(.width(32), .trigger("rising"), .Select("low")) EPC1 (
    .D(Ret_addr), .en(and_12_out), .Q(EPC1_q), .clk(CLK));  // open: clr
  Register #(.width(32), .trigger("rising"), .Select("low")) EPC2 (
    .D(Ret_addr), .en(and_13_out), .Q(EPC2_q), .clk(CLK));  // open: clr
  Multiplexer #(.select(1), .width(32), .disabled("Z"), .enable("false")) multiplexer_15 (
    .in0({alu_1_result, select}), .in1(SB2), .out(PCJalr), .sel(\单周期硬布线控制器_1_memtoreg ));
  Multiplexer #(.select(2), .width(32), .disabled("Z"), .enable("false")) multiplexer_16 (
    .in0({SB2[31:8], rs2[7:0]}), .in1({SB2[31:16], rs2[7:0], SB2[7:0]}),
    .in2({SB2[31:24], rs2[7:0], SB2[15:0]}), .in3({rs2[7:0], SB2[23:0]}), .out(sb_t), .sel(select));
  Adder #(.width(2)) adder_6 (.a(P), .b(2'b01), .out(Q_NUM));  // open: cin, cout
  Register #(.width(2), .trigger("rising"), .Select("low")) IR_reg1 (
    .D(IR_NUM), .en(and_15_out), .Q(IR_reg1_q), .clk(CLK));  // open: clr
  Register #(.width(32), .trigger("rising"), .Select("low")) EPC3 (
    .D(Ret_addr), .en(and_14_out), .Q(EPC3_q), .clk(CLK));  // open: clr
  Register #(.width(2), .trigger("rising"), .Select("low")) IR_reg2 (
    .D(IR_NUM), .en(and_16_out), .Q(IR_reg2_q), .clk(CLK));  // open: clr
  Register #(.width(2), .trigger("rising"), .Select("low")) IR_reg3 (
    .D(IR_NUM), .en(and_17_out), .Q(IR_reg3_q), .clk(CLK));  // open: clr
  Comparator #(.width(16), .mode("twosComplement")) comparator_3 (
    .a(16'h258), .b(\总周期数 ), .eq(comparator_3_eq));  // open: gt, lt
  Comparator #(.width(16), .mode("twosComplement")) comparator_4 (
    .a(\总周期数 ), .b(16'h1), .eq(comparator_4_eq));  // open: gt, lt
  Comparator #(.width(16), .mode("twosComplement")) comparator_5 (
    .a(\总周期数 ), .b(16'h4), .eq(comparator_5_eq));  // open: gt, lt
  Comparator #(.width(16), .mode("twosComplement")) comparator_6 (
    .a(\总周期数 ), .b(16'h7), .eq(comparator_6_eq));  // open: gt, lt
  Comparator #(.width(16), .mode("twosComplement")) comparator_7 (
    .a(\总周期数 ), .b(16'h241), .eq(comparator_7_eq));  // open: gt, lt
  Multiplexer #(.select(2), .width(2), .disabled("Z"), .enable("false")) multiplexer_17 (
    .in0(2'b00), .in1(IR_reg1_q), .in2(IR_reg2_q), .in3(IR_reg3_q), .out(CUR_IR_NUM), .sel(P));
  Multiplexer #(.select(2), .width(32), .disabled("Z"), .enable("false")) multiplexer_18 (
    .in1(EPC1_q), .in2(EPC2_q), .in3(EPC3_q), .out(Ret_PC), .sel(CUR_IR_NUM));  // open: in0
  or or_16 (or_16_out, comparator_3_eq, comparator_4_eq);
  assign IRA = or_16_out ? ~CLK : 1'bz;  // Controlled_Inverter controlled_inverter_1
  assign IRB = comparator_5_eq ? ~CLK : 1'bz;  // Controlled_Inverter controlled_inverter_2
  or or_17 (or_17_out, comparator_6_eq, comparator_7_eq);
  assign IRC = or_17_out ? ~CLK : 1'bz;  // Controlled_Inverter controlled_inverter_3
  Comparator #(.width(2), .mode("unsigned")) comparator_8 (.a(CUR_IR_NUM), .b(IR_NUM), .lt(in));  // open: gt, eq
  Pull_Resistor #(.pull(0)) pull_resistor_1 (.node(IRA));
  Pull_Resistor #(.pull(0)) pull_resistor_2 (.node(IRB));
  Pull_Resistor #(.pull(0)) pull_resistor_3 (.node(IRC));

  // Other names for the same wires on the sheet: SB1[7:0] = rs2[7:0]

  // Notes on the sheet:
  //   中断源
  //   中断等待指示
  //   总复位信号应将除ROM以外所有存储组件全部清零
  //   数码管输出
  //   数码管输出应该用寄存器锁存，否则显示数据只能一闪而过
  //   指令存储器
  //   Reset 
  //   Reset 
  //   Reset 
  //   指令字
  //   contents of rom_1 (hex, n*v repeats v):
  //   7d000113 100413 1f41993 41f9d993 433 c00913 800b13 140413 f47413 800293 100313 499993 89e9b3 1300533
  //   2200893 73 406282b3 fe0294e3 140413 f00f93 1f47433 1c41413 800293 100313 49d993 89e9b3 1300533
  //   2200893 73 406282b3 fe0294e3 1c45413 406b0b33 b0463 f95ff06f 2b3 fff2c293 1029293 fff2e293 500533
  //   2200893 73 f5dff06f 1112023 410113 a12023 410113 812023 410113 1312023 410113 1412023 410113 1512023
  //   410113 1612023 410113 40e073 100b13 300a13 100a93 1600433 441413 14469b3 1300533 2200893 73 fe0416e3
  //   415a0a33 fe0a10e3 40f073 ffc10113 12b03 ffc10113 12a83 ffc10113 12a03 ffc10113 12983 ffc10113 12403
  //   ffc10113 12503 ffc10113 12883 200073 1112023 410113 a12023 410113 812023 410113 1312023 410113
  //   1412023 410113 1512023 410113 1612023 410113 40e073 200b13 300a13 100a93 1600433 441413 14469b3
  //   1300533 2200893 73 fe0416e3 415a0a33 fe0a10e3 40f073 ffc10113 12b03 ffc10113 12a83 ffc10113 12a03
  //   ffc10113 12983 ffc10113 12403 ffc10113 12503 ffc10113 12883 200073 1112023 410113 a12023 410113
  //   812023 410113 1312023 410113 1412023 410113 1512023 410113 1612023 410113 40e073 300b13 300a13
  //   100a93 1600433 441413 14469b3 1300533 2200893 73 fe0416e3 415a0a33 fe0a10e3 40f073 ffc10113 12b03
  //   ffc10113 12a83 ffc10113 12a03 ffc10113 12983 ffc10113 12403 ffc10113 12503 ffc10113 12883 200073
  //   Jal
  //   Jalr
  //   SB
  //   BGEU
  //   I型指令
  //   s型指令
  //   B型指令
  //   Jal
  //   Beq
  //   Bne
  //   MemToReg
  //   MemWrite
  //   AluOP
  //   AluSrcB
  //   RegWrite
  //   S_type
  //   ecall
  //   为方便自动评测，需要输出PC，IR，寄存器堆写如数据RDin
  //   RAM写使能MemWrite、RAM写入数据MDin等信号
  //   数据存储器
  //   多级中断测试信号模拟器
endmodule

module \封装正确性测试  (
);

  wire IR1, IR2, IR3, MemW, RegW;
  wire [31:0] EX_PC, ID_PC, IF_PC, IR, LED, MDin, MDinr, MEM_PC, PC, RDin, RDinr, WB_PC;

  \单周期RISC_V  \u_单周期risc_v_1  (
    .IR1(IR1), .IR2(IR2), .IR3(IR3), .RegWrite(RegW), .MemWrite(MemW), .PC(PC), .IR(IR), .RDin(RDin),
    .MDin(MDin), .LedData(LED));
  \气泡流水线  \u_气泡流水线_1  (
    .RegWrite(RegW), .MemWrite(MemW), .IF_PC(IF_PC), .ID_PC(ID_PC), .EX_PC(EX_PC), .M_PC(MEM_PC),
    .WB_PC(WB_PC), .RDin(RDinr), .MDin(MDinr), .LedData(LED));
  \单周期_单级中断  \u_单周期_单级中断_1  (
    .IR1(IR1), .IR2(IR2), .IR3(IR3), .RegWrite(RegW), .MemWrite(MemW), .PC(PC), .IR(IR), .RDin(RDin),
    .MDin(MDin), .LedData(LED));
  \理想流水线  \u_理想流水线_1  (
    .RegWrite(RegW), .MemWrite(MemW), .IF_PC(IF_PC), .ID_PC(ID_PC), .EX_PC(EX_PC), .M_PC(MEM_PC),
    .WB_PC(WB_PC), .RDin(RDinr), .MDin(MDinr), .LedData(LED));
  \重定向流水线  \u_重定向流水线_1  (
    .RegWrite(RegW), .MemWrite(MemW), .IF_PC(IF_PC), .ID_PC(ID_PC), .EX_PC(EX_PC), .M_PC(MEM_PC),
    .WB_PC(WB_PC), .RDin(RDinr), .MDin(MDinr), .LedData(LED));
  \单周期_多级中断  \u_单周期_多级中断_1  (
    .IR1(IR1), .IR2(IR2), .IR3(IR3), .RegWrite(RegW), .MemWrite(MemW), .PC(PC), .IR(IR), .RDin(RDin),
    .MDin(MDin), .LedData(LED));

  // Notes on the sheet:
  //   单周期封装测试
  //   气泡流水封装测试
  //   单周期+单级中断封装测试
  //   请检查上面封装有无位宽不匹配，引脚标签是否和连接的标签相对应，否则无法在educoder平台上正确测试
  //   理想流水封装测试
  //   重定向流水封装测试
  //   单周期+多级中断封装测试
endmodule

module \理想IF_ID  (
  input  [31:0] IF_PC,
  input  [31:0] IF_IR,
  input  \同步清零_高电平有效 ,
  input  CLK,
  input  \使能端_低电平有效_stall_高电平有效 ,
  output [31:0] ID_PC,
  output [31:0] ID_IR
);

  wire not_1_out;
  wire [31:0] multiplexer_1_out, multiplexer_2_out;

  Multiplexer #(.select(1), .width(32), .disabled("Z"), .enable("false")) multiplexer_1 (
    .in0(IF_PC), .in1({32{1'b0}}), .out(multiplexer_1_out), .sel(\同步清零_高电平有效 ));
  Multiplexer #(.select(1), .width(32), .disabled("Z"), .enable("false")) multiplexer_2 (
    .in0(IF_IR), .in1({32{1'b0}}), .out(multiplexer_2_out), .sel(\同步清零_高电平有效 ));
  Pull_Resistor #(.pull(0)) pull_resistor_1 (.node(\同步清零_高电平有效 ));
  not not_1 (not_1_out, \使能端_低电平有效_stall_高电平有效 );
  Register #(.width(32), .trigger("rising"), .Select("low")) register_1 (
    .D(multiplexer_1_out), .en(not_1_out), .Q(ID_PC), .clk(CLK));  // open: clr
  Register #(.width(32), .trigger("rising"), .Select("low")) register_2 (
    .D(multiplexer_2_out), .en(not_1_out), .Q(ID_IR), .clk(CLK));  // open: clr
  Pull_Resistor #(.pull(0)) pull_resistor_2 (.node(not_1_out));

  // Notes on the sheet:
  //   使能端_低电平有效_stall_高电平有效: pull=down
  //   同步清零_高电平有效: pull=down
endmodule

module \理想ID_EX  (
  input  [31:0] ID_IR,
  input  [31:0] ID_PC,
  input  jal,
  input  jalr,
  input  SB,
  input  BGEU,
  input  Beq,
  input  Bne,
  input  MemToReg,
  input  MemWrite,
  input  [3:0] AluOP,
  input  ecall,
  input  RegWrite,
  input  AluSrcB,
  input  [31:0] rs1,
  input  [31:0] rs2,
  input  [31:0] imm,
  input  [31:0] immB,
  input  [31:0] immJal,
  input  [4:0] rd,
  input  [1:0] FwdRs1,
  input  [1:0] FwdRs2,
  input  \同步清零_气泡_高电平有效 ,
  input  CLK,
  input  \使能端_低电平有效_stall_高电平有效 ,
  output [31:0] EX_IR,
  output [31:0] EX_PC,
  output Jal_2,
  output jalr_2,
  output SB_2,
  output BGEU_2,
  output Beq_2,
  output Bne_2,
  output MemToReg_2,
  output MemWrite_2,
  output [3:0] AluOP_2,
  output ecall_2,
  output RegWrite_2,
  output AluSrcB_2,
  output [31:0] rs1_2,
  output [31:0] rs2_2,
  output [31:0] imm_2,
  output [31:0] immB_2,
  output [31:0] immJal_2,
  output [4:0] rd_2,
  output [1:0] FwdRs1_2,
  output [1:0] FwdRs2_2
);

  wire multiplexer_3_out, multiplexer_4_out, multiplexer_5_out, multiplexer_6_out, multiplexer_7_out,
       multiplexer_8_out, multiplexer_9_out, multiplexer_10_out, multiplexer_12_out, multiplexer_13_out,
       multiplexer_14_out, pull_resistor_2_node;
  wire [1:0] multiplexer_21_out, multiplexer_22_out;
  wire [3:0] multiplexer_11_out;
  wire [4:0] multiplexer_20_out;
  wire [31:0] multiplexer_1_out, multiplexer_2_out, multiplexer_15_out, multiplexer_16_out,
       multiplexer_17_out, multiplexer_18_out, multiplexer_19_out;

  Multiplexer #(.select(1), .width(32), .disabled("Z"), .enable("false")) multiplexer_1 (
    .in0(ID_IR), .in1({32{1'b0}}), .out(multiplexer_1_out), .sel(\同步清零_气泡_高电平有效 ));
  Multiplexer #(.select(1), .width(32), .disabled("Z"), .enable("false")) multiplexer_2 (
    .in0(ID_PC), .in1({32{1'b0}}), .out(multiplexer_2_out), .sel(\同步清零_气泡_高电平有效 ));
  Multiplexer #(.select(1), .width(1), .disabled("Z"), .enable("false")) multiplexer_3 (
    .in0(jal), .in1(1'b0), .out(multiplexer_3_out), .sel(\同步清零_气泡_高电平有效 ));
  Multiplexer #(.select(1), .width(1), .disabled("Z"), .enable("false")) multiplexer_4 (
    .in0(jalr), .in1(1'b0), .out(multiplexer_4_out), .sel(\同步清零_气泡_高电平有效 ));
  Multiplexer #(.select(1), .width(1), .disabled("Z"), .enable("false")) multiplexer_5 (
    .in0(SB), .in1(1'b0), .out(multiplexer_5_out), .sel(\同步清零_气泡_高电平有效 ));
  Multiplexer #(.select(1), .width(1), .disabled("Z"), .enable("false")) multiplexer_6 (
    .in0(BGEU), .in1(1'b0), .out(multiplexer_6_out), .sel(\同步清零_气泡_高电平有效 ));
  Multiplexer #(.select(1), .width(1), .disabled("Z"), .enable("false")) multiplexer_7 (
    .in0(Beq), .in1(1'b0), .out(multiplexer_7_out), .sel(\同步清零_气泡_高电平有效 ));
  Multiplexer #(.select(1), .width(1), .disabled("Z"), .enable("false")) multiplexer_8 (
    .in0(Bne), .in1(1'b0), .out(multiplexer_8_out), .sel(\同步清零_气泡_高电平有效 ));
  Multiplexer #(.select(1), .width(1), .disabled("Z"), .enable("false")) multiplexer_9 (
    .in0(MemToReg), .in1(1'b0), .out(multiplexer_9_out), .sel(\同步清零_气泡_高电平有效 ));
  Multiplexer #(.select(1), .width(1), .disabled("Z"), .enable("false")) multiplexer_10 (
    .in0(MemWrite), .in1(1'b0), .out(multiplexer_10_out), .sel(\同步清零_气泡_高电平有效 ));
  Multiplexer #(.select(1), .width(4), .disabled("Z"), .enable("false")) multiplexer_11 (
    .in0(AluOP), .in1(4'b0000), .out(multiplexer_11_out), .sel(\同步清零_气泡_高电平有效 ));
  Multiplexer #(.select(1), .width(1), .disabled("Z"), .enable("false")) multiplexer_12 (
    .in0(ecall), .in1(1'b0), .out(multiplexer_12_out), .sel(\同步清零_气泡_高电平有效 ));
  Multiplexer #(.select(1), .width(1), .disabled("Z"), .enable("false")) multiplexer_13 (
    .in0(RegWrite), .in1(1'b0), .out(multiplexer_13_out), .sel(\同步清零_气泡_高电平有效 ));
  Multiplexer #(.select(1), .width(1), .disabled("Z"), .enable("false")) multiplexer_14 (
    .in0(AluSrcB), .in1(1'b0), .out(multiplexer_14_out), .sel(\同步清零_气泡_高电平有效 ));
  Multiplexer #(.select(1), .width(32), .disabled("Z"), .enable("false")) multiplexer_15 (
    .in0(rs1), .in1({32{1'b0}}), .out(multiplexer_15_out), .sel(\同步清零_气泡_高电平有效 ));
  Multiplexer #(.select(1), .width(32), .disabled("Z"), .enable("false")) multiplexer_16 (
    .in0(rs2), .in1({32{1'b0}}), .out(multiplexer_16_out), .sel(\同步清零_气泡_高电平有效 ));
  Multiplexer #(.select(1), .width(32), .disabled("Z"), .enable("false")) multiplexer_17 (
    .in0(imm), .in1({32{1'b0}}), .out(multiplexer_17_out), .sel(\同步清零_气泡_高电平有效 ));
  Multiplexer #(.select(1), .width(32), .disabled("Z"), .enable("false")) multiplexer_18 (
    .in0(immB), .in1({32{1'b0}}), .out(multiplexer_18_out), .sel(\同步清零_气泡_高电平有效 ));
  Multiplexer #(.select(1), .width(32), .disabled("Z"), .enable("false")) multiplexer_19 (
    .in0(immJal), .in1({32{1'b0}}), .out(multiplexer_19_out), .sel(\同步清零_气泡_高电平有效 ));
  Multiplexer #(.select(1), .width(5), .disabled("Z"), .enable("false")) multiplexer_20 (
    .in0(rd), .in1({5{1'b0}}), .out(multiplexer_20_out), .sel(\同步清零_气泡_高电平有效 ));
  Multiplexer #(.select(1), .width(2), .disabled("Z"), .enable("false")) multiplexer_21 (
    .in0(FwdRs1), .in1(2'b00), .out(multiplexer_21_out), .sel(\同步清零_气泡_高电平有效 ));
  Multiplexer #(.select(1), .width(2), .disabled("Z"), .enable("false")) multiplexer_22 (
    .in0(FwdRs2), .in1(2'b00), .out(multiplexer_22_out), .sel(\同步清零_气泡_高电平有效 ));
  Pull_Resistor #(.pull(0)) pull_resistor_1 (.node(\同步清零_气泡_高电平有效 ));
  Pull_Resistor #(.pull(0)) pull_resistor_2 (.node(pull_resistor_2_node));
  not not_1 (pull_resistor_2_node, \使能端_低电平有效_stall_高电平有效 );
  Register #(.width(32), .trigger("rising"), .Select("low")) register_1 (
    .D(multiplexer_1_out), .en(pull_resistor_2_node), .Q(EX_IR), .clk(CLK));  // open: clr
  Register #(.width(32), .trigger("rising"), .Select("low")) register_2 (
    .D(multiplexer_2_out), .en(pull_resistor_2_node), .Q(EX_PC), .clk(CLK));  // open: clr
  Register #(.width(1), .trigger("rising"), .Select("low")) register_3 (
    .D(multiplexer_3_out), .en(pull_resistor_2_node), .Q(Jal_2), .clk(CLK));  // open: clr
  Register #(.width(1), .trigger("rising"), .Select("low")) register_4 (
    .D(multiplexer_4_out), .en(pull_resistor_2_node), .Q(jalr_2), .clk(CLK));  // open: clr
  Register #(.width(1), .trigger("rising"), .Select("low")) register_5 (
    .D(multiplexer_5_out), .en(pull_resistor_2_node), .Q(SB_2), .clk(CLK));  // open: clr
  Register #(.width(1), .trigger("rising"), .Select("low")) register_6 (
    .D(multiplexer_6_out), .en(pull_resistor_2_node), .Q(BGEU_2), .clk(CLK));  // open: clr
  Register #(.width(1), .trigger("rising"), .Select("low")) register_7 (
    .D(multiplexer_7_out), .en(pull_resistor_2_node), .Q(Beq_2), .clk(CLK));  // open: clr
  Register #(.width(1), .trigger("rising"), .Select("low")) register_8 (
    .D(multiplexer_8_out), .en(pull_resistor_2_node), .Q(Bne_2), .clk(CLK));  // open: clr
  Register #(.width(1), .trigger("rising"), .Select("low")) register_9 (
    .D(multiplexer_9_out), .en(pull_resistor_2_node), .Q(MemToReg_2), .clk(CLK));  // open: clr
  Register #(.width(1), .trigger("rising"), .Select("low")) register_10 (
    .D(multiplexer_10_out), .en(pull_resistor_2_node), .Q(MemWrite_2), .clk(CLK));  // open: clr
  Register #(.width(4), .trigger("rising"), .Select("low")) register_11 (
    .D(multiplexer_11_out), .en(pull_resistor_2_node), .Q(AluOP_2), .clk(CLK));  // open: clr
  Register #(.width(1), .trigger("rising"), .Select("low")) register_12 (
    .D(multiplexer_12_out), .en(pull_resistor_2_node), .Q(ecall_2), .clk(CLK));  // open: clr
  Register #(.width(1), .trigger("rising"), .Select("low")) register_13 (
    .D(multiplexer_13_out), .en(pull_resistor_2_node), .Q(RegWrite_2), .clk(CLK));  // open: clr
  Register #(.width(1), .trigger("rising"), .Select("low")) register_14 (
    .D(multiplexer_14_out), .en(pull_resistor_2_node), .Q(AluSrcB_2), .clk(CLK));  // open: clr
  Register #(.width(32), .trigger("rising"), .Select("low")) register_15 (
    .D(multiplexer_15_out), .en(pull_resistor_2_node), .Q(rs1_2), .clk(CLK));  // open: clr
  Register #(.width(32), .trigger("rising"), .Select("low")) register_16 (
    .D(multiplexer_16_out), .en(pull_resistor_2_node), .Q(rs2_2), .clk(CLK));  // open: clr
  Register #(.width(32), .trigger("rising"), .Select("low")) register_17 (
    .D(multiplexer_17_out), .en(pull_resistor_2_node), .Q(imm_2), .clk(CLK));  // open: clr
  Register #(.width(32), .trigger("rising"), .Select("low")) register_18 (
    .D(multiplexer_18_out), .en(pull_resistor_2_node), .Q(immB_2), .clk(CLK));  // open: clr
  Register #(.width(32), .trigger("rising"), .Select("low")) register_19 (
    .D(multiplexer_19_out), .en(pull_resistor_2_node), .Q(immJal_2), .clk(CLK));  // open: clr
  Register #(.width(5), .trigger("rising"), .Select("low")) register_20 (
    .D(multiplexer_20_out), .en(pull_resistor_2_node), .Q(rd_2), .clk(CLK));  // open: clr
  Register #(.width(2), .trigger("rising"), .Select("low")) register_21 (
    .D(multiplexer_21_out), .en(pull_resistor_2_node), .Q(FwdRs1_2), .clk(CLK));  // open: clr
  Register #(.width(2), .trigger("rising"), .Select("low")) register_22 (
    .D(multiplexer_22_out), .en(pull_resistor_2_node), .Q(FwdRs2_2), .clk(CLK));  // open: clr

  // Notes on the sheet:
  //   使能端_低电平有效_stall_高电平有效: pull=down
  //   同步清零_气泡_高电平有效: pull=down
endmodule

module \理想EX_MEM  (
  input  [31:0] EX_IR,
  input  [31:0] EX_PC,
  input  jal,
  input  jalr,
  input  SB,
  input  [1:0] select,
  input  [31:0] rs1,
  input  [31:0] rs2,
  input  MemToReg,
  input  MemWrite,
  input  RegWrite,
  input  ecall,
  input  [9:0] ALU,
  input  [31:0] MDin,
  input  [31:0] select_2,
  input  [7:0] SB1,
  input  [4:0] rd,
  input  \同步清零_气泡_高电平有效 ,
  input  CLK,
  input  \使能端_低电平有效_stall_高电平有效 ,
  output [31:0] MEM_IR,
  output [31:0] MEM_PC,
  output Jal_2,
  output jalr_2,
  output SB_2,
  output [1:0] select_3,
  output [31:0] rs1_2,
  output [31:0] rs2_2,
  output MemToReg_2,
  output MemWrite_2,
  output RegWrite_2,
  output ecall_2,
  output [9:0] ALU_2,
  output [31:0] MDin_2,
  output [31:0] select_4,
  output [7:0] SB1_2,
  output [4:0] rd_2
);

  wire multiplexer_3_out, multiplexer_4_out, multiplexer_5_out, multiplexer_9_out, multiplexer_10_out,
       multiplexer_11_out, multiplexer_12_out, pull_resistor_2_node;
  wire [1:0] multiplexer_6_out;
  wire [4:0] multiplexer_17_out;
  wire [7:0] multiplexer_16_out;
  wire [9:0] multiplexer_13_out;
  wire [31:0] multiplexer_1_out, multiplexer_2_out, multiplexer_7_out, multiplexer_8_out, multiplexer_14_out,
       multiplexer_15_out;

  Multiplexer #(.select(1), .width(32), .disabled("Z"), .enable("false")) multiplexer_1 (
    .in0(EX_IR), .in1({32{1'b0}}), .out(multiplexer_1_out), .sel(\同步清零_气泡_高电平有效 ));
  Multiplexer #(.select(1), .width(32), .disabled("Z"), .enable("false")) multiplexer_2 (
    .in0(EX_PC), .in1({32{1'b0}}), .out(multiplexer_2_out), .sel(\同步清零_气泡_高电平有效 ));
  Multiplexer #(.select(1), .width(1), .disabled("Z"), .enable("false")) multiplexer_3 (
    .in0(jal), .in1(1'b0), .out(multiplexer_3_out), .sel(\同步清零_气泡_高电平有效 ));
  Multiplexer #(.select(1), .width(1), .disabled("Z"), .enable("false")) multiplexer_4 (
    .in0(jalr), .in1(1'b0), .out(multiplexer_4_out), .sel(\同步清零_气泡_高电平有效 ));
  Multiplexer #(.select(1), .width(1), .disabled("Z"), .enable("false")) multiplexer_5 (
    .in0(SB), .in1(1'b0), .out(multiplexer_5_out), .sel(\同步清零_气泡_高电平有效 ));
  Multiplexer #(.select(1), .width(2), .disabled("Z"), .enable("false")) multiplexer_6 (
    .in0(select), .in1(2'b00), .out(multiplexer_6_out), .sel(\同步清零_气泡_高电平有效 ));
  Multiplexer #(.select(1), .width(32), .disabled("Z"), .enable("false")) multiplexer_7 (
    .in0(rs1), .in1({32{1'b0}}), .out(multiplexer_7_out), .sel(\同步清零_气泡_高电平有效 ));
  Multiplexer #(.select(1), .width(32), .disabled("Z"), .enable("false")) multiplexer_8 (
    .in0(rs2), .in1({32{1'b0}}), .out(multiplexer_8_out), .sel(\同步清零_气泡_高电平有效 ));
  Multiplexer #(.select(1), .width(1), .disabled("Z"), .enable("false")) multiplexer_9 (
    .in0(MemToReg), .in1(1'b0), .out(multiplexer_9_out), .sel(\同步清零_气泡_高电平有效 ));
  Multiplexer #(.select(1), .width(1), .disabled("Z"), .enable("false")) multiplexer_10 (
    .in0(MemWrite), .in1(1'b0), .out(multiplexer_10_out), .sel(\同步清零_气泡_高电平有效 ));
  Multiplexer #(.select(1), .width(1), .disabled("Z"), .enable("false")) multiplexer_11 (
    .in0(RegWrite), .in1(1'b0), .out(multiplexer_11_out), .sel(\同步清零_气泡_高电平有效 ));
  Multiplexer #(.select(1), .width(1), .disabled("Z"), .enable("false")) multiplexer_12 (
    .in0(ecall), .in1(1'b0), .out(multiplexer_12_out), .sel(\同步清零_气泡_高电平有效 ));
  Multiplexer #(.select(1), .width(10), .disabled("Z"), .enable("false")) multiplexer_13 (
    .in0(ALU), .in1({10{1'b0}}), .out(multiplexer_13_out), .sel(\同步清零_气泡_高电平有效 ));
  Multiplexer #(.select(1), .width(32), .disabled("Z"), .enable("false")) multiplexer_14 (
    .in0(MDin), .in1({32{1'b0}}), .out(multiplexer_14_out), .sel(\同步清零_气泡_高电平有效 ));
  Multiplexer #(.select(1), .width(32), .disabled("Z"), .enable("false")) multiplexer_15 (
    .in0(select_2), .in1({32{1'b0}}), .out(multiplexer_15_out), .sel(\同步清零_气泡_高电平有效 ));
  Multiplexer #(.select(1), .width(8), .disabled("Z"), .enable("false")) multiplexer_16 (
    .in0(SB1), .in1({8{1'b0}}), .out(multiplexer_16_out), .sel(\同步清零_气泡_高电平有效 ));
  Multiplexer #(.select(1), .width(5), .disabled("Z"), .enable("false")) multiplexer_17 (
    .in0(rd), .in1({5{1'b0}}), .out(multiplexer_17_out), .sel(\同步清零_气泡_高电平有效 ));
  Pull_Resistor #(.pull(0)) pull_resistor_1 (.node(\同步清零_气泡_高电平有效 ));
  Pull_Resistor #(.pull(0)) pull_resistor_2 (.node(pull_resistor_2_node));
  not not_1 (pull_resistor_2_node, \使能端_低电平有效_stall_高电平有效 );
  Register #(.width(32), .trigger("rising"), .Select("low")) register_1 (
    .D(multiplexer_1_out), .en(pull_resistor_2_node), .Q(MEM_IR), .clk(CLK));  // open: clr
  Register #(.width(32), .trigger("rising"), .Select("low")) register_2 (
    .D(multiplexer_2_out), .en(pull_resistor_2_node), .Q(MEM_PC), .clk(CLK));  // open: clr
  Register #(.width(1), .trigger("rising"), .Select("low")) register_3 (
    .D(multiplexer_3_out), .en(pull_resistor_2_node), .Q(Jal_2), .clk(CLK));  // open: clr
  Register #(.width(1), .trigger("rising"), .Select("low")) register_4 (
    .D(multiplexer_4_out), .en(pull_resistor_2_node), .Q(jalr_2), .clk(CLK));  // open: clr
  Register #(.width(1), .trigger("rising"), .Select("low")) register_5 (
    .D(multiplexer_5_out), .en(pull_resistor_2_node), .Q(SB_2), .clk(CLK));  // open: clr
  Register #(.width(2), .trigger("rising"), .Select("low")) register_6 (
    .D(multiplexer_6_out), .en(pull_resistor_2_node), .Q(select_3), .clk(CLK));  // open: clr
  Register #(.width(32), .trigger("rising"), .Select("low")) register_7 (
    .D(multiplexer_7_out), .en(pull_resistor_2_node), .Q(rs1_2), .clk(CLK));  // open: clr
  Register #(.width(32), .trigger("rising"), .Select("low")) register_8 (
    .D(multiplexer_8_out), .en(pull_resistor_2_node), .Q(rs2_2), .clk(CLK));  // open: clr
  Register #(.width(1), .trigger("rising"), .Select("low")) register_9 (
    .D(multiplexer_9_out), .en(pull_resistor_2_node), .Q(MemToReg_2), .clk(CLK));  // open: clr
  Register #(.width(1), .trigger("rising"), .Select("low")) register_10 (
    .D(multiplexer_10_out), .en(pull_resistor_2_node), .Q(MemWrite_2), .clk(CLK));  // open: clr
  Register #(.width(1), .trigger("rising"), .Select("low")) register_11 (
    .D(multiplexer_11_out), .en(pull_resistor_2_node), .Q(RegWrite_2), .clk(CLK));  // open: clr
  Register #(.width(1), .trigger("rising"), .Select("low")) register_12 (
    .D(multiplexer_12_out), .en(pull_resistor_2_node), .Q(ecall_2), .clk(CLK));  // open: clr
  Register #(.width(10), .trigger("rising"), .Select("low")) register_13 (
    .D(multiplexer_13_out), .en(pull_resistor_2_node), .Q(ALU_2), .clk(CLK));  // open: clr
  Register #(.width(32), .trigger("rising"), .Select("low")) register_14 (
    .D(multiplexer_14_out), .en(pull_resistor_2_node), .Q(MDin_2), .clk(CLK));  // open: clr
  Register #(.width(32), .trigger("rising"), .Select("low")) register_15 (
    .D(multiplexer_15_out), .en(pull_resistor_2_node), .Q(select_4), .clk(CLK));  // open: clr
  Register #(.width(8), .trigger("rising"), .Select("low")) register_16 (
    .D(multiplexer_16_out), .en(pull_resistor_2_node), .Q(SB1_2), .clk(CLK));  // open: clr
  Register #(.width(5), .trigger("rising"), .Select("low")) register_17 (
    .D(multiplexer_17_out), .en(pull_resistor_2_node), .Q(rd_2), .clk(CLK));  // open: clr

  // Notes on the sheet:
  //   同步清零_气泡_高电平有效: pull=down
  //   使能端_低电平有效_stall_高电平有效: pull=down
endmodule

module \理想MEM_WB  (
  input  [31:0] EX_IR,
  input  [31:0] EX_PC,
  input  jal,
  input  jalr,
  input  SB,
  input  [1:0] select,
  input  [31:0] rs1,
  input  [31:0] rs2,
  input  MemToReg,
  input  RegWrite,
  input  [31:0] ALU,
  input  [31:0] MDout,
  input  [7:0] SB1,
  input  [4:0] rd,
  input  ecall,
  input  \同步清零_气泡_高电平有效 ,
  input  CLK,
  input  \使能端_低电平有效_stall_高电平有效 ,
  output [31:0] MEM_IR,
  output [31:0] MEM_PC,
  output Jal_2,
  output jalr_2,
  output SB_2,
  output [1:0] select_2,
  output [31:0] rs1_2,
  output [31:0] rs2_2,
  output MemToReg_2,
  output RegWrite_2,
  output [31:0] ALU_2,
  output [31:0] MDout_2,
  output [7:0] SB1_2,
  output [4:0] rd_2,
  output ecall_2
);

  wire multiplexer_3_out, multiplexer_4_out, multiplexer_5_out, multiplexer_9_out, multiplexer_10_out,
       multiplexer_15_out, pull_resistor_2_node;
  wire [1:0] multiplexer_6_out;
  wire [4:0] multiplexer_14_out;
  wire [7:0] multiplexer_13_out;
  wire [31:0] multiplexer_1_out, multiplexer_2_out, multiplexer_7_out, multiplexer_8_out, multiplexer_11_out,
       multiplexer_12_out;

  Multiplexer #(.select(1), .width(32), .disabled("Z"), .enable("false")) multiplexer_1 (
    .in0(EX_IR), .in1({32{1'b0}}), .out(multiplexer_1_out), .sel(\同步清零_气泡_高电平有效 ));
  Multiplexer #(.select(1), .width(32), .disabled("Z"), .enable("false")) multiplexer_2 (
    .in0(EX_PC), .in1({32{1'b0}}), .out(multiplexer_2_out), .sel(\同步清零_气泡_高电平有效 ));
  Multiplexer #(.select(1), .width(1), .disabled("Z"), .enable("false")) multiplexer_3 (
    .in0(jal), .in1(1'b0), .out(multiplexer_3_out), .sel(\同步清零_气泡_高电平有效 ));
  Multiplexer #(.select(1), .width(1), .disabled("Z"), .enable("false")) multiplexer_4 (
    .in0(jalr), .in1(1'b0), .out(multiplexer_4_out), .sel(\同步清零_气泡_高电平有效 ));
  Multiplexer #(.select(1), .width(1), .disabled("Z"), .enable("false")) multiplexer_5 (
    .in0(SB), .in1(1'b0), .out(multiplexer_5_out), .sel(\同步清零_气泡_高电平有效 ));
  Multiplexer #(.select(1), .width(2), .disabled("Z"), .enable("false")) multiplexer_6 (
    .in0(select), .in1(2'b00), .out(multiplexer_6_out), .sel(\同步清零_气泡_高电平有效 ));
  Multiplexer #(.select(1), .width(32), .disabled("Z"), .enable("false")) multiplexer_7 (
    .in0(rs1), .in1({32{1'b0}}), .out(multiplexer_7_out), .sel(\同步清零_气泡_高电平有效 ));
  Multiplexer #(.select(1), .width(32), .disabled("Z"), .enable("false")) multiplexer_8 (
    .in0(rs2), .in1({32{1'b0}}), .out(multiplexer_8_out), .sel(\同步清零_气泡_高电平有效 ));
  Multiplexer #(.select(1), .width(1), .disabled("Z"), .enable("false")) multiplexer_9 (
    .in0(MemToReg), .in1(1'b0), .out(multiplexer_9_out), .sel(\同步清零_气泡_高电平有效 ));
  Multiplexer #(.select(1), .width(1), .disabled("Z"), .enable("false")) multiplexer_10 (
    .in0(RegWrite), .in1(1'b0), .out(multiplexer_10_out), .sel(\同步清零_气泡_高电平有效 ));
  Multiplexer #(.select(1), .width(32), .disabled("Z"), .enable("false")) multiplexer_11 (
    .in0(ALU), .in1({32{1'b0}}), .out(multiplexer_11_out), .sel(\同步清零_气泡_高电平有效 ));
  Multiplexer #(.select(1), .width(32), .disabled("Z"), .enable("false")) multiplexer_12 (
    .in0(MDout), .in1({32{1'b0}}), .out(multiplexer_12_out), .sel(\同步清零_气泡_高电平有效 ));
  Multiplexer #(.select(1), .width(8), .disabled("Z"), .enable("false")) multiplexer_13 (
    .in0(SB1), .in1({8{1'b0}}), .out(multiplexer_13_out), .sel(\同步清零_气泡_高电平有效 ));
  Multiplexer #(.select(1), .width(5), .disabled("Z"), .enable("false")) multiplexer_14 (
    .in0(rd), .in1({5{1'b0}}), .out(multiplexer_14_out), .sel(\同步清零_气泡_高电平有效 ));
  Multiplexer #(.select(1), .width(1), .disabled("Z"), .enable("false")) multiplexer_15 (
    .in0(ecall), .in1(1'b0), .out(multiplexer_15_out), .sel(\同步清零_气泡_高电平有效 ));
  Pull_Resistor #(.pull(0)) pull_resistor_1 (.node(\同步清零_气泡_高电平有效 ));
  Pull_Resistor #(.pull(0)) pull_resistor_2 (.node(pull_resistor_2_node));
  not not_1 (pull_resistor_2_node, \使能端_低电平有效_stall_高电平有效 );
  Register #(.width(32), .trigger("rising"), .Select("low")) register_1 (
    .D(multiplexer_1_out), .en(pull_resistor_2_node), .Q(MEM_IR), .clk(CLK));  // open: clr
  Register #(.width(32), .trigger("rising"), .Select("low")) register_2 (
    .D(multiplexer_2_out), .en(pull_resistor_2_node), .Q(MEM_PC), .clk(CLK));  // open: clr
  Register #(.width(1), .trigger("rising"), .Select("low")) register_3 (
    .D(multiplexer_3_out), .en(pull_resistor_2_node), .Q(Jal_2), .clk(CLK));  // open: clr
  Register #(.width(1), .trigger("rising"), .Select("low")) register_4 (
    .D(multiplexer_4_out), .en(pull_resistor_2_node), .Q(jalr_2), .clk(CLK));  // open: clr
  Register #(.width(1), .trigger("rising"), .Select("low")) register_5 (
    .D(multiplexer_5_out), .en(pull_resistor_2_node), .Q(SB_2), .clk(CLK));  // open: clr
  Register #(.width(2), .trigger("rising"), .Select("low")) register_6 (
    .D(multiplexer_6_out), .en(pull_resistor_2_node), .Q(select_2), .clk(CLK));  // open: clr
  Register #(.width(32), .trigger("rising"), .Select("low")) register_7 (
    .D(multiplexer_7_out), .en(pull_resistor_2_node), .Q(rs1_2), .clk(CLK));  // open: clr
  Register #(.width(32), .trigger("rising"), .Select("low")) register_8 (
    .D(multiplexer_8_out), .en(pull_resistor_2_node), .Q(rs2_2), .clk(CLK));  // open: clr
  Register #(.width(1), .trigger("rising"), .Select("low")) register_9 (
    .D(multiplexer_9_out), .en(pull_resistor_2_node), .Q(MemToReg_2), .clk(CLK));  // open: clr
  Register #(.width(1), .trigger("rising"), .Select("low")) register_10 (
    .D(multiplexer_10_out), .en(pull_resistor_2_node), .Q(RegWrite_2), .clk(CLK));  // open: clr
  Register #(.width(32), .trigger("rising"), .Select("low")) register_11 (
    .D(multiplexer_11_out), .en(pull_resistor_2_node), .Q(ALU_2), .clk(CLK));  // open: clr
  Register #(.width(32), .trigger("rising"), .Select("low")) register_12 (
    .D(multiplexer_12_out), .en(pull_resistor_2_node), .Q(MDout_2), .clk(CLK));  // open: clr
  Register #(.width(8), .trigger("rising"), .Select("low")) register_13 (
    .D(multiplexer_13_out), .en(pull_resistor_2_node), .Q(SB1_2), .clk(CLK));  // open: clr
  Register #(.width(5), .trigger("rising"), .Select("low")) register_14 (
    .D(multiplexer_14_out), .en(pull_resistor_2_node), .Q(rd_2), .clk(CLK));  // open: clr
  Register #(.width(1), .trigger("rising"), .Select("low")) register_15 (
    .D(multiplexer_15_out), .en(pull_resistor_2_node), .Q(ecall_2), .clk(CLK));  // open: clr

  // Notes on the sheet:
  //   使能端_低电平有效_stall_高电平有效: pull=down
  //   同步清零_气泡_高电平有效: pull=down
endmodule

module rs_used (
  input  OP2,
  input  OP3,
  input  OP4,
  input  OP5,
  input  OP6,
  input  F12,
  input  F13,
  input  F14,
  input  F25,
  input  F30,
  output rs1_used,
  output rs2_used
);

  wire and_1_out, and_2_out, and_3_out, and_4_out, and_5_out, and_6_out, and_7_out, and_8_out, and_9_out,
       and_10_out, and_11_out, and_12_out, and_13_out, and_14_out, and_15_out, and_16_out, and_17_out,
       and_18_out, and_19_out, and_20_out, and_21_out, and_22_out, and_23_out, and_24_out, and_25_out,
       and_26_out, and_27_out, and_28_out, and_29_out, and_30_out, and_31_out, and_32_out, and_33_out,
       and_34_out, and_35_out, and_36_out, and_37_out, and_38_out, not_1_out, not_2_out, not_3_out,
       not_4_out, not_5_out, not_6_out, not_7_out, not_8_out, not_9_out, not_10_out, not_11_out, not_12_out,
       not_13_out, not_14_out, not_15_out, not_16_out, not_17_out, not_18_out, not_19_out, not_20_out,
       not_21_out, not_22_out, not_23_out, not_24_out, not_25_out, not_26_out, not_27_out, not_28_out,
       not_29_out, not_30_out, not_31_out, not_32_out, not_33_out, not_34_out, not_35_out, not_36_out,
       not_37_out, not_38_out, not_39_out, not_40_out, not_41_out, not_42_out, not_43_out, not_44_out,
       not_45_out, not_46_out, not_47_out, not_48_out, not_49_out, not_50_out, not_51_out, not_52_out,
       not_53_out, not_54_out, not_55_out, not_56_out, not_57_out, not_58_out, not_59_out, not_60_out,
       not_61_out, not_62_out, not_63_out, not_64_out, not_65_out, not_66_out, not_67_out, not_68_out,
       not_69_out, not_70_out, not_71_out, not_72_out, not_73_out, not_74_out, not_75_out, not_76_out,
       not_77_out, not_78_out, not_79_out, not_80_out, not_81_out, not_82_out, not_83_out, not_84_out,
       not_85_out, not_86_out, not_87_out, not_88_out, not_89_out, not_90_out, not_91_out, not_92_out,
       not_93_out, not_94_out, not_95_out, not_96_out, not_97_out, not_98_out, not_99_out, not_100_out,
       not_101_out, not_102_out, not_103_out, not_104_out, not_105_out, not_106_out, not_107_out,
       not_108_out, not_109_out, not_110_out, not_111_out, not_112_out, not_113_out, not_114_out,
       not_115_out, not_116_out, not_117_out, not_118_out, not_119_out, not_120_out, not_121_out,
       not_122_out, not_123_out, not_124_out, not_125_out, not_126_out, not_127_out, not_128_out,
       not_129_out, not_130_out, not_131_out, not_132_out, not_133_out, not_134_out, not_135_out,
       not_136_out, not_137_out, not_138_out, not_139_out, not_140_out, not_141_out, not_142_out,
       not_143_out, not_144_out, not_145_out, not_146_out, not_147_out, not_148_out, not_149_out,
       not_150_out, not_151_out, not_152_out, not_153_out, not_154_out, not_155_out, not_156_out,
       not_157_out, not_158_out, not_159_out, not_160_out, not_161_out, not_162_out, not_163_out,
       not_164_out, not_165_out, not_166_out, not_167_out, not_168_out, not_169_out, not_170_out,
       not_171_out, not_172_out, not_173_out, not_174_out, not_175_out, not_176_out, not_177_out,
       not_178_out, not_179_out, not_180_out, not_181_out, not_182_out, not_183_out, not_184_out,
       not_185_out, not_186_out, not_187_out, not_188_out, not_189_out, not_190_out, not_191_out,
       not_192_out, not_193_out, not_194_out, not_195_out, not_196_out, not_197_out, not_198_out,
       not_199_out, not_200_out, not_201_out, not_202_out, not_203_out, not_204_out, not_205_out,
       not_206_out, not_207_out, not_208_out, not_209_out, not_210_out, not_211_out, not_212_out,
       not_213_out, not_214_out, not_215_out, not_216_out, not_217_out, not_218_out, not_219_out,
       not_220_out, not_221_out, not_222_out, not_223_out, not_224_out, not_225_out, not_226_out,
       not_227_out, not_228_out, not_229_out, not_230_out, not_231_out;

  not not_1 (not_1_out, F30);
  not not_2 (not_2_out, F25);
  not not_3 (not_3_out, F14);
  not not_4 (not_4_out, F13);
  not not_5 (not_5_out, F12);
  not not_6 (not_6_out, OP6);
  not not_7 (not_7_out, OP3);
  not not_8 (not_8_out, OP2);
  not not_9 (not_9_out, F25);
  not not_10 (not_10_out, F14);
  not not_11 (not_11_out, F13);
  not not_12 (not_12_out, F12);
  not not_13 (not_13_out, OP6);
  not not_14 (not_14_out, OP3);
  not not_15 (not_15_out, OP2);
  not not_16 (not_16_out, F30);
  not not_17 (not_17_out, F25);
  not not_18 (not_18_out, OP6);
  not not_19 (not_19_out, OP3);
  not not_20 (not_20_out, OP2);
  not not_21 (not_21_out, F30);
  not not_22 (not_22_out, F25);
  not not_23 (not_23_out, F12);
  not not_24 (not_24_out, OP6);
  not not_25 (not_25_out, OP3);
  not not_26 (not_26_out, OP2);
  not not_27 (not_27_out, F30);
  not not_28 (not_28_out, F25);
  not not_29 (not_29_out, F14);
  not not_30 (not_30_out, F12);
  not not_31 (not_31_out, OP6);
  not not_32 (not_32_out, OP3);
  not not_33 (not_33_out, OP2);
  not not_34 (not_34_out, F30);
  not not_35 (not_35_out, F25);
  not not_36 (not_36_out, F14);
  not not_37 (not_37_out, OP6);
  not not_38 (not_38_out, OP3);
  not not_39 (not_39_out, OP2);
  not not_40 (not_40_out, F14);
  not not_41 (not_41_out, F13);
  not not_42 (not_42_out, F12);
  not not_43 (not_43_out, OP6);
  not not_44 (not_44_out, OP5);
  not not_45 (not_45_out, OP3);
  not not_46 (not_46_out, OP2);
  not not_47 (not_47_out, OP6);
  not not_48 (not_48_out, OP5);
  not not_49 (not_49_out, OP3);
  not not_50 (not_50_out, OP2);
  not not_51 (not_51_out, F12);
  not not_52 (not_52_out, OP6);
  not not_53 (not_53_out, OP5);
  not not_54 (not_54_out, OP3);
  not not_55 (not_55_out, OP2);
  not not_56 (not_56_out, F13);
  not not_57 (not_57_out, F12);
  not not_58 (not_58_out, OP6);
  not not_59 (not_59_out, OP5);
  not not_60 (not_60_out, OP3);
  not not_61 (not_61_out, OP2);
  not not_62 (not_62_out, F14);
  not not_63 (not_63_out, F12);
  not not_64 (not_64_out, OP6);
  not not_65 (not_65_out, OP5);
  not not_66 (not_66_out, OP3);
  not not_67 (not_67_out, OP2);
  not not_68 (not_68_out, F30);
  not not_69 (not_69_out, F25);
  not not_70 (not_70_out, F14);
  not not_71 (not_71_out, F13);
  not not_72 (not_72_out, OP6);
  not not_73 (not_73_out, OP5);
  not not_74 (not_74_out, OP3);
  not not_75 (not_75_out, OP2);
  not not_76 (not_76_out, F30);
  not not_77 (not_77_out, F25);
  not not_78 (not_78_out, F13);
  not not_79 (not_79_out, OP6);
  not not_80 (not_80_out, OP5);
  not not_81 (not_81_out, OP3);
  not not_82 (not_82_out, OP2);
  not not_83 (not_83_out, F25);
  not not_84 (not_84_out, F13);
  not not_85 (not_85_out, OP6);
  not not_86 (not_86_out, OP5);
  not not_87 (not_87_out, OP3);
  not not_88 (not_88_out, OP2);
  not not_89 (not_89_out, F14);
  not not_90 (not_90_out, F12);
  not not_91 (not_91_out, OP6);
  not not_92 (not_92_out, OP5);
  not not_93 (not_93_out, OP4);
  not not_94 (not_94_out, OP3);
  not not_95 (not_95_out, OP2);
  not not_96 (not_96_out, F14);
  not not_97 (not_97_out, F12);
  not not_98 (not_98_out, OP6);
  not not_99 (not_99_out, OP4);
  not not_100 (not_100_out, OP3);
  not not_101 (not_101_out, OP2);
  not not_102 (not_102_out, F30);
  not not_103 (not_103_out, F25);
  not not_104 (not_104_out, F14);
  not not_105 (not_105_out, F13);
  not not_106 (not_106_out, F12);
  not not_107 (not_107_out, OP3);
  not not_108 (not_108_out, OP2);
  not not_109 (not_109_out, F14);
  not not_110 (not_110_out, F13);
  not not_111 (not_111_out, F12);
  not not_112 (not_112_out, OP4);
  not not_113 (not_113_out, OP3);
  not not_114 (not_114_out, OP2);
  not not_115 (not_115_out, F14);
  not not_116 (not_116_out, F13);
  not not_117 (not_117_out, OP4);
  not not_118 (not_118_out, OP3);
  not not_119 (not_119_out, OP2);
  not not_120 (not_120_out, F14);
  not not_121 (not_121_out, F13);
  not not_122 (not_122_out, F12);
  not not_123 (not_123_out, OP4);
  not not_124 (not_124_out, OP3);
  not not_125 (not_125_out, F25);
  not not_126 (not_126_out, F13);
  not not_127 (not_127_out, OP6);
  not not_128 (not_128_out, OP3);
  not not_129 (not_129_out, OP2);
  not not_130 (not_130_out, F30);
  not not_131 (not_131_out, F25);
  not not_132 (not_132_out, F13);
  not not_133 (not_133_out, F12);
  not not_134 (not_134_out, OP6);
  not not_135 (not_135_out, OP3);
  not not_136 (not_136_out, OP2);
  not not_137 (not_137_out, F14);
  not not_138 (not_138_out, F13);
  not not_139 (not_139_out, F12);
  not not_140 (not_140_out, OP6);
  not not_141 (not_141_out, OP4);
  not not_142 (not_142_out, OP3);
  not not_143 (not_143_out, OP2);
  not not_144 (not_144_out, OP4);
  not not_145 (not_145_out, OP3);
  not not_146 (not_146_out, OP2);
  not not_147 (not_147_out, F30);
  not not_148 (not_148_out, F25);
  not not_149 (not_149_out, F14);
  not not_150 (not_150_out, F13);
  not not_151 (not_151_out, F12);
  not not_152 (not_152_out, OP6);
  not not_153 (not_153_out, OP3);
  not not_154 (not_154_out, OP2);
  not not_155 (not_155_out, F25);
  not not_156 (not_156_out, F14);
  not not_157 (not_157_out, F13);
  not not_158 (not_158_out, F12);
  not not_159 (not_159_out, OP6);
  not not_160 (not_160_out, OP3);
  not not_161 (not_161_out, OP2);
  not not_162 (not_162_out, F30);
  not not_163 (not_163_out, F25);
  not not_164 (not_164_out, OP6);
  not not_165 (not_165_out, OP3);
  not not_166 (not_166_out, OP2);
  not not_167 (not_167_out, F30);
  not not_168 (not_168_out, F25);
  not not_169 (not_169_out, F12);
  not not_170 (not_170_out, OP6);
  not not_171 (not_171_out, OP3);
  not not_172 (not_172_out, OP2);
  not not_173 (not_173_out, F30);
  not not_174 (not_174_out, F25);
  not not_175 (not_175_out, F14);
  not not_176 (not_176_out, F12);
  not not_177 (not_177_out, OP6);
  not not_178 (not_178_out, OP3);
  not not_179 (not_179_out, OP2);
  not not_180 (not_180_out, F30);
  not not_181 (not_181_out, F25);
  not not_182 (not_182_out, F14);
  not not_183 (not_183_out, OP6);
  not not_184 (not_184_out, OP3);
  not not_185 (not_185_out, OP2);
  not not_186 (not_186_out, F14);
  not not_187 (not_187_out, F12);
  not not_188 (not_188_out, OP6);
  not not_189 (not_189_out, OP4);
  not not_190 (not_190_out, OP3);
  not not_191 (not_191_out, OP2);
  not not_192 (not_192_out, F30);
  not not_193 (not_193_out, F25);
  not not_194 (not_194_out, F14);
  not not_195 (not_195_out, F13);
  not not_196 (not_196_out, F12);
  not not_197 (not_197_out, OP3);
  not not_198 (not_198_out, OP2);
  not not_199 (not_199_out, F14);
  not not_200 (not_200_out, F13);
  not not_201 (not_201_out, F12);
  not not_202 (not_202_out, OP4);
  not not_203 (not_203_out, OP3);
  not not_204 (not_204_out, OP2);
  not not_205 (not_205_out, F14);
  not not_206 (not_206_out, F13);
  not not_207 (not_207_out, OP4);
  not not_208 (not_208_out, OP3);
  not not_209 (not_209_out, OP2);
  not not_210 (not_210_out, F25);
  not not_211 (not_211_out, F13);
  not not_212 (not_212_out, OP6);
  not not_213 (not_213_out, OP3);
  not not_214 (not_214_out, OP2);
  not not_215 (not_215_out, F30);
  not not_216 (not_216_out, F25);
  not not_217 (not_217_out, F13);
  not not_218 (not_218_out, F12);
  not not_219 (not_219_out, OP6);
  not not_220 (not_220_out, OP3);
  not not_221 (not_221_out, OP2);
  not not_222 (not_222_out, F14);
  not not_223 (not_223_out, F13);
  not not_224 (not_224_out, F12);
  not not_225 (not_225_out, OP6);
  not not_226 (not_226_out, OP4);
  not not_227 (not_227_out, OP3);
  not not_228 (not_228_out, OP2);
  not not_229 (not_229_out, OP4);
  not not_230 (not_230_out, OP3);
  not not_231 (not_231_out, OP2);
  and and_1 (and_1_out, not_1_out, not_2_out, not_3_out, not_4_out, not_5_out, not_6_out, OP5, OP4, not_7_out, not_8_out);
  and and_2 (and_2_out, F30, not_9_out, not_10_out, not_11_out, not_12_out, not_13_out, OP5, OP4, not_14_out, not_15_out);
  and and_3 (and_3_out, not_16_out, not_17_out, F14, F13, F12, not_18_out, OP5, OP4, not_19_out, not_20_out);
  and and_4 (and_4_out, not_21_out, not_22_out, F14, F13, not_23_out, not_24_out, OP5, OP4, not_25_out, not_26_out);
  and and_5 (and_5_out, not_27_out, not_28_out, not_29_out, F13, not_30_out, not_31_out, OP5, OP4, not_32_out, not_33_out);
  and and_6 (and_6_out, not_34_out, not_35_out, not_36_out, F13, F12, not_37_out, OP5, OP4, not_38_out, not_39_out);
  and and_7 (and_7_out, not_40_out, not_41_out, not_42_out, not_43_out, not_44_out, OP4, not_45_out, not_46_out);
  and and_8 (and_8_out, F14, F13, F12, not_47_out, not_48_out, OP4, not_49_out, not_50_out);
  and and_9 (and_9_out, F14, F13, not_51_out, not_52_out, not_53_out, OP4, not_54_out, not_55_out);
  and and_10 (and_10_out, F14, not_56_out, not_57_out, not_58_out, not_59_out, OP4, not_60_out, not_61_out);
  and and_11 (and_11_out, not_62_out, F13, not_63_out, not_64_out, not_65_out, OP4, not_66_out, not_67_out);
  and and_12 (and_12_out, not_68_out, not_69_out, not_70_out, not_71_out, F12, not_72_out, not_73_out, OP4, not_74_out, not_75_out);
  and and_13 (and_13_out, not_76_out, not_77_out, F14, not_78_out, F12, not_79_out, not_80_out, OP4, not_81_out, not_82_out);
  and and_14 (and_14_out, F30, not_83_out, F14, not_84_out, F12, not_85_out, not_86_out, OP4, not_87_out, not_88_out);
  and and_15 (and_15_out, not_89_out, F13, not_90_out, not_91_out, not_92_out, not_93_out, not_94_out, not_95_out);
  and and_16 (and_16_out, not_96_out, F13, not_97_out, not_98_out, OP5, not_99_out, not_100_out, not_101_out);
  and and_17 (and_17_out, not_102_out, not_103_out, not_104_out, not_105_out, not_106_out, OP6, OP5, OP4, not_107_out, not_108_out);
  and and_18 (and_18_out, not_109_out, not_110_out, not_111_out, OP6, OP5, not_112_out, not_113_out, not_114_out);
  and and_19 (and_19_out, not_115_out, not_116_out, F12, OP6, OP5, not_117_out, not_118_out, not_119_out);
  and and_20 (and_20_out, not_120_out, not_121_out, not_122_out, OP6, OP5, not_123_out, not_124_out, OP2);
  and and_21 (and_21_out, F30, not_125_out, F14, not_126_out, F12, not_127_out, OP5, OP4, not_128_out, not_129_out);
  and and_22 (and_22_out, not_130_out, not_131_out, F14, not_132_out, not_133_out, not_134_out, OP5, OP4, not_135_out, not_136_out);
  and and_23 (and_23_out, not_137_out, not_138_out, not_139_out, not_140_out, OP5, not_141_out, not_142_out, not_143_out);
  and and_24 (and_24_out, F14, F13, F12, OP6, OP5, not_144_out, not_145_out, not_146_out);
  and and_25 (and_25_out, not_147_out, not_148_out, not_149_out, not_150_out, not_151_out, not_152_out, OP5, OP4, not_153_out, not_154_out);
  and and_26 (and_26_out, F30, not_155_out, not_156_out, not_157_out, not_158_out, not_159_out, OP5, OP4, not_160_out, not_161_out);
  and and_27 (and_27_out, not_162_out, not_163_out, F14, F13, F12, not_164_out, OP5, OP4, not_165_out, not_166_out);
  and and_28 (and_28_out, not_167_out, not_168_out, F14, F13, not_169_out, not_170_out, OP5, OP4, not_171_out, not_172_out);
  and and_29 (and_29_out, not_173_out, not_174_out, not_175_out, F13, not_176_out, not_177_out, OP5, OP4, not_178_out, not_179_out);
  and and_30 (and_30_out, not_180_out, not_181_out, not_182_out, F13, F12, not_183_out, OP5, OP4, not_184_out, not_185_out);
  and and_31 (and_31_out, not_186_out, F13, not_187_out, not_188_out, OP5, not_189_out, not_190_out, not_191_out);
  and and_32 (and_32_out, not_192_out, not_193_out, not_194_out, not_195_out, not_196_out, OP6, OP5, OP4, not_197_out, not_198_out);
  and and_33 (and_33_out, not_199_out, not_200_out, not_201_out, OP6, OP5, not_202_out, not_203_out, not_204_out);
  and and_34 (and_34_out, not_205_out, not_206_out, F12, OP6, OP5, not_207_out, not_208_out, not_209_out);
  and and_35 (and_35_out, F30, not_210_out, F14, not_211_out, F12, not_212_out, OP5, OP4, not_213_out, not_214_out);
  and and_36 (and_36_out, not_215_out, not_216_out, F14, not_217_out, not_218_out, not_219_out, OP5, OP4, not_220_out, not_221_out);
  and and_37 (and_37_out, not_222_out, not_223_out, not_224_out, not_225_out, OP5, not_226_out, not_227_out, not_228_out);
  and and_38 (and_38_out, F14, F13, F12, OP6, OP5, not_229_out, not_230_out, not_231_out);
  or or_1 (rs2_used, and_25_out, and_26_out, and_27_out, and_28_out, and_29_out, and_30_out, and_31_out, and_32_out, and_33_out, and_34_out, and_35_out, and_36_out, and_37_out, and_38_out);
  or or_2 (rs1_used, and_1_out, and_2_out, and_3_out, and_4_out, and_5_out, and_6_out, and_7_out, and_8_out, and_9_out, and_10_out, and_11_out, and_12_out, and_13_out, and_14_out, and_15_out, and_16_out, and_17_out, and_18_out, and_19_out, and_20_out, and_21_out, and_22_out, and_23_out, and_24_out);
endmodule
